// Logisim project io-demo.circ as structural Verilog: 1 circuit, main circuit main
module main (
  output [3:0] X,
  output [3:0] Y
);

  wire \Botón_out , clock_1_out, keyboard_1_avail;
  wire [6:0] keyboard_1_data;

  Button \Botón  (.out(\Botón_out ));
  Clock clock_1 (.out(clock_1_out));
  Keyboard keyboard_1 (.clk(clock_1_out), .re(1'b1), .clr(1'b0), .avail(keyboard_1_avail), .data(keyboard_1_data));
  LED LED (.in(\Botón_out ));
  Joystick joystick_1 (.x(X), .y(Y));
  TTY #(.rows(6), .cols(24)) tty_1 (.data(keyboard_1_data), .clk(clock_1_out), .we(keyboard_1_avail), .clr(1'b0));
  Hex_Digit_Display hex_digit_display_1 (.value(4'b1010), .dp(1'b0));
  _7_Segment_Display u_7_segment_display_1 (
    .g(1'b1), .f(1'b0), .a(1'b1), .b(1'b1), .e(1'b1), .d(1'b1), .c(1'b0), .dp(1'b0));
  DotMatrix dotmatrix_1 (.col0(7'b0111111), .col1(7'b1001000), .col2(7'b1001000), .col3(7'b1001000), .col4(7'b0111111));

  // Notes on the sheet:
  //   Entrada/salida de Logisim
  //   Activá el reloj o usá Conmutar Reloj para enviar el texto al TTY.
  //   Tocá el teclado con la mano y escribí
  //   Arrastrá el joystick
  //   TTY: recibe un carácter por flanco de reloj
  //   Hex A
  //   7 segmentos
  //   Matriz LED
endmodule
