// Logisim project marquee.circ as structural Verilog: 1 circuit, main circuit main
module main (
);

  wire reloj_out;
  wire [6:0] columna_q;
  wire [7:0] rom_1_data;
  wire [31:0] fila_0_q0, fila_1_q0, fila_2_q0, fila_3_q0, fila_4_q0, fila_5_q0, fila_6_q0, fila_7_q0;

  Clock reloj (.out(reloj_out));
  Counter #(.width(7), .max('h67)) columna (.Q(columna_q), .clk(reloj_out));  // open: load, D, count, carry, clr
  ROM #(.addrWidth(7)) rom_1 (.addr(columna_q), .data(rom_1_data));  // open: sel
  Shift_Register #(.length(32)) fila_0 (
    .in(rom_1_data[0]), .clk(reloj_out), .q0(fila_0_q0[0]), .q1(fila_0_q0[1]), .q2(fila_0_q0[2]),
    .q3(fila_0_q0[3]), .q4(fila_0_q0[4]), .q5(fila_0_q0[5]), .q6(fila_0_q0[6]), .q7(fila_0_q0[7]),
    .q8(fila_0_q0[8]), .q9(fila_0_q0[9]), .q10(fila_0_q0[10]), .q11(fila_0_q0[11]), .q12(fila_0_q0[12]),
    .q13(fila_0_q0[13]), .q14(fila_0_q0[14]), .q15(fila_0_q0[15]), .q16(fila_0_q0[16]), .q17(fila_0_q0[17]),
    .q18(fila_0_q0[18]), .q19(fila_0_q0[19]), .q20(fila_0_q0[20]), .q21(fila_0_q0[21]), .q22(fila_0_q0[22]),
    .q23(fila_0_q0[23]), .q24(fila_0_q0[24]), .q25(fila_0_q0[25]), .q26(fila_0_q0[26]), .q27(fila_0_q0[27]),
    .q28(fila_0_q0[28]), .q29(fila_0_q0[29]), .q30(fila_0_q0[30]), .q31(fila_0_q0[31]));  // open: shift, out, load, clr, d0, d1, d2, d3, d4, d5, d6, d7, d8, d9, d10, d11, d12, d13, d14, d15, d16, d17, d18, d19, d20, d21, d22, d23, d24, d25, d26, d27, d28, d29, d30, d31
  Shift_Register #(.length(32)) fila_1 (
    .in(rom_1_data[1]), .clk(reloj_out), .q0(fila_1_q0[0]), .q1(fila_1_q0[1]), .q2(fila_1_q0[2]),
    .q3(fila_1_q0[3]), .q4(fila_1_q0[4]), .q5(fila_1_q0[5]), .q6(fila_1_q0[6]), .q7(fila_1_q0[7]),
    .q8(fila_1_q0[8]), .q9(fila_1_q0[9]), .q10(fila_1_q0[10]), .q11(fila_1_q0[11]), .q12(fila_1_q0[12]),
    .q13(fila_1_q0[13]), .q14(fila_1_q0[14]), .q15(fila_1_q0[15]), .q16(fila_1_q0[16]), .q17(fila_1_q0[17]),
    .q18(fila_1_q0[18]), .q19(fila_1_q0[19]), .q20(fila_1_q0[20]), .q21(fila_1_q0[21]), .q22(fila_1_q0[22]),
    .q23(fila_1_q0[23]), .q24(fila_1_q0[24]), .q25(fila_1_q0[25]), .q26(fila_1_q0[26]), .q27(fila_1_q0[27]),
    .q28(fila_1_q0[28]), .q29(fila_1_q0[29]), .q30(fila_1_q0[30]), .q31(fila_1_q0[31]));  // open: shift, out, load, clr, d0, d1, d2, d3, d4, d5, d6, d7, d8, d9, d10, d11, d12, d13, d14, d15, d16, d17, d18, d19, d20, d21, d22, d23, d24, d25, d26, d27, d28, d29, d30, d31
  Shift_Register #(.length(32)) fila_2 (
    .in(rom_1_data[2]), .clk(reloj_out), .q0(fila_2_q0[0]), .q1(fila_2_q0[1]), .q2(fila_2_q0[2]),
    .q3(fila_2_q0[3]), .q4(fila_2_q0[4]), .q5(fila_2_q0[5]), .q6(fila_2_q0[6]), .q7(fila_2_q0[7]),
    .q8(fila_2_q0[8]), .q9(fila_2_q0[9]), .q10(fila_2_q0[10]), .q11(fila_2_q0[11]), .q12(fila_2_q0[12]),
    .q13(fila_2_q0[13]), .q14(fila_2_q0[14]), .q15(fila_2_q0[15]), .q16(fila_2_q0[16]), .q17(fila_2_q0[17]),
    .q18(fila_2_q0[18]), .q19(fila_2_q0[19]), .q20(fila_2_q0[20]), .q21(fila_2_q0[21]), .q22(fila_2_q0[22]),
    .q23(fila_2_q0[23]), .q24(fila_2_q0[24]), .q25(fila_2_q0[25]), .q26(fila_2_q0[26]), .q27(fila_2_q0[27]),
    .q28(fila_2_q0[28]), .q29(fila_2_q0[29]), .q30(fila_2_q0[30]), .q31(fila_2_q0[31]));  // open: shift, out, load, clr, d0, d1, d2, d3, d4, d5, d6, d7, d8, d9, d10, d11, d12, d13, d14, d15, d16, d17, d18, d19, d20, d21, d22, d23, d24, d25, d26, d27, d28, d29, d30, d31
  Shift_Register #(.length(32)) fila_3 (
    .in(rom_1_data[3]), .clk(reloj_out), .q0(fila_3_q0[0]), .q1(fila_3_q0[1]), .q2(fila_3_q0[2]),
    .q3(fila_3_q0[3]), .q4(fila_3_q0[4]), .q5(fila_3_q0[5]), .q6(fila_3_q0[6]), .q7(fila_3_q0[7]),
    .q8(fila_3_q0[8]), .q9(fila_3_q0[9]), .q10(fila_3_q0[10]), .q11(fila_3_q0[11]), .q12(fila_3_q0[12]),
    .q13(fila_3_q0[13]), .q14(fila_3_q0[14]), .q15(fila_3_q0[15]), .q16(fila_3_q0[16]), .q17(fila_3_q0[17]),
    .q18(fila_3_q0[18]), .q19(fila_3_q0[19]), .q20(fila_3_q0[20]), .q21(fila_3_q0[21]), .q22(fila_3_q0[22]),
    .q23(fila_3_q0[23]), .q24(fila_3_q0[24]), .q25(fila_3_q0[25]), .q26(fila_3_q0[26]), .q27(fila_3_q0[27]),
    .q28(fila_3_q0[28]), .q29(fila_3_q0[29]), .q30(fila_3_q0[30]), .q31(fila_3_q0[31]));  // open: shift, out, load, clr, d0, d1, d2, d3, d4, d5, d6, d7, d8, d9, d10, d11, d12, d13, d14, d15, d16, d17, d18, d19, d20, d21, d22, d23, d24, d25, d26, d27, d28, d29, d30, d31
  Shift_Register #(.length(32)) fila_4 (
    .in(rom_1_data[4]), .clk(reloj_out), .q0(fila_4_q0[0]), .q1(fila_4_q0[1]), .q2(fila_4_q0[2]),
    .q3(fila_4_q0[3]), .q4(fila_4_q0[4]), .q5(fila_4_q0[5]), .q6(fila_4_q0[6]), .q7(fila_4_q0[7]),
    .q8(fila_4_q0[8]), .q9(fila_4_q0[9]), .q10(fila_4_q0[10]), .q11(fila_4_q0[11]), .q12(fila_4_q0[12]),
    .q13(fila_4_q0[13]), .q14(fila_4_q0[14]), .q15(fila_4_q0[15]), .q16(fila_4_q0[16]), .q17(fila_4_q0[17]),
    .q18(fila_4_q0[18]), .q19(fila_4_q0[19]), .q20(fila_4_q0[20]), .q21(fila_4_q0[21]), .q22(fila_4_q0[22]),
    .q23(fila_4_q0[23]), .q24(fila_4_q0[24]), .q25(fila_4_q0[25]), .q26(fila_4_q0[26]), .q27(fila_4_q0[27]),
    .q28(fila_4_q0[28]), .q29(fila_4_q0[29]), .q30(fila_4_q0[30]), .q31(fila_4_q0[31]));  // open: shift, out, load, clr, d0, d1, d2, d3, d4, d5, d6, d7, d8, d9, d10, d11, d12, d13, d14, d15, d16, d17, d18, d19, d20, d21, d22, d23, d24, d25, d26, d27, d28, d29, d30, d31
  Shift_Register #(.length(32)) fila_5 (
    .in(rom_1_data[5]), .clk(reloj_out), .q0(fila_5_q0[0]), .q1(fila_5_q0[1]), .q2(fila_5_q0[2]),
    .q3(fila_5_q0[3]), .q4(fila_5_q0[4]), .q5(fila_5_q0[5]), .q6(fila_5_q0[6]), .q7(fila_5_q0[7]),
    .q8(fila_5_q0[8]), .q9(fila_5_q0[9]), .q10(fila_5_q0[10]), .q11(fila_5_q0[11]), .q12(fila_5_q0[12]),
    .q13(fila_5_q0[13]), .q14(fila_5_q0[14]), .q15(fila_5_q0[15]), .q16(fila_5_q0[16]), .q17(fila_5_q0[17]),
    .q18(fila_5_q0[18]), .q19(fila_5_q0[19]), .q20(fila_5_q0[20]), .q21(fila_5_q0[21]), .q22(fila_5_q0[22]),
    .q23(fila_5_q0[23]), .q24(fila_5_q0[24]), .q25(fila_5_q0[25]), .q26(fila_5_q0[26]), .q27(fila_5_q0[27]),
    .q28(fila_5_q0[28]), .q29(fila_5_q0[29]), .q30(fila_5_q0[30]), .q31(fila_5_q0[31]));  // open: shift, out, load, clr, d0, d1, d2, d3, d4, d5, d6, d7, d8, d9, d10, d11, d12, d13, d14, d15, d16, d17, d18, d19, d20, d21, d22, d23, d24, d25, d26, d27, d28, d29, d30, d31
  Shift_Register #(.length(32)) fila_6 (
    .in(rom_1_data[6]), .clk(reloj_out), .q0(fila_6_q0[0]), .q1(fila_6_q0[1]), .q2(fila_6_q0[2]),
    .q3(fila_6_q0[3]), .q4(fila_6_q0[4]), .q5(fila_6_q0[5]), .q6(fila_6_q0[6]), .q7(fila_6_q0[7]),
    .q8(fila_6_q0[8]), .q9(fila_6_q0[9]), .q10(fila_6_q0[10]), .q11(fila_6_q0[11]), .q12(fila_6_q0[12]),
    .q13(fila_6_q0[13]), .q14(fila_6_q0[14]), .q15(fila_6_q0[15]), .q16(fila_6_q0[16]), .q17(fila_6_q0[17]),
    .q18(fila_6_q0[18]), .q19(fila_6_q0[19]), .q20(fila_6_q0[20]), .q21(fila_6_q0[21]), .q22(fila_6_q0[22]),
    .q23(fila_6_q0[23]), .q24(fila_6_q0[24]), .q25(fila_6_q0[25]), .q26(fila_6_q0[26]), .q27(fila_6_q0[27]),
    .q28(fila_6_q0[28]), .q29(fila_6_q0[29]), .q30(fila_6_q0[30]), .q31(fila_6_q0[31]));  // open: shift, out, load, clr, d0, d1, d2, d3, d4, d5, d6, d7, d8, d9, d10, d11, d12, d13, d14, d15, d16, d17, d18, d19, d20, d21, d22, d23, d24, d25, d26, d27, d28, d29, d30, d31
  Shift_Register #(.length(32)) fila_7 (
    .in(rom_1_data[7]), .clk(reloj_out), .q0(fila_7_q0[0]), .q1(fila_7_q0[1]), .q2(fila_7_q0[2]),
    .q3(fila_7_q0[3]), .q4(fila_7_q0[4]), .q5(fila_7_q0[5]), .q6(fila_7_q0[6]), .q7(fila_7_q0[7]),
    .q8(fila_7_q0[8]), .q9(fila_7_q0[9]), .q10(fila_7_q0[10]), .q11(fila_7_q0[11]), .q12(fila_7_q0[12]),
    .q13(fila_7_q0[13]), .q14(fila_7_q0[14]), .q15(fila_7_q0[15]), .q16(fila_7_q0[16]), .q17(fila_7_q0[17]),
    .q18(fila_7_q0[18]), .q19(fila_7_q0[19]), .q20(fila_7_q0[20]), .q21(fila_7_q0[21]), .q22(fila_7_q0[22]),
    .q23(fila_7_q0[23]), .q24(fila_7_q0[24]), .q25(fila_7_q0[25]), .q26(fila_7_q0[26]), .q27(fila_7_q0[27]),
    .q28(fila_7_q0[28]), .q29(fila_7_q0[29]), .q30(fila_7_q0[30]), .q31(fila_7_q0[31]));  // open: shift, out, load, clr, d0, d1, d2, d3, d4, d5, d6, d7, d8, d9, d10, d11, d12, d13, d14, d15, d16, d17, d18, d19, d20, d21, d22, d23, d24, d25, d26, d27, d28, d29, d30, d31
  DotMatrix #(.inputtype("row"), .matrixcols(32), .matrixrows(8), .dotshape("circle")) dotmatrix_1 (
    .row0(fila_0_q0), .row1(fila_1_q0), .row2(fila_2_q0), .row3(fila_3_q0), .row4(fila_4_q0),
    .row5(fila_5_q0), .row6(fila_6_q0), .row7(fila_7_q0));

  // Notes on the sheet:
  //   Marquesina LED
  //   Activá los ticks automáticos (Ctrl+K) y subí la frecuencia a 16 o 32 Hz para ver el mensaje correr.
  //   El contador recorre la ROM, que guarda el mensaje columna por columna.
  //   Cada fila es un registro de desplazamiento de 32 bits: en cada flanco entra una columna nueva
  //   por la izquierda, y el divisor la manda a la derecha de la matriz, así el texto avanza hacia la izquierda.
  //   mensaje (1 columna por dirección)
  //   contents of rom_1 (hex, n*v repeats v):
  //   7e 80 80 80 7e 0 fe 8 10 20 fe 0 fc 12 12 12 fc 0 fe 10 10 10 fe 0 7e 80 80 80 7e 0 fe 12 32 52 8c
  //   4*0 1c 3e 7e fc 7e 3e 1c 4*0 fe 4*80 0 7c 82 82 82 7c 0 7c 82 92 92 74 0 82 fe 82 0 fe 10 10 10 fe 0
  //   7e 80 80 80 7e 0 fe 12 32 52 8c 4*0 1c 3e 7e fc 7e 3e 1c
  //   Matriz de puntos 32×8 (entrada por filas)
endmodule
