// Logisim project full-adder.circ as structural Verilog: 2 circuits, main circuit main
module main (
  input  A,
  input  B,
  input  Cin,
  output Sum,
  output Cout
);

  wire half_1_c, half_1_s, half_2_c;

  half half_1 (.A(A), .B(B), .S(half_1_s), .C(half_1_c));
  half half_2 (.A(half_1_s), .B(Cin), .S(Sum), .C(half_2_c));
  or or_1 (Cout, half_2_c, half_1_c);
endmodule

module half (
  input  A,
  input  B,
  output S,
  output C
);

  xor xor_1 (S, A, B);
  and and_1 (C, A, B);
endmodule
