// Logisim project conflict-003.circ as structural Verilog: 1 circuit, main circuit main
module main (
  input  in0,
  input  in1,
  input  in2,
  output out0,
  output out1
);

  nor nor_1 (out1, in1, 1'b0, ~1'b0);  // NOR_Gate
  not not_1 (out0, in1);
endmodule
