// Logisim project conflict-004.circ as structural Verilog: 1 circuit, main circuit main
module main (
  input  in0,
  input  in1,
  input  in2,
  input  in3,
  output out0
);

  wire nand_1_out, nor_1_out, xor_1_out;

  xor xor_1 (xor_1_out, in0, 1'b0);
  nand nand_1 (nand_1_out, in2, in1, in3, in0);
  xnor even_parity_1 (out0, in1, in3, in1, 1'b0, nand_1_out);
  nor nor_1 (nor_1_out, in2, in1);
endmodule
