// Logisim project conflict-006.circ as structural Verilog: 1 circuit, main circuit main
module main (
  input  in0,
  input  in1,
  input  in2,
  output out0,
  output out1
);

  and and_1 (out0, in2, in1);
  nor nor_1 (out1, in2, in0);
endmodule
