// Logisim project conflict-008.circ as structural Verilog: 1 circuit, main circuit main
module main (
  input  in0,
  output out0
);

  wire nor_1_out, or_1_out, undriven, xor_1_out, xor_3_out;

  nor nor_1 (nor_1_out, 1'b1, ~in0, 1'b1, ~in0, 1'b1);  // NOR_Gate
  or or_1 (or_1_out, ~nor_1_out, ~in0, ~nor_1_out, in0, in0);  // OR_Gate
  xor odd_parity_1 (or_1_out, 1'b1, in0);
  xor xor_1 (xor_1_out, undriven, undriven);
  ExactlyOne xor_2 (.out(out0), .in0(or_1_out), .in1(in0), .in2(or_1_out));
  not not_1 (xor_1_out, xor_1_out);
  xor xor_3 (xor_3_out, or_1_out, or_1_out);
endmodule
