// Logisim project conflict-009.circ as structural Verilog: 1 circuit, main circuit main
module main (
  input  in0,
  output out0
);

  wire and_1_out, nand_2_out, undriven, xnor_1_out, xor_1_out, xor_2_out;

  xnor xnor_1 (xnor_1_out, ~in0, 1'b1);  // XNOR_Gate
  xor xor_1 (xor_1_out, in0, xnor_1_out);
  nand nand_1 (xor_1_out, 1'b1, xor_1_out, 1'b1, ~1'b1);  // NAND_Gate
  nand nand_2 (nand_2_out, 1'b1, in0);
  and and_1 (and_1_out, ~nand_2_out, ~nand_2_out, xor_1_out, nand_2_out, xnor_1_out);  // AND_Gate
  ExactlyOne xor_2 (.out(xor_2_out), .in0(1'b1), .in1(in0), .in2(nand_2_out));
  xor odd_parity_1 (and_1_out, xor_1_out, nand_2_out, xor_1_out, ~undriven);  // Odd_Parity
  ExactlyOne xor_3 (.out(out0), .in0(xor_2_out), .in1(and_1_out), .in2(1'b1));
endmodule
