// Logisim project conflict-010.circ as structural Verilog: 1 circuit, main circuit main
module main (
  input  in0,
  input  in1,
  input  in2,
  output out0,
  output out1,
  output out2
);

  wire even_parity_1_out, nand_1_out, nor_1_out, not_2_out, or_1_out, or_2_out, undriven;

  nor nor_1 (nor_1_out, ~in2, in2);  // NOR_Gate
  or or_1 (or_1_out, 1'b1, in2, in1);
  xnor even_parity_1 (even_parity_1_out, or_1_out, in0);
  nand nand_1 (nand_1_out, in1, ~in0, 1'b1);  // NAND_Gate
  not not_1 (nand_1_out, nor_1_out);
  or or_2 (or_2_out, nor_1_out, undriven);
  NotExactlyOne xnor_1 (.out(out0), .in0(in0), .in1(in1), .in2(nor_1_out));
  xnor xnor_2 (or_1_out, 1'b1, nand_1_out);
  not not_2 (not_2_out, nor_1_out);

  assign out1 = out0;
  assign out2 = out0;
endmodule
