// Logisim project conflict-011.circ as structural Verilog: 1 circuit, main circuit main
module main (
  input  in0,
  input  in1,
  input  in2,
  output out0,
  output out1
);

  wire nand_1_out, odd_parity_2_out, undriven, undriven_2, xor_1_out;

  xor xor_1 (xor_1_out, in0, in0);
  xor odd_parity_1 (xor_1_out, 1'b1, ~in2, ~in2);  // Odd_Parity
  nor nor_1 (xor_1_out, ~undriven, in0, xor_1_out);  // NOR_Gate
  xor odd_parity_2 (odd_parity_2_out, undriven, 1'b1, in2, ~xor_1_out, in2);  // Odd_Parity
  nand nand_1 (nand_1_out, xor_1_out, undriven_2);
  xor odd_parity_3 (out0, undriven, xor_1_out);

  assign out1 = out0;
endmodule
