// Logisim project feedback-001.circ as structural Verilog: 1 circuit, main circuit main
module main (
  input  in0,
  input  in1,
  input  in2,
  output out0,
  output out1
);

  wire not_1_out;

  nand nand_1 (out0, in0, in0, 1'b1, in0);
  not not_1 (not_1_out, out0);

  assign out1 = out0;
endmodule
