// Logisim project feedback-002.circ as structural Verilog: 1 circuit, main circuit main
module main (
  input  in0,
  input  in1,
  input  in2,
  output out0
);

  wire even_parity_1_out, or_1_out, xnor_1_out;

  xnor xnor_1 (xnor_1_out, out0, ~in2);  // XNOR_Gate
  or or_1 (or_1_out, in1, ~in1, even_parity_1_out);  // OR_Gate
  xnor even_parity_1 (even_parity_1_out, ~xnor_1_out, ~or_1_out);  // Even_Parity
  buf buffer_1 (out0, out0);
endmodule
