// Logisim project feedback-003.circ as structural Verilog: 1 circuit, main circuit main
module main (
  input  in0,
  input  in1,
  input  in2,
  output out0,
  output out1
);

  wire not_1_out;

  nor nor_1 (out0, 1'b0, in1, ~in1);  // NOR_Gate
  not not_1 (not_1_out, in2);

  assign out1 = out0;
endmodule
