// Logisim project feedback-006.circ as structural Verilog: 1 circuit, main circuit main
module main (
  input  in0,
  input  in1,
  input  in2,
  output out0,
  output out1
);

  wire nor_1_out;

  and and_1 (out0, in1, in0);
  nor nor_1 (nor_1_out, 1'b0, 1'b0);

  assign out1 = out0;
endmodule
