// Logisim project feedback-007.circ as structural Verilog: 1 circuit, main circuit main
module main (
  input  in0,
  output out0,
  output out1,
  output out2
);

  nor nor_1 (out1, 1'b1, out1, 1'b1);
  buf buffer_1 (out0, 1'b1);

  assign out2 = out0;
endmodule
