// Logisim project feedback-009.circ as structural Verilog: 1 circuit, main circuit main
module main (
  input  in0,
  output out0
);

  wire and_1_out, nand_1_out, nand_2_out, odd_parity_1_out, xnor_1_out, xor_1_out, xor_3_out;

  xnor xnor_1 (xnor_1_out, ~out0, out0);  // XNOR_Gate
  xor xor_1 (xor_1_out, 1'b1, 1'b1);
  nand nand_1 (nand_1_out, in0, 1'b1, xor_3_out, ~1'b1);  // NAND_Gate
  nand nand_2 (nand_2_out, nand_1_out, nand_1_out);
  and and_1 (and_1_out, ~in0, ~nand_1_out, nand_1_out, xor_1_out, odd_parity_1_out);  // AND_Gate
  ExactlyOne xor_2 (.out(out0), .in0(nand_1_out), .in1(and_1_out), .in2(xor_1_out));
  xor odd_parity_1 (odd_parity_1_out, and_1_out, nand_1_out, and_1_out, ~nand_2_out);  // Odd_Parity
  ExactlyOne xor_3 (.out(xor_3_out), .in0(xor_1_out), .in1(xor_1_out), .in2(nand_1_out));
endmodule
