// Logisim project feedback-010.circ as structural Verilog: 1 circuit, main circuit main
module main (
  input  in0,
  input  in1,
  input  in2,
  output out0,
  output out1,
  output out2
);

  wire even_parity_1_out, nand_1_out, nor_1_out, not_1_out, not_2_out, or_1_out, or_2_out;

  nor nor_1 (nor_1_out, ~in2, in2);  // NOR_Gate
  or or_1 (or_1_out, in1, in0, in1);
  xnor even_parity_1 (even_parity_1_out, out1, in2);
  nand nand_1 (nand_1_out, out1, ~1'b1, in0);  // NAND_Gate
  not not_1 (not_1_out, even_parity_1_out);
  or or_2 (or_2_out, 1'b1, in0);
  NotExactlyOne xnor_1 (.out(out0), .in0(nor_1_out), .in1(or_2_out), .in2(or_2_out));
  xnor xnor_2 (out1, in2, 1'b1);
  not not_2 (not_2_out, or_2_out);

  assign out2 = out1;
endmodule
