// Logisim project feedback-011.circ as structural Verilog: 1 circuit, main circuit main
module main (
  input  in0,
  input  in1,
  input  in2,
  output out0,
  output out1
);

  wire nor_1_out, odd_parity_1_out, odd_parity_2_out, odd_parity_3_out, xor_1_out;

  xor xor_1 (xor_1_out, xor_1_out, in1);
  xor odd_parity_1 (odd_parity_1_out, in1, ~xor_1_out, ~odd_parity_2_out);  // Odd_Parity
  nor nor_1 (nor_1_out, ~nor_1_out, 1'b1, in2);  // NOR_Gate
  xor odd_parity_2 (odd_parity_2_out, in0, in2, in2, ~in2, in1);  // Odd_Parity
  nand nand_1 (out0, odd_parity_2_out, in1);
  xor odd_parity_3 (odd_parity_3_out, xor_1_out, out0);

  assign out1 = out0;
endmodule
