// Logisim project open-001.circ as structural Verilog: 1 circuit, main circuit main
module main (
  input  in0,
  input  in1,
  input  in2,
  output out0,
  output out1
);

  wire nand_1_out;

  nand nand_1 (nand_1_out, in0, 1'b1);
  not not_1 (out0, in0);

  assign out1 = out0;
endmodule
