// Logisim project open-002.circ as structural Verilog: 1 circuit, main circuit main
module main (
  input  in0,
  input  in1,
  input  in2,
  output out0
);

  wire buffer_1_out, even_parity_1_out, xnor_1_out;

  not xnor_1 (xnor_1_out, ~in1);  // XNOR_Gate XNOR_Gate
  or or_1 (out0, 1'b1, in1);  // OR_Gate
  not even_parity_1 (even_parity_1_out, ~in0);  // Even_Parity Even_Parity
  // Buffer buffer_1 has open pins: in=open, out=buffer_1_out
endmodule
