// Logisim project open-004.circ as structural Verilog: 1 circuit, main circuit main
module main (
  input  in0,
  input  in1,
  input  in2,
  input  in3,
  output out0
);

  wire nand_1_out, nor_1_out, xor_1_out;

  buf xor_1 (xor_1_out, in2);  // XOR_Gate
  nand nand_1 (nand_1_out, in3, in1, in0);
  xnor even_parity_1 (out0, nand_1_out, in2, in3);
  not nor_1 (nor_1_out, 1'b0);  // NOR_Gate
endmodule
