// Logisim project open-008.circ as structural Verilog: 1 circuit, main circuit main
module main (
  input  in0,
  output out0
);

  wire nor_1_out, odd_parity_1_out, or_1_out, xor_1_out, xor_2_out, xor_3_out;

  nor nor_1 (nor_1_out, in0, ~in0, 1'b1, in0);  // NOR_Gate
  or or_1 (or_1_out, ~1'b1, nor_1_out);  // OR_Gate
  xor odd_parity_1 (odd_parity_1_out, nor_1_out, in0);
  xor xor_1 (xor_1_out, nor_1_out, in0);
  ExactlyOne xor_2 (.out(xor_2_out), .in0(or_1_out), .in1(1'b1), .in2(1'b1));
  not not_1 (out0, xor_1_out);
  buf xor_3 (xor_3_out, or_1_out);  // XOR_Gate
endmodule
