// Logisim project open-009.circ as structural Verilog: 1 circuit, main circuit main
module main (
  input  in0,
  output out0
);

  wire and_1_out, nand_1_out, nand_2_out, xnor_1_out, xor_1_out, xor_2_out, xor_3_out;

  not xnor_1 (xnor_1_out, in0);  // XNOR_Gate XNOR_Gate
  xor xor_1 (xor_1_out, xnor_1_out, 1'b1);
  nand nand_1 (nand_1_out, 1'b1, 1'b1);  // NAND_Gate
  nand nand_2 (nand_2_out, nand_1_out, xnor_1_out);
  and and_1 (and_1_out, ~xnor_1_out, ~1'b1, nand_1_out, nand_1_out);  // AND_Gate
  xor xor_2 (xor_2_out, ~nand_1_out, nand_2_out);  // XOR_Gate
  xor odd_parity_1 (out0, 1'b1, in0, ~and_1_out);  // Odd_Parity
  xor xor_3 (xor_3_out, 1'b1, in0);
endmodule
