// Logisim project open-010.circ as structural Verilog: 1 circuit, main circuit main
module main (
  input  in0,
  input  in1,
  input  in2,
  output out0,
  output out1,
  output out2
);

  wire even_parity_1_out, nand_1_out, nor_1_out, not_1_out, or_1_out, or_2_out, xnor_2_out;

  nor nor_1 (nor_1_out, ~in2, in2);  // NOR_Gate
  or or_1 (or_1_out, in1, in0, in1);
  not even_parity_1 (even_parity_1_out, in2);  // Even_Parity
  nand nand_1 (nand_1_out, in1, ~in2, 1'b1);  // NAND_Gate
  // NOT_Gate not_1 has open pins: in=open, out=not_1_out
  buf or_2 (or_2_out, 1'b1);  // OR_Gate
  not xnor_1 (out2, even_parity_1_out);  // XNOR_Gate
  xnor xnor_2 (xnor_2_out, or_2_out, out2);
  not not_2 (out0, nor_1_out);

  assign out1 = out0;
endmodule
