// Logisim project open-011.circ as structural Verilog: 1 circuit, main circuit main
module main (
  input  in0,
  input  in1,
  input  in2,
  output out0,
  output out1
);

  wire nor_1_out, odd_parity_1_out, odd_parity_2_out, xor_1_out;

  // XOR_Gate xor_1 has open pins: out=xor_1_out
  xor odd_parity_1 (odd_parity_1_out, in2, ~in1, ~xor_1_out);  // Odd_Parity
  nor nor_1 (nor_1_out, in0, xor_1_out);  // NOR_Gate
  xor odd_parity_2 (odd_parity_2_out, in2, in2, ~in2, in2);  // Odd_Parity
  nand nand_1 (out1, in2, in1);
  buf odd_parity_3 (out0, nor_1_out);  // Odd_Parity
endmodule
