// Logisim project plain-001.circ as structural Verilog: 1 circuit, main circuit main
module main (
  input  in0,
  input  in1,
  input  in2,
  output out0,
  output out1
);

  nand nand_1 (out0, in0, in0, in1, in0);
  not not_1 (out1, in1);
endmodule
