// Logisim project plain-002.circ as structural Verilog: 1 circuit, main circuit main
module main (
  input  in0,
  input  in1,
  input  in2,
  output out0
);

  wire even_parity_1_out, or_1_out, xnor_1_out;

  xnor xnor_1 (xnor_1_out, in0, ~1'b1);  // XNOR_Gate
  or or_1 (or_1_out, in2, ~xnor_1_out, 1'b1);  // OR_Gate
  xnor even_parity_1 (even_parity_1_out, ~in1, ~in2);  // Even_Parity
  buf buffer_1 (out0, in2);
endmodule
