// Logisim project plain-005.circ as structural Verilog: 1 circuit, main circuit main
module main (
  input  in0,
  input  in1,
  input  in2,
  output out0
);

  wire even_parity_1_out, nor_1_out, nor_2_out, not_1_out, not_2_out, odd_parity_1_out, or_1_out;

  not not_1 (not_1_out, in1);
  nor nor_1 (nor_1_out, 1'b1, in0, in1, ~not_1_out, in1);  // NOR_Gate
  xnor even_parity_1 (even_parity_1_out, not_1_out, in0, ~in0);  // Even_Parity
  or or_1 (or_1_out, even_parity_1_out, not_1_out, in1);
  not not_2 (not_2_out, 1'b1);
  nor nor_2 (nor_2_out, in0, or_1_out, 1'b1, in2, nor_1_out);
  xor odd_parity_1 (odd_parity_1_out, nor_2_out, nor_2_out, even_parity_1_out, 1'b1);
  and and_1 (out0, not_2_out, even_parity_1_out, in1, ~not_1_out, even_parity_1_out);  // AND_Gate
endmodule
