// Logisim project plain-010.circ as structural Verilog: 1 circuit, main circuit main
module main (
  input  in0,
  input  in1,
  input  in2,
  output out0,
  output out1,
  output out2
);

  wire even_parity_1_out, nand_1_out, nor_1_out, not_1_out, or_1_out, or_2_out, xnor_1_out, xnor_2_out;

  nor nor_1 (nor_1_out, ~in2, in2);  // NOR_Gate
  or or_1 (or_1_out, 1'b1, in2, in1);
  xnor even_parity_1 (even_parity_1_out, in1, or_1_out);
  nand nand_1 (nand_1_out, in0, ~in2, in1);  // NAND_Gate
  not not_1 (not_1_out, in0);
  or or_2 (or_2_out, not_1_out, nor_1_out);
  NotExactlyOne xnor_1 (.out(xnor_1_out), .in0(or_1_out), .in1(in1), .in2(or_2_out));
  xnor xnor_2 (xnor_2_out, or_1_out, xnor_1_out);
  not not_2 (out0, 1'b1);

  assign out1 = out0;
  assign out2 = out0;
endmodule
