// Logisim project plain-011.circ as structural Verilog: 1 circuit, main circuit main
module main (
  input  in0,
  input  in1,
  input  in2,
  output out0,
  output out1
);

  wire nand_1_out, nor_1_out, odd_parity_1_out, xor_1_out;

  xor xor_1 (xor_1_out, in0, in0);
  xor odd_parity_1 (odd_parity_1_out, 1'b1, ~in2, ~in2);  // Odd_Parity
  nor nor_1 (nor_1_out, ~in1, xor_1_out, odd_parity_1_out);  // NOR_Gate
  xor odd_parity_2 (out1, in0, odd_parity_1_out, in0, ~xor_1_out, odd_parity_1_out);  // Odd_Parity
  nand nand_1 (nand_1_out, 1'b1, xor_1_out);
  xor odd_parity_3 (out0, odd_parity_1_out, xor_1_out);
endmodule
