// Logisim project plain-012.circ as structural Verilog: 1 circuit, main circuit main
module main (
  input  in0,
  input  in1,
  output out0,
  output out1
);

  buf buffer_1 (out0, in1);
  not not_1 (out1, out0);
endmodule
