// Logisim project plain-013.circ as structural Verilog: 1 circuit, main circuit main
module main (
  input  in0,
  input  in1,
  input  in2,
  output out0
);

  wire not_1_out, not_2_out, odd_parity_1_out;

  not not_1 (not_1_out, in1);
  not not_2 (not_2_out, in0);
  xor odd_parity_1 (odd_parity_1_out, not_2_out, ~in2, in0, in1);  // Odd_Parity
  xor xor_1 (out0, in0, in0);
endmodule
