// Logisim project plain-014.circ as structural Verilog: 1 circuit, main circuit main
module main (
  input  in0,
  input  in1,
  output out0,
  output out1
);

  wire buffer_1_out, not_2_out, xnor_1_out;

  buf buffer_1 (buffer_1_out, in1);
  xnor xnor_1 (xnor_1_out, 1'b0, in1);
  not not_1 (out1, in1);
  not not_2 (not_2_out, in0);
  nor nor_1 (out0, out1, in1, in1, out1, buffer_1_out);
endmodule
