// Logisim project plain-015.circ as structural Verilog: 1 circuit, main circuit main
module main (
  input  in0,
  output out0,
  output out1
);

  wire and_1_out, buffer_1_out, xnor_1_out;

  NotExactlyOne xnor_1 (.out(xnor_1_out), .in0(1'b0), .in1(in0), .in2(in0));
  and and_1 (and_1_out, in0, ~1'b0, 1'b0, xnor_1_out);  // AND_Gate
  nand nand_1 (out0, ~and_1_out, 1'b0);  // NAND_Gate
  buf buffer_1 (buffer_1_out, in0);
  and and_2 (out1, buffer_1_out, xnor_1_out, ~in0, buffer_1_out);  // AND_Gate
endmodule
