// Logisim project plain-016.circ as structural Verilog: 1 circuit, main circuit main
module main (
  input  in0,
  input  in1,
  input  in2,
  output out0,
  output out1,
  output out2
);

  wire nand_1_out, xor_1_out;

  and and_1 (out0, ~in0, in0, 1'b0, ~in0, 1'b0);  // AND_Gate
  ExactlyOne xor_1 (.out(xor_1_out), .in0(out0), .in1(out0), .in2(in2));
  nand nand_1 (nand_1_out, out0, out0, xor_1_out, in2);

  assign out1 = out0;
  assign out2 = out0;
endmodule
