// Logisim project plain-017.circ as structural Verilog: 1 circuit, main circuit main
module main (
  input  in0,
  input  in1,
  input  in2,
  output out0,
  output out1
);

  wire not_1_out;

  not not_1 (not_1_out, in2);
  xor xor_1 (out1, not_1_out, in2);
  or or_1 (out0, in2, in0, in0, 1'b0);
endmodule
