// Logisim project plain-018.circ as structural Verilog: 1 circuit, main circuit main
module main (
  input  in0,
  input  in1,
  output out0,
  output out1
);

  wire even_parity_1_out, nor_1_out, or_1_out, xor_1_out;

  ExactlyOne xor_1 (.out(xor_1_out), .in0(1'b0), .in1(in1), .in2(1'b0));
  or or_1 (or_1_out, ~xor_1_out, in0, in1);  // OR_Gate
  nor nor_1 (nor_1_out, or_1_out, xor_1_out);
  buf buffer_1 (out0, xor_1_out);
  or or_2 (out1, xor_1_out, 1'b0);
  xnor even_parity_1 (even_parity_1_out, 1'b0, in0);
endmodule
