// Logisim project plain-019.circ as structural Verilog: 1 circuit, main circuit main
module main (
  input  in0,
  output out0,
  output out1
);

  wire buffer_1_out, nand_1_out, or_1_out;

  nand nand_1 (nand_1_out, 1'b1, in0, ~1'b1, 1'b1);  // NAND_Gate
  nor nor_1 (out0, ~nand_1_out, in0, in0, 1'b1);  // NOR_Gate
  or or_1 (or_1_out, 1'b1, in0);
  buf buffer_1 (buffer_1_out, nand_1_out);

  assign out1 = out0;
endmodule
