// Logisim project plain-020.circ as structural Verilog: 1 circuit, main circuit main
module main (
  input  in0,
  input  in1,
  input  in2,
  input  in3,
  output out0,
  output out1
);

  wire not_1_out, not_2_out, or_1_out, xor_1_out;

  or or_1 (or_1_out, in1, in2, in0, ~in0);  // OR_Gate
  xor xor_1 (xor_1_out, in0, or_1_out);
  not not_1 (not_1_out, in3);
  not not_2 (not_2_out, not_1_out);
  xnor even_parity_1 (out0, not_2_out, not_2_out, ~or_1_out, xor_1_out, not_2_out);  // Even_Parity

  assign out1 = out0;
endmodule
