// Logisim project plain-021.circ as structural Verilog: 1 circuit, main circuit main
module main (
  input  in0,
  input  in1,
  output out0
);

  wire and_1_out, even_parity_1_out, nor_1_out, xor_1_out;

  xnor even_parity_1 (even_parity_1_out, 1'b0, 1'b0, ~1'b0, in1, in0);  // Even_Parity
  and and_1 (and_1_out, in1, in0, ~in0, even_parity_1_out, in1);  // AND_Gate
  nor nor_1 (nor_1_out, and_1_out, in1);
  xor xor_1 (xor_1_out, in1, and_1_out);
  nor nor_2 (out0, xor_1_out, in0, in0);
endmodule
