// Logisim project plain-022.circ as structural Verilog: 1 circuit, main circuit main
module main (
  input  in0,
  input  in1,
  input  in2,
  output out0
);

  wire even_parity_1_out, not_1_out;

  xnor even_parity_1 (even_parity_1_out, in0, ~in2, ~in1);  // Even_Parity
  not not_1 (not_1_out, in0);
  or or_1 (out0, in0, even_parity_1_out, in2, in1);
endmodule
