// Logisim project plain-023.circ as structural Verilog: 1 circuit, main circuit main
module main (
  input  in0,
  output out0,
  output out1
);

  wire not_1_out;

  or or_1 (out0, 1'b0, ~in0, 1'b0, in0);  // OR_Gate
  not not_1 (not_1_out, out0);

  assign out1 = out0;
endmodule
