// Logisim project plain-024.circ as structural Verilog: 1 circuit, main circuit main
module main (
  input  in0,
  input  in1,
  output out0
);

  wire and_1_out, and_2_out, even_parity_1_out, nand_1_out, nand_2_out, nor_1_out, not_1_out, xnor_1_out;

  and and_1 (and_1_out, in0, 1'b0, 1'b0);
  and and_2 (and_2_out, in1, 1'b0, in0);
  nand nand_1 (nand_1_out, 1'b0, in1, 1'b0, ~and_1_out, ~in1);  // NAND_Gate
  xnor even_parity_1 (even_parity_1_out, in0, and_2_out, in1, 1'b0, and_1_out);
  not not_1 (not_1_out, and_1_out);
  nor nor_1 (nor_1_out, and_2_out, in0, even_parity_1_out);
  nand nand_2 (nand_2_out, in0, nor_1_out, in1, nor_1_out);
  xnor xnor_1 (xnor_1_out, and_2_out, in0);
  nor nor_2 (out0, and_2_out, nor_1_out);
endmodule
