// Logisim project plain-025.circ as structural Verilog: 1 circuit, main circuit main
module main (
  input  in0,
  input  in1,
  input  in2,
  output out0,
  output out1
);

  wire and_1_out, buffer_1_out, even_parity_1_out, nand_1_out, not_1_out, xnor_1_out;

  and and_1 (and_1_out, in2, in1, 1'b1);
  not not_1 (not_1_out, in1);
  buf buffer_1 (buffer_1_out, in0);
  nand nand_1 (nand_1_out, not_1_out, in0);
  xnor even_parity_1 (even_parity_1_out, ~in0, ~in1, not_1_out, buffer_1_out, ~nand_1_out);  // Even_Parity
  xnor xnor_1 (xnor_1_out, in0, in2);
  or or_1 (out0, ~in2, nand_1_out, in1);  // OR_Gate
  xnor even_parity_2 (out1, not_1_out, in0, in2);
endmodule
