// Logisim project plain-026.circ as structural Verilog: 1 circuit, main circuit main
module main (
  input  in0,
  input  in1,
  input  in2,
  output out0,
  output out1
);

  wire not_1_out, not_2_out, odd_parity_1_out, xnor_1_out, xor_1_out;

  ExactlyOne xor_1 (.out(xor_1_out), .in0(1'b0), .in1(in0), .in2(in1));
  not not_1 (not_1_out, 1'b0);
  xor odd_parity_1 (odd_parity_1_out, not_1_out, not_1_out);
  not not_2 (not_2_out, not_1_out);
  NotExactlyOne xnor_1 (.out(xnor_1_out), .in0(in1), .in1(in1), .in2(not_2_out));
  xor odd_parity_2 (out0, ~1'b0, ~not_1_out);  // Odd_Parity
  or or_1 (out1, in1, xnor_1_out, in0, not_2_out);
endmodule
