// Logisim project plain-027.circ as structural Verilog: 1 circuit, main circuit main
module main (
  input  in0,
  input  in1,
  output out0
);

  wire nor_1_out;

  or or_1 (out0, 1'b0, 1'b0, in1);
  nor nor_1 (nor_1_out, ~in1, 1'b0, in1);  // NOR_Gate
endmodule
