// Logisim project plain-028.circ as structural Verilog: 1 circuit, main circuit main
module main (
  input  in0,
  input  in1,
  output out0,
  output out1,
  output out2
);

  wire even_parity_1_out, nand_1_out, not_1_out, or_1_out, xor_1_out;

  nand nand_1 (nand_1_out, 1'b1, in0, in1);
  xnor even_parity_1 (even_parity_1_out, in1, nand_1_out);
  not not_1 (not_1_out, 1'b1);
  or or_1 (or_1_out, in1, even_parity_1_out, not_1_out);
  nand nand_2 (out0, ~even_parity_1_out, 1'b1, in0, not_1_out, ~in1);  // NAND_Gate
  xor odd_parity_1 (out1, ~1'b1, even_parity_1_out, in0, not_1_out, out0);  // Odd_Parity
  xor xor_1 (xor_1_out, ~nand_1_out, not_1_out);  // XOR_Gate

  assign out2 = out0;
endmodule
