// Logisim project plain-029.circ as structural Verilog: 1 circuit, main circuit main
module main (
  input  in0,
  output out0
);

  wire even_parity_1_out, nand_1_out;

  nand nand_1 (nand_1_out, 1'b0, ~in0, 1'b0);  // NAND_Gate
  not not_1 (out0, in0);
  xnor even_parity_1 (even_parity_1_out, ~nand_1_out, in0, in0);  // Even_Parity
endmodule
