// Logisim project plain-030.circ as structural Verilog: 1 circuit, main circuit main
module main (
  input  in0,
  input  in1,
  input  in2,
  input  in3,
  output out0,
  output out1
);

  wire buffer_1_out, nand_1_out, odd_parity_1_out, or_1_out, xnor_1_out, xor_1_out;

  buf buffer_1 (buffer_1_out, in3);
  xor odd_parity_1 (odd_parity_1_out, 1'b0, 1'b0, in3);
  NotExactlyOne xnor_1 (.out(xnor_1_out), .in0(in2), .in1(in2), .in2(in0));
  nand nand_1 (nand_1_out, xnor_1_out, in1, odd_parity_1_out, in2, in0);
  or or_1 (or_1_out, in3, buffer_1_out, buffer_1_out, 1'b0, in2);
  xor xor_1 (xor_1_out, ~1'b0, ~odd_parity_1_out);  // XOR_Gate
  xor xor_2 (out0, ~1'b0, xor_1_out);  // XOR_Gate
  not not_1 (out1, in1);
endmodule
