// Logisim project plain-031.circ as structural Verilog: 1 circuit, main circuit main
module main (
  input  in0,
  input  in1,
  input  in2,
  output out0,
  output out1,
  output out2
);

  wire nand_1_out, nand_2_out, nor_1_out, odd_parity_1_out, xnor_1_out, xnor_2_out;

  nand nand_1 (nand_1_out, in2, 1'b0);
  NotExactlyOne xnor_1 (.out(xnor_1_out), .in0(1'b0), .in1(in1), .in2(nand_1_out));
  xor odd_parity_1 (odd_parity_1_out, in2, 1'b0, xnor_1_out);
  NotExactlyOne xnor_2 (.out(xnor_2_out), .in0(1'b0), .in1(nand_1_out), .in2(in2));
  nand nand_2 (nand_2_out, xnor_2_out, in1, xnor_2_out, nand_1_out);
  nor nor_1 (nor_1_out, nand_2_out, ~in0, 1'b0);  // NOR_Gate
  not not_1 (out0, in1);
  xnor even_parity_1 (out2, out0, odd_parity_1_out, ~1'b0, odd_parity_1_out);  // Even_Parity

  assign out1 = out0;
endmodule
