// Logisim project plain-032.circ as structural Verilog: 1 circuit, main circuit main
module main (
  input  in0,
  input  in1,
  output out0
);

  wire and_1_out, even_parity_1_out, nand_1_out, nor_1_out, not_1_out, or_1_out, xnor_2_out;

  nor nor_1 (nor_1_out, in0, in0);
  and and_1 (and_1_out, in1, in0);
  nand nand_1 (nand_1_out, 1'b1, and_1_out, ~in0, nor_1_out);  // NAND_Gate
  or or_1 (or_1_out, nand_1_out, and_1_out, in1);
  not not_1 (not_1_out, in0);
  xnor even_parity_1 (even_parity_1_out, nand_1_out, ~in1, ~or_1_out, or_1_out);  // Even_Parity
  NotExactlyOne xnor_1 (.out(out0), .in0(nand_1_out), .in1(nand_1_out), .in2(1'b1));
  NotExactlyOne xnor_2 (.out(xnor_2_out), .in0(in1), .in1(nor_1_out), .in2(1'b1));
endmodule
