// Logisim project plain-033.circ as structural Verilog: 1 circuit, main circuit main
module main (
  input  in0,
  input  in1,
  input  in2,
  output out0,
  output out1
);

  wire not_1_out, odd_parity_1_out, or_1_out, or_2_out, xnor_1_out;

  xor odd_parity_1 (odd_parity_1_out, in0, in2, in1);
  or or_1 (or_1_out, in1, in2, ~odd_parity_1_out, ~odd_parity_1_out, 1'b0);  // OR_Gate
  or or_2 (or_2_out, or_1_out, or_1_out, or_1_out, 1'b0);
  NotExactlyOne xnor_1 (.out(xnor_1_out), .in0(in0), .in1(odd_parity_1_out), .in2(or_2_out));
  xor xor_1 (out0, 1'b0, 1'b0);
  or or_3 (out1, in0, in0, in0, out0, out0);
  not not_1 (not_1_out, xnor_1_out);
endmodule
