// Logisim project plain-034.circ as structural Verilog: 1 circuit, main circuit main
module main (
  input  in0,
  input  in1,
  input  in2,
  output out0
);

  wire even_parity_1_out, even_parity_2_out, nor_1_out, not_1_out, not_2_out, not_3_out, odd_parity_1_out;

  not not_1 (not_1_out, 1'b0);
  xor odd_parity_1 (odd_parity_1_out, in1, in1);
  not not_2 (not_2_out, in2);
  not not_3 (not_3_out, in2);
  nor nor_1 (nor_1_out, in0, ~not_2_out);  // NOR_Gate
  and and_1 (out0, in1, nor_1_out, not_1_out);
  xnor even_parity_1 (even_parity_1_out, in0, in2, not_1_out, not_1_out, in1);
  xnor even_parity_2 (even_parity_2_out, even_parity_1_out, 1'b0, 1'b0, out0, not_3_out);
endmodule
