// Logisim project plain-035.circ as structural Verilog: 1 circuit, main circuit main
module main (
  input  in0,
  output out0,
  output out1,
  output out2
);

  wire nand_1_out, odd_parity_1_out, xor_1_out;

  nand nand_1 (nand_1_out, in0, 1'b1, in0);
  xor xor_1 (xor_1_out, nand_1_out, nand_1_out);
  xor odd_parity_1 (odd_parity_1_out, in0, 1'b1, in0, in0);
  buf buffer_1 (out1, 1'b1);
  or or_1 (out0, ~nand_1_out, ~nand_1_out, nand_1_out, ~odd_parity_1_out, ~out1);  // OR_Gate
  ExactlyOne xor_2 (.out(out2), .in0(nand_1_out), .in1(nand_1_out), .in2(in0));
endmodule
