// Logisim project plain-036.circ as structural Verilog: 1 circuit, main circuit main
module main (
  input  in0,
  input  in1,
  input  in2,
  input  in3,
  output out0
);

  wire buffer_1_out, even_parity_1_out, not_1_out, not_2_out, not_3_out, not_4_out, odd_parity_1_out,
       or_1_out;

  xor odd_parity_1 (odd_parity_1_out, in1, in3, 1'b0, in0);
  not not_1 (not_1_out, odd_parity_1_out);
  not not_2 (not_2_out, not_1_out);
  xnor even_parity_1 (even_parity_1_out, odd_parity_1_out, ~not_1_out, in2);  // Even_Parity
  not not_3 (not_3_out, not_1_out);
  or or_1 (or_1_out, ~in3, ~1'b0);  // OR_Gate
  nand nand_1 (out0, ~in3, not_3_out);  // NAND_Gate
  buf buffer_1 (buffer_1_out, or_1_out);
  not not_4 (not_4_out, in3);
endmodule
