// Logisim project plain-037.circ as structural Verilog: 1 circuit, main circuit main
module main (
  input  in0,
  input  in1,
  input  in2,
  output out0
);

  wire and_1_out, buffer_1_out, even_parity_1_out, nand_1_out, nor_1_out, or_1_out, xor_1_out, xor_2_out;

  buf buffer_1 (buffer_1_out, in1);
  or or_1 (or_1_out, 1'b1, buffer_1_out, 1'b1, in2, in2);
  xnor even_parity_1 (even_parity_1_out, in0, in1, ~in1, 1'b1, ~in2);  // Even_Parity
  nand nand_1 (nand_1_out, in1, in2, in0, 1'b1, or_1_out);
  xor xor_1 (xor_1_out, in0, ~in0);  // XOR_Gate
  ExactlyOne xor_2 (.out(xor_2_out), .in0(in2), .in1(buffer_1_out), .in2(in1));
  and and_1 (and_1_out, or_1_out, ~in1, or_1_out, 1'b1);  // AND_Gate
  xor xor_3 (out0, xor_2_out, or_1_out);
  nor nor_1 (nor_1_out, 1'b1, ~buffer_1_out, ~in1, in1, buffer_1_out);  // NOR_Gate
endmodule
