// Logisim project plain-038.circ as structural Verilog: 1 circuit, main circuit main
module main (
  input  in0,
  input  in1,
  input  in2,
  output out0
);

  wire and_1_out, nand_1_out, nor_1_out, not_1_out, odd_parity_1_out, odd_parity_2_out, xnor_1_out;

  nand nand_1 (nand_1_out, in0, in1, in0);
  not not_1 (not_1_out, 1'b1);
  nor nor_1 (nor_1_out, nand_1_out, nand_1_out, in0, 1'b1, in0);
  NotExactlyOne xnor_1 (.out(xnor_1_out), .in0(in1), .in1(nand_1_out), .in2(1'b1));
  xor odd_parity_1 (odd_parity_1_out, in2, not_1_out, xnor_1_out, not_1_out);
  and and_1 (and_1_out, in0, 1'b1);
  xor odd_parity_2 (odd_parity_2_out, and_1_out, odd_parity_1_out, in2, nor_1_out);
  xnor even_parity_1 (out0, odd_parity_1_out, in1, odd_parity_1_out, ~in0, nor_1_out);  // Even_Parity
endmodule
