// Logisim project plain-039.circ as structural Verilog: 1 circuit, main circuit main
module main (
  input  in0,
  output out0,
  output out1
);

  wire even_parity_1_out, nor_1_out, nor_2_out, not_1_out, odd_parity_1_out, xor_1_out;

  xor xor_1 (xor_1_out, 1'b0, 1'b0);
  xor odd_parity_1 (odd_parity_1_out, 1'b0, xor_1_out, in0, xor_1_out, ~1'b0);  // Odd_Parity
  not not_1 (not_1_out, odd_parity_1_out);
  xnor even_parity_1 (even_parity_1_out, odd_parity_1_out, not_1_out, ~odd_parity_1_out);  // Even_Parity
  nor nor_1 (nor_1_out, ~not_1_out, not_1_out);  // NOR_Gate
  nor nor_2 (nor_2_out, ~even_parity_1_out, ~not_1_out, ~not_1_out, in0, even_parity_1_out);  // NOR_Gate
  or or_1 (out1, not_1_out, xor_1_out);
  xor xor_2 (out0, out1, in0);
endmodule
