// Logisim project plain-040.circ as structural Verilog: 1 circuit, main circuit main
module main (
  input  in0,
  input  in1,
  input  in2,
  output out0
);

  wire and_1_out, buffer_1_out, even_parity_1_out, odd_parity_1_out, or_1_out, or_2_out, xnor_1_out;

  xor odd_parity_1 (odd_parity_1_out, ~in0, in0, ~in0, in0);  // Odd_Parity
  or or_1 (or_1_out, odd_parity_1_out, in0);
  NotExactlyOne xnor_1 (.out(xnor_1_out), .in0(in2), .in1(in2), .in2(in2));
  buf buffer_1 (buffer_1_out, 1'b1);
  and and_1 (and_1_out, buffer_1_out, xnor_1_out, odd_parity_1_out, ~or_1_out, 1'b1);  // AND_Gate
  xnor even_parity_1 (even_parity_1_out, odd_parity_1_out, buffer_1_out, 1'b1, or_1_out, 1'b1);
  buf buffer_2 (out0, in2);
  or or_2 (or_2_out, in0, ~in2, out0);  // OR_Gate
endmodule
