// Logisim project comp-adder-w3-floatb.circ as structural Verilog: 2 circuits, main circuit tty_harness
module main (
  input  i0_0,
  input  i0_1,
  input  i0_2,
  input  i3,
  input  i4,
  output [2:0] o2
);

  wire [2:0] n1;

  Adder #(.width(3)) adder_1 (.a({i0_2, i0_1, i0_0}), .b(n1), .out(o2), .cin(i3), .cout(i4));

  // Other names for the same wires on the sheet: n0[2:0] = {i0_2, i0_1, i0_0}; n0_0 = i0_0; n0_1 = i0_1; n0_2 = i0_2;
  //   n2[2:0] = o2; n3 = i3; n4 = i4
endmodule

module tty_harness (
  output p_i0_0,
  output p_i0_1,
  output p_i0_2,
  output [2:0] p_o2,
  output p_i3,
  output p_i4,
  output halt
);

  Clock #(.lowDuration(32)) clock_1 (.out(halt));
  Clock clock_2 (.out(p_i0_0));
  Clock #(.highDuration(2), .lowDuration(2)) clock_3 (.out(p_i0_1));
  Clock #(.highDuration(4), .lowDuration(4)) clock_4 (.out(p_i0_2));
  Clock #(.highDuration(8), .lowDuration(8)) clock_5 (.out(p_i3));
  Clock #(.highDuration(16), .lowDuration(16)) clock_6 (.out(p_i4));
  main main_1 (.i0_0(p_i0_0), .i0_1(p_i0_1), .i0_2(p_i0_2), .i3(p_i3), .i4(p_i4), .o2(p_o2));
endmodule
