// Logisim project comp-bitadder-w1-i5.circ as structural Verilog: 2 circuits, main circuit tty_harness
module main (
  input  i1,
  input  i2,
  input  i3,
  input  i4,
  input  i5,
  output [2:0] o0
);

  BitAdder #(.width(1)) bitadder_1 (.in0(i1), .in1(i2), .in2(i3), .in3(i4), .in4(i5), .out(o0));

  // Other names for the same wires on the sheet: n0[2:0] = o0; n1 = i1; n2 = i2; n3 = i3; n4 = i4; n5 = i5
endmodule

module tty_harness (
  output p_i1,
  output p_i2,
  output p_i3,
  output [2:0] p_o0,
  output p_i4,
  output p_i5,
  output halt
);

  Clock #(.lowDuration(32)) clock_1 (.out(halt));
  Clock clock_2 (.out(p_i1));
  Clock #(.highDuration(2), .lowDuration(2)) clock_3 (.out(p_i2));
  Clock #(.highDuration(4), .lowDuration(4)) clock_4 (.out(p_i3));
  Clock #(.highDuration(8), .lowDuration(8)) clock_5 (.out(p_i4));
  Clock #(.highDuration(16), .lowDuration(16)) clock_6 (.out(p_i5));
  main main_1 (.i1(p_i1), .i2(p_i2), .i3(p_i3), .i4(p_i4), .i5(p_i5), .o0(p_o0));
endmodule
