// Logisim project comp-bitadder-w2-i3.circ as structural Verilog: 2 circuits, main circuit tty_harness
module main (
  input  i1_0,
  input  i1_1,
  input  i2_0,
  input  i2_1,
  input  i3_0,
  input  i3_1,
  output [2:0] o0
);

  BitAdder #(.width(2)) bitadder_1 (.in0({i1_1, i1_0}), .in1({i2_1, i2_0}), .in2({i3_1, i3_0}), .out(o0));

  // Other names for the same wires on the sheet: n0[2:0] = o0; n1[1:0] = {i1_1, i1_0}; n1_0 = i1_0; n1_1 = i1_1;
  //   n2[1:0] = {i2_1, i2_0}; n2_0 = i2_0; n2_1 = i2_1; n3[1:0] = {i3_1, i3_0}; n3_0 = i3_0; n3_1 = i3_1
endmodule

module tty_harness (
  output p_i1_0,
  output p_i1_1,
  output p_i2_0,
  output [2:0] p_o0,
  output p_i2_1,
  output p_i3_0,
  output p_i3_1,
  output halt
);

  Clock #(.lowDuration(64)) clock_1 (.out(halt));
  Clock clock_2 (.out(p_i1_0));
  Clock #(.highDuration(2), .lowDuration(2)) clock_3 (.out(p_i1_1));
  Clock #(.highDuration(4), .lowDuration(4)) clock_4 (.out(p_i2_0));
  Clock #(.highDuration(8), .lowDuration(8)) clock_5 (.out(p_i2_1));
  Clock #(.highDuration(16), .lowDuration(16)) clock_6 (.out(p_i3_0));
  Clock #(.highDuration(32), .lowDuration(32)) clock_7 (.out(p_i3_1));
  main main_1 (.i1_0(p_i1_0), .i1_1(p_i1_1), .i2_0(p_i2_0), .i2_1(p_i2_1), .i3_0(p_i3_0), .i3_1(p_i3_1), .o0(p_o0));
endmodule
