// Logisim project comp-bitfinder-w6-high0.circ as structural Verilog: 2 circuits, main circuit tty_harness
module main (
  input  i2_0,
  input  i2_1,
  input  i2_2,
  input  i2_3,
  input  i2_4,
  input  i2_5,
  output o0,
  output [2:0] o1
);

  BitFinder #(.width(6), .\type ("high0")) bitfinder_1 (
    .in({i2_5, i2_4, i2_3, i2_2, i2_1, i2_0}), .index(o1), .found(o0));

  // Other names for the same wires on the sheet: n0 = o0; n1[2:0] = o1;
  //   n2[5:0] = {i2_5, i2_4, i2_3, i2_2, i2_1, i2_0}; n2_0 = i2_0; n2_1 = i2_1; n2_2 = i2_2; n2_3 = i2_3; n2_4 = i2_4;
  //   n2_5 = i2_5
endmodule

module tty_harness (
  output p_i2_0,
  output p_i2_1,
  output p_i2_2,
  output p_o0,
  output p_i2_3,
  output [2:0] p_o1,
  output p_i2_4,
  output p_i2_5,
  output halt
);

  Clock #(.lowDuration(64)) clock_1 (.out(halt));
  Clock clock_2 (.out(p_i2_0));
  Clock #(.highDuration(2), .lowDuration(2)) clock_3 (.out(p_i2_1));
  Clock #(.highDuration(4), .lowDuration(4)) clock_4 (.out(p_i2_2));
  Clock #(.highDuration(8), .lowDuration(8)) clock_5 (.out(p_i2_3));
  Clock #(.highDuration(16), .lowDuration(16)) clock_6 (.out(p_i2_4));
  Clock #(.highDuration(32), .lowDuration(32)) clock_7 (.out(p_i2_5));
  main main_1 (
    .i2_0(p_i2_0), .i2_1(p_i2_1), .i2_2(p_i2_2), .i2_3(p_i2_3), .i2_4(p_i2_4), .i2_5(p_i2_5), .o0(p_o0),
    .o1(p_o1));
endmodule
