// Logisim project comp-bitselector-w5-g1.circ as structural Verilog: 2 circuits, main circuit tty_harness
module main (
  input  i1_0,
  input  i1_1,
  input  i1_2,
  input  i1_3,
  input  i1_4,
  input  i2_0,
  input  i2_1,
  input  i2_2,
  output o0
);

  BitSelector #(.width(5)) bitselector_1 (.in({i1_4, i1_3, i1_2, i1_1, i1_0}), .out(o0), .sel({i2_2, i2_1, i2_0}));

  // Other names for the same wires on the sheet: n0 = o0; n1[4:0] = {i1_4, i1_3, i1_2, i1_1, i1_0}; n1_0 = i1_0;
  //   n1_1 = i1_1; n1_2 = i1_2; n1_3 = i1_3; n1_4 = i1_4; n2[2:0] = {i2_2, i2_1, i2_0}; n2_0 = i2_0; n2_1 = i2_1;
  //   n2_2 = i2_2
endmodule

module tty_harness (
  output p_i1_0,
  output p_i1_1,
  output p_i1_2,
  output p_i1_3,
  output p_o0,
  output p_i1_4,
  output p_i2_0,
  output p_i2_1,
  output p_i2_2,
  output halt
);

  Clock #(.lowDuration(256)) clock_1 (.out(halt));
  Clock clock_2 (.out(p_i1_0));
  Clock #(.highDuration(2), .lowDuration(2)) clock_3 (.out(p_i1_1));
  Clock #(.highDuration(4), .lowDuration(4)) clock_4 (.out(p_i1_2));
  Clock #(.highDuration(8), .lowDuration(8)) clock_5 (.out(p_i1_3));
  Clock #(.highDuration(16), .lowDuration(16)) clock_6 (.out(p_i1_4));
  Clock #(.highDuration(32), .lowDuration(32)) clock_7 (.out(p_i2_0));
  Clock #(.highDuration(64), .lowDuration(64)) clock_8 (.out(p_i2_1));
  Clock #(.highDuration(128), .lowDuration(128)) clock_9 (.out(p_i2_2));
  main main_1 (
    .i1_0(p_i1_0), .i1_1(p_i1_1), .i1_2(p_i1_2), .i1_3(p_i1_3), .i1_4(p_i1_4), .i2_0(p_i2_0), .i2_1(p_i2_1),
    .i2_2(p_i2_2), .o0(p_o0));
endmodule
