// Logisim project comp-bitselector-w6-g2.circ as structural Verilog: 2 circuits, main circuit tty_harness
module main (
  input  i1_0,
  input  i1_1,
  input  i1_2,
  input  i1_3,
  input  i1_4,
  input  i1_5,
  input  i2_0,
  input  i2_1,
  output [1:0] o0
);

  BitSelector #(.width(6), .group(2)) bitselector_1 (
    .in({i1_5, i1_4, i1_3, i1_2, i1_1, i1_0}), .out(o0), .sel({i2_1, i2_0}));

  // Other names for the same wires on the sheet: n0[1:0] = o0; n1[5:0] = {i1_5, i1_4, i1_3, i1_2, i1_1, i1_0};
  //   n1_0 = i1_0; n1_1 = i1_1; n1_2 = i1_2; n1_3 = i1_3; n1_4 = i1_4; n1_5 = i1_5; n2[1:0] = {i2_1, i2_0};
  //   n2_0 = i2_0; n2_1 = i2_1
endmodule

module tty_harness (
  output p_i1_0,
  output p_i1_1,
  output p_i1_2,
  output p_i1_3,
  output [1:0] p_o0,
  output p_i1_4,
  output p_i1_5,
  output p_i2_0,
  output p_i2_1,
  output halt
);

  Clock #(.lowDuration(256)) clock_1 (.out(halt));
  Clock clock_2 (.out(p_i1_0));
  Clock #(.highDuration(2), .lowDuration(2)) clock_3 (.out(p_i1_1));
  Clock #(.highDuration(4), .lowDuration(4)) clock_4 (.out(p_i1_2));
  Clock #(.highDuration(8), .lowDuration(8)) clock_5 (.out(p_i1_3));
  Clock #(.highDuration(16), .lowDuration(16)) clock_6 (.out(p_i1_4));
  Clock #(.highDuration(32), .lowDuration(32)) clock_7 (.out(p_i1_5));
  Clock #(.highDuration(64), .lowDuration(64)) clock_8 (.out(p_i2_0));
  Clock #(.highDuration(128), .lowDuration(128)) clock_9 (.out(p_i2_1));
  main main_1 (
    .i1_0(p_i1_0), .i1_1(p_i1_1), .i1_2(p_i1_2), .i1_3(p_i1_3), .i1_4(p_i1_4), .i1_5(p_i1_5), .i2_0(p_i2_0),
    .i2_1(p_i2_1), .o0(p_o0));
endmodule
