// Logisim project comp-comparator-w4-unsigned.circ as structural Verilog: 2 circuits, main circuit tty_harness
module main (
  input  i0_0,
  input  i0_1,
  input  i0_2,
  input  i0_3,
  input  i1_0,
  input  i1_1,
  input  i1_2,
  input  i1_3,
  output o2,
  output o3,
  output o4
);

  Comparator #(.width(4), .mode("unsigned")) comparator_1 (
    .a({i0_3, i0_2, i0_1, i0_0}), .b({i1_3, i1_2, i1_1, i1_0}), .gt(o2), .eq(o3), .lt(o4));

  // Other names for the same wires on the sheet: n0[3:0] = {i0_3, i0_2, i0_1, i0_0}; n0_0 = i0_0; n0_1 = i0_1;
  //   n0_2 = i0_2; n0_3 = i0_3; n1[3:0] = {i1_3, i1_2, i1_1, i1_0}; n1_0 = i1_0; n1_1 = i1_1; n1_2 = i1_2;
  //   n1_3 = i1_3; n2 = o2; n3 = o3; n4 = o4
endmodule

module tty_harness (
  output p_i0_0,
  output p_i0_1,
  output p_i0_2,
  output p_o2,
  output p_i0_3,
  output p_o3,
  output p_i1_0,
  output p_o4,
  output p_i1_1,
  output p_i1_2,
  output p_i1_3,
  output halt
);

  Clock #(.lowDuration(256)) clock_1 (.out(halt));
  Clock clock_2 (.out(p_i0_0));
  Clock #(.highDuration(2), .lowDuration(2)) clock_3 (.out(p_i0_1));
  Clock #(.highDuration(4), .lowDuration(4)) clock_4 (.out(p_i0_2));
  Clock #(.highDuration(8), .lowDuration(8)) clock_5 (.out(p_i0_3));
  Clock #(.highDuration(16), .lowDuration(16)) clock_6 (.out(p_i1_0));
  Clock #(.highDuration(32), .lowDuration(32)) clock_7 (.out(p_i1_1));
  Clock #(.highDuration(64), .lowDuration(64)) clock_8 (.out(p_i1_2));
  Clock #(.highDuration(128), .lowDuration(128)) clock_9 (.out(p_i1_3));
  main main_1 (
    .i0_0(p_i0_0), .i0_1(p_i0_1), .i0_2(p_i0_2), .i0_3(p_i0_3), .i1_0(p_i1_0), .i1_1(p_i1_1), .i1_2(p_i1_2),
    .i1_3(p_i1_3), .o2(p_o2), .o3(p_o3), .o4(p_o4));
endmodule
