// Logisim project comp-counter-w3-max5-continue.circ as structural Verilog: 2 circuits, main circuit tty_harness
module main (
  input  i1_0,
  input  i1_1,
  input  i1_2,
  input  i2,
  input  i3,
  input  i4,
  input  i5,
  output [2:0] o0,
  output o6
);

  Counter #(.width(3), .max('h5), .ongoal("continue")) counter_1 (
    .load(i4), .D({i1_2, i1_1, i1_0}), .count(i5), .Q(o0), .carry(o6), .clk(i2), .clr(i3));

  // Other names for the same wires on the sheet: n0[2:0] = o0; n1[2:0] = {i1_2, i1_1, i1_0}; n1_0 = i1_0; n1_1 = i1_1;
  //   n1_2 = i1_2; n2 = i2; n3 = i3; n4 = i4; n5 = i5; n6 = o6
endmodule

module tty_harness (
  output p_i1_0,
  output p_i1_1,
  output p_i1_2,
  output [2:0] p_o0,
  output p_i2,
  output p_o6,
  output p_i3,
  output p_i4,
  output p_i5,
  output halt
);

  Clock #(.lowDuration(128)) clock_1 (.out(halt));
  Clock clock_2 (.out(p_i1_0));
  Clock #(.highDuration(2), .lowDuration(2)) clock_3 (.out(p_i1_1));
  Clock #(.highDuration(4), .lowDuration(4)) clock_4 (.out(p_i1_2));
  Clock #(.highDuration(8), .lowDuration(8)) clock_5 (.out(p_i2));
  Clock #(.highDuration(16), .lowDuration(16)) clock_6 (.out(p_i3));
  Clock #(.highDuration(32), .lowDuration(32)) clock_7 (.out(p_i4));
  Clock #(.highDuration(64), .lowDuration(64)) clock_8 (.out(p_i5));
  main main_1 (
    .i1_0(p_i1_0), .i1_1(p_i1_1), .i1_2(p_i1_2), .i2(p_i2), .i3(p_i3), .i4(p_i4), .i5(p_i5), .o0(p_o0),
    .o6(p_o6));
endmodule
