// Logisim project comp-decoder-s3-tristate.circ as structural Verilog: 2 circuits, main circuit tty_harness
module main (
  input  i8_0,
  input  i8_1,
  input  i8_2,
  input  i9,
  output o0,
  output o1,
  output o2,
  output o3,
  output o4,
  output o5,
  output o6,
  output o7
);

  Decoder #(.select(3), .tristate("true")) decoder_1 (
    .out0(o0), .out1(o1), .out2(o2), .out3(o3), .out4(o4), .out5(o5), .out6(o6), .out7(o7),
    .sel({i8_2, i8_1, i8_0}), .en(i9));

  // Other names for the same wires on the sheet: n0 = o0; n1 = o1; n2 = o2; n3 = o3; n4 = o4; n5 = o5; n6 = o6;
  //   n7 = o7; n8[2:0] = {i8_2, i8_1, i8_0}; n8_0 = i8_0; n8_1 = i8_1; n8_2 = i8_2; n9 = i9
endmodule

module tty_harness (
  output p_o0,
  output p_o1,
  output p_i8_0,
  output p_o2,
  output p_i8_1,
  output p_o3,
  output p_i8_2,
  output p_o4,
  output p_i9,
  output p_o5,
  output p_o6,
  output p_o7,
  output halt
);

  Clock #(.lowDuration(16)) clock_1 (.out(halt));
  Clock clock_2 (.out(p_i8_0));
  Clock #(.highDuration(2), .lowDuration(2)) clock_3 (.out(p_i8_1));
  Clock #(.highDuration(4), .lowDuration(4)) clock_4 (.out(p_i8_2));
  Clock #(.highDuration(8), .lowDuration(8)) clock_5 (.out(p_i9));
  main main_1 (
    .i8_0(p_i8_0), .i8_1(p_i8_1), .i8_2(p_i8_2), .i9(p_i9), .o0(p_o0), .o1(p_o1), .o2(p_o2), .o3(p_o3),
    .o4(p_o4), .o5(p_o5), .o6(p_o6), .o7(p_o7));
endmodule
