// Logisim project comp-demux-s1-west-zero.circ as structural Verilog: 2 circuits, main circuit tty_harness
module main (
  input  i2,
  input  i3,
  input  i4,
  output o0,
  output o1
);

  Demultiplexer #(.disabled(0)) demultiplexer_1 (.out0(o0), .out1(o1), .in(i4), .sel(i2), .en(i3));

  // Other names for the same wires on the sheet: n0 = o0; n1 = o1; n2 = i2; n3 = i3; n4 = i4
endmodule

module tty_harness (
  output p_i2,
  output p_o0,
  output p_i3,
  output p_o1,
  output p_i4,
  output halt
);

  Clock #(.lowDuration(8)) clock_1 (.out(halt));
  Clock clock_2 (.out(p_i2));
  Clock #(.highDuration(2), .lowDuration(2)) clock_3 (.out(p_i3));
  Clock #(.highDuration(4), .lowDuration(4)) clock_4 (.out(p_i4));
  main main_1 (.i2(p_i2), .i3(p_i3), .i4(p_i4), .o0(p_o0), .o1(p_o1));
endmodule
