// Logisim project comp-demux-s2-w2-tristate.circ as structural Verilog: 2 circuits, main circuit tty_harness
module main (
  input  i4_0,
  input  i4_1,
  input  i5,
  input  i6_0,
  input  i6_1,
  output [1:0] o0,
  output [1:0] o1,
  output [1:0] o2,
  output [1:0] o3
);

  Demultiplexer #(.select(2), .width(2), .tristate("true")) demultiplexer_1 (
    .out0(o0), .out1(o1), .out2(o2), .out3(o3), .in({i6_1, i6_0}), .sel({i4_1, i4_0}), .en(i5));

  // Other names for the same wires on the sheet: n0[1:0] = o0; n1[1:0] = o1; n2[1:0] = o2; n3[1:0] = o3;
  //   n4[1:0] = {i4_1, i4_0}; n4_0 = i4_0; n4_1 = i4_1; n5 = i5; n6[1:0] = {i6_1, i6_0}; n6_0 = i6_0; n6_1 = i6_1
endmodule

module tty_harness (
  output p_i4_0,
  output [1:0] p_o0,
  output p_i4_1,
  output [1:0] p_o1,
  output p_i5,
  output [1:0] p_o2,
  output p_i6_0,
  output [1:0] p_o3,
  output p_i6_1,
  output halt
);

  Clock #(.lowDuration(32)) clock_1 (.out(halt));
  Clock clock_2 (.out(p_i4_0));
  Clock #(.highDuration(2), .lowDuration(2)) clock_3 (.out(p_i4_1));
  Clock #(.highDuration(4), .lowDuration(4)) clock_4 (.out(p_i5));
  Clock #(.highDuration(8), .lowDuration(8)) clock_5 (.out(p_i6_0));
  Clock #(.highDuration(16), .lowDuration(16)) clock_6 (.out(p_i6_1));
  main main_1 (
    .i4_0(p_i4_0), .i4_1(p_i4_1), .i5(p_i5), .i6_0(p_i6_0), .i6_1(p_i6_1), .o0(p_o0), .o1(p_o1), .o2(p_o2),
    .o3(p_o3));
endmodule
