// Logisim project comp-dff-falling.circ as structural Verilog: 2 circuits, main circuit tty_harness
module main (
  input  i0,
  input  i1,
  input  i4,
  input  i5,
  input  i6,
  output o2,
  output o3
);

  D_Flip_Flop #(.trigger("falling")) d_ff_1 (.clk(i1), .D(i0), .Q(o2), .Qn(o3), .preset(i5), .en(i6), .reset(i4));

  // Other names for the same wires on the sheet: n0 = i0; n1 = i1; n2 = o2; n3 = o3; n4 = i4; n5 = i5; n6 = i6
endmodule

module tty_harness (
  output p_i0,
  output p_i1,
  output p_o2,
  output p_i4,
  output p_o3,
  output p_i5,
  output p_i6,
  output halt
);

  Clock #(.lowDuration(32)) clock_1 (.out(halt));
  Clock clock_2 (.out(p_i0));
  Clock #(.highDuration(2), .lowDuration(2)) clock_3 (.out(p_i1));
  Clock #(.highDuration(4), .lowDuration(4)) clock_4 (.out(p_i4));
  Clock #(.highDuration(8), .lowDuration(8)) clock_5 (.out(p_i5));
  Clock #(.highDuration(16), .lowDuration(16)) clock_6 (.out(p_i6));
  main main_1 (.i0(p_i0), .i1(p_i1), .i4(p_i4), .i5(p_i5), .i6(p_i6), .o2(p_o2), .o3(p_o3));
endmodule
