// Logisim project comp-jkff-falling.circ as structural Verilog: 2 circuits, main circuit tty_harness
module main (
  input  i0,
  input  i1,
  input  i2,
  input  i5,
  input  i6,
  input  i7,
  output o3,
  output o4
);

  J_K_Flip_Flop #(.trigger("falling")) j_k_ff_1 (
    .J(i0), .clk(i2), .K(i1), .Q(o3), .Qn(o4), .preset(i6), .en(i7), .reset(i5));

  // Other names for the same wires on the sheet: n0 = i0; n1 = i1; n2 = i2; n3 = o3; n4 = o4; n5 = i5; n6 = i6;
  //   n7 = i7
endmodule

module tty_harness (
  output p_i0,
  output p_i1,
  output p_i2,
  output p_o3,
  output p_i5,
  output p_o4,
  output p_i6,
  output p_i7,
  output halt
);

  Clock #(.lowDuration(64)) clock_1 (.out(halt));
  Clock clock_2 (.out(p_i0));
  Clock #(.highDuration(2), .lowDuration(2)) clock_3 (.out(p_i1));
  Clock #(.highDuration(4), .lowDuration(4)) clock_4 (.out(p_i2));
  Clock #(.highDuration(8), .lowDuration(8)) clock_5 (.out(p_i5));
  Clock #(.highDuration(16), .lowDuration(16)) clock_6 (.out(p_i6));
  Clock #(.highDuration(32), .lowDuration(32)) clock_7 (.out(p_i7));
  main main_1 (.i0(p_i0), .i1(p_i1), .i2(p_i2), .i5(p_i5), .i6(p_i6), .i7(p_i7), .o3(p_o3), .o4(p_o4));
endmodule
