// Logisim project comp-mux-s1-w2.circ as structural Verilog: 2 circuits, main circuit tty_harness
module main (
  input  i0_0,
  input  i0_1,
  input  i1_0,
  input  i1_1,
  input  i2,
  input  i3,
  output [1:0] o4
);

  Multiplexer #(.width(2)) multiplexer_1 (.in0({i0_1, i0_0}), .in1({i1_1, i1_0}), .out(o4), .sel(i2), .en(i3));

  // Other names for the same wires on the sheet: n0[1:0] = {i0_1, i0_0}; n0_0 = i0_0; n0_1 = i0_1;
  //   n1[1:0] = {i1_1, i1_0}; n1_0 = i1_0; n1_1 = i1_1; n2 = i2; n3 = i3; n4[1:0] = o4
endmodule

module tty_harness (
  output p_i0_0,
  output p_i0_1,
  output p_i1_0,
  output [1:0] p_o4,
  output p_i1_1,
  output p_i2,
  output p_i3,
  output halt
);

  Clock #(.lowDuration(64)) clock_1 (.out(halt));
  Clock clock_2 (.out(p_i0_0));
  Clock #(.highDuration(2), .lowDuration(2)) clock_3 (.out(p_i0_1));
  Clock #(.highDuration(4), .lowDuration(4)) clock_4 (.out(p_i1_0));
  Clock #(.highDuration(8), .lowDuration(8)) clock_5 (.out(p_i1_1));
  Clock #(.highDuration(16), .lowDuration(16)) clock_6 (.out(p_i2));
  Clock #(.highDuration(32), .lowDuration(32)) clock_7 (.out(p_i3));
  main main_1 (.i0_0(p_i0_0), .i0_1(p_i0_1), .i1_0(p_i1_0), .i1_1(p_i1_1), .i2(p_i2), .i3(p_i3), .o4(p_o4));
endmodule
