// Logisim project comp-mux-s2-tr-north-zero.circ as structural Verilog: 2 circuits, main circuit tty_harness
module main (
  input  i0,
  input  i1,
  input  i2,
  input  i3,
  input  i4_0,
  input  i4_1,
  input  i5,
  output o6
);

  Multiplexer #(.select(2), .disabled(0)) multiplexer_1 (
    .in0(i0), .in1(i1), .in2(i2), .in3(i3), .out(o6), .sel({i4_1, i4_0}), .en(i5));

  // Other names for the same wires on the sheet: n0 = i0; n1 = i1; n2 = i2; n3 = i3; n4[1:0] = {i4_1, i4_0};
  //   n4_0 = i4_0; n4_1 = i4_1; n5 = i5; n6 = o6
endmodule

module tty_harness (
  output p_i0,
  output p_i1,
  output p_i2,
  output p_i3,
  output p_o6,
  output p_i4_0,
  output p_i4_1,
  output p_i5,
  output halt
);

  Clock #(.lowDuration(128)) clock_1 (.out(halt));
  Clock clock_2 (.out(p_i0));
  Clock #(.highDuration(2), .lowDuration(2)) clock_3 (.out(p_i1));
  Clock #(.highDuration(4), .lowDuration(4)) clock_4 (.out(p_i2));
  Clock #(.highDuration(8), .lowDuration(8)) clock_5 (.out(p_i3));
  Clock #(.highDuration(16), .lowDuration(16)) clock_6 (.out(p_i4_0));
  Clock #(.highDuration(32), .lowDuration(32)) clock_7 (.out(p_i4_1));
  Clock #(.highDuration(64), .lowDuration(64)) clock_8 (.out(p_i5));
  main main_1 (.i0(p_i0), .i1(p_i1), .i2(p_i2), .i3(p_i3), .i4_0(p_i4_0), .i4_1(p_i4_1), .i5(p_i5), .o6(p_o6));
endmodule
