// Logisim project comp-mux-s3-noenable.circ as structural Verilog: 2 circuits, main circuit tty_harness
module main (
  input  i0,
  input  i1,
  input  i2,
  input  i3,
  input  i4,
  input  i5,
  input  i6,
  input  i7,
  input  i8_0,
  input  i8_1,
  input  i8_2,
  output o9
);

  Multiplexer #(.select(3), .enable("false")) multiplexer_1 (
    .in0(i0), .in1(i1), .in2(i2), .in3(i3), .in4(i4), .in5(i5), .in6(i6), .in7(i7), .out(o9),
    .sel({i8_2, i8_1, i8_0}));

  // Other names for the same wires on the sheet: n0 = i0; n1 = i1; n2 = i2; n3 = i3; n4 = i4; n5 = i5; n6 = i6;
  //   n7 = i7; n8[2:0] = {i8_2, i8_1, i8_0}; n8_0 = i8_0; n8_1 = i8_1; n8_2 = i8_2; n9 = o9
endmodule

module tty_harness (
  output p_i0,
  output p_i1,
  output p_i2,
  output p_i3,
  output p_i4,
  output p_i5,
  output p_o9,
  output p_i6,
  output p_i7,
  output p_i8_0,
  output p_i8_1,
  output p_i8_2,
  output halt
);

  Clock #(.lowDuration(2048)) clock_1 (.out(halt));
  Clock clock_2 (.out(p_i0));
  Clock #(.highDuration(2), .lowDuration(2)) clock_3 (.out(p_i1));
  Clock #(.highDuration(4), .lowDuration(4)) clock_4 (.out(p_i2));
  Clock #(.highDuration(8), .lowDuration(8)) clock_5 (.out(p_i3));
  Clock #(.highDuration(16), .lowDuration(16)) clock_6 (.out(p_i4));
  Clock #(.highDuration(32), .lowDuration(32)) clock_7 (.out(p_i5));
  Clock #(.highDuration(64), .lowDuration(64)) clock_8 (.out(p_i6));
  Clock #(.highDuration(128), .lowDuration(128)) clock_9 (.out(p_i7));
  Clock #(.highDuration(256), .lowDuration(256)) clock_10 (.out(p_i8_0));
  Clock #(.highDuration(512), .lowDuration(512)) clock_11 (.out(p_i8_1));
  Clock #(.highDuration(1024), .lowDuration(1024)) clock_12 (.out(p_i8_2));
  main main_1 (
    .i0(p_i0), .i1(p_i1), .i2(p_i2), .i3(p_i3), .i4(p_i4), .i5(p_i5), .i6(p_i6), .i7(p_i7), .i8_0(p_i8_0),
    .i8_1(p_i8_1), .i8_2(p_i8_2), .o9(p_o9));
endmodule
