// Logisim project comp-negator-w4-float.circ as structural Verilog: 2 circuits, main circuit tty_harness
module main (
  output [3:0] o1
);

  wire [3:0] n0;

  Negator #(.width(4)) negator_1 (.in(n0), .out(o1));

  // Other names for the same wires on the sheet: n1[3:0] = o1
endmodule

module tty_harness (
  output [3:0] p_o1,
  output halt
);

  Clock clock_1 (.out(halt));
  main main_1 (.o1(p_o1));
endmodule
