// Logisim project comp-negator-w5.circ as structural Verilog: 2 circuits, main circuit tty_harness
module main (
  input  i0_0,
  input  i0_1,
  input  i0_2,
  input  i0_3,
  input  i0_4,
  output [4:0] o1
);

  Negator #(.width(5)) negator_1 (.in({i0_4, i0_3, i0_2, i0_1, i0_0}), .out(o1));

  // Other names for the same wires on the sheet: n0[4:0] = {i0_4, i0_3, i0_2, i0_1, i0_0}; n0_0 = i0_0; n0_1 = i0_1;
  //   n0_2 = i0_2; n0_3 = i0_3; n0_4 = i0_4; n1[4:0] = o1
endmodule

module tty_harness (
  output p_i0_0,
  output p_i0_1,
  output p_i0_2,
  output [4:0] p_o1,
  output p_i0_3,
  output p_i0_4,
  output halt
);

  Clock #(.lowDuration(32)) clock_1 (.out(halt));
  Clock clock_2 (.out(p_i0_0));
  Clock #(.highDuration(2), .lowDuration(2)) clock_3 (.out(p_i0_1));
  Clock #(.highDuration(4), .lowDuration(4)) clock_4 (.out(p_i0_2));
  Clock #(.highDuration(8), .lowDuration(8)) clock_5 (.out(p_i0_3));
  Clock #(.highDuration(16), .lowDuration(16)) clock_6 (.out(p_i0_4));
  main main_1 (.i0_0(p_i0_0), .i0_1(p_i0_1), .i0_2(p_i0_2), .i0_3(p_i0_3), .i0_4(p_i0_4), .o1(p_o1));
endmodule
