// Logisim project comp-priencoder-s2.circ as structural Verilog: 2 circuits, main circuit tty_harness
module main (
  input  i0,
  input  i1,
  input  i2,
  input  i3,
  input  i5,
  output [1:0] o4,
  output o6,
  output o7
);

  Priority_Encoder #(.select(2)) priority_encoder_1 (
    .in0(i0), .in1(i1), .in2(i2), .in3(i3), .out(o4), .gs(o7), .en_out(o6), .en_in(i5));

  // Other names for the same wires on the sheet: n0 = i0; n1 = i1; n2 = i2; n3 = i3; n4[1:0] = o4; n5 = i5; n6 = o6;
  //   n7 = o7
endmodule

module tty_harness (
  output p_i0,
  output p_i1,
  output [1:0] p_o4,
  output p_i2,
  output p_o6,
  output p_i3,
  output p_o7,
  output p_i5,
  output halt
);

  Clock #(.lowDuration(32)) clock_1 (.out(halt));
  Clock clock_2 (.out(p_i0));
  Clock #(.highDuration(2), .lowDuration(2)) clock_3 (.out(p_i1));
  Clock #(.highDuration(4), .lowDuration(4)) clock_4 (.out(p_i2));
  Clock #(.highDuration(8), .lowDuration(8)) clock_5 (.out(p_i3));
  Clock #(.highDuration(16), .lowDuration(16)) clock_6 (.out(p_i5));
  main main_1 (.i0(p_i0), .i1(p_i1), .i2(p_i2), .i3(p_i3), .i5(p_i5), .o4(p_o4), .o6(p_o6), .o7(p_o7));
endmodule
