// Logisim project comp-priencoder-s3-zero.circ as structural Verilog: 2 circuits, main circuit tty_harness
module main (
  input  i0,
  input  i1,
  input  i2,
  input  i3,
  input  i4,
  input  i5,
  input  i6,
  input  i7,
  input  i9,
  output [2:0] o8,
  output o10,
  output o11
);

  Priority_Encoder #(.disabled(0)) priority_encoder_1 (
    .in0(i0), .in1(i1), .in2(i2), .in3(i3), .in4(i4), .in5(i5), .in6(i6), .in7(i7), .out(o8), .en_in(i9),
    .gs(o11), .en_out(o10));

  // Other names for the same wires on the sheet: n0 = i0; n1 = i1; n2 = i2; n3 = i3; n4 = i4; n5 = i5; n6 = i6;
  //   n7 = i7; n8[2:0] = o8; n9 = i9; n10 = o10; n11 = o11
endmodule

module tty_harness (
  output p_i0,
  output p_i1,
  output p_i2,
  output p_i3,
  output [2:0] p_o8,
  output p_i4,
  output p_o10,
  output p_i5,
  output p_o11,
  output p_i6,
  output p_i7,
  output p_i9,
  output halt
);

  Clock #(.lowDuration(512)) clock_1 (.out(halt));
  Clock clock_2 (.out(p_i0));
  Clock #(.highDuration(2), .lowDuration(2)) clock_3 (.out(p_i1));
  Clock #(.highDuration(4), .lowDuration(4)) clock_4 (.out(p_i2));
  Clock #(.highDuration(8), .lowDuration(8)) clock_5 (.out(p_i3));
  Clock #(.highDuration(16), .lowDuration(16)) clock_6 (.out(p_i4));
  Clock #(.highDuration(32), .lowDuration(32)) clock_7 (.out(p_i5));
  Clock #(.highDuration(64), .lowDuration(64)) clock_8 (.out(p_i6));
  Clock #(.highDuration(128), .lowDuration(128)) clock_9 (.out(p_i7));
  Clock #(.highDuration(256), .lowDuration(256)) clock_10 (.out(p_i9));
  main main_1 (
    .i0(p_i0), .i1(p_i1), .i2(p_i2), .i3(p_i3), .i4(p_i4), .i5(p_i5), .i6(p_i6), .i7(p_i7), .i9(p_i9),
    .o8(p_o8), .o10(p_o10), .o11(p_o11));
endmodule
