// Logisim project comp-ram-a2-d2-combined.circ as structural Verilog: 2 circuits, main circuit tty_harness
module main (
  input  i5,
  input  i3,
  input  i1_0,
  input  i1_1,
  input  write_0,
  input  write_1,
  output [1:0] o0
);

  wire write_enable;

  RAM #(.addrWidth(2), .dataWidth(2)) ram_1 (.addr({i1_1, i1_0}), .data(o0), .sel(1'b1), .clk(i5), .ld(i3), .clr(1'b0));
  not not_1 (write_enable, i3);
  assign o0 = write_enable ? {write_1, write_0} : 2'bz;  // Controlled_Buffer controlled_buffer_1

  // Other names for the same wires on the sheet: n0[1:0] = o0; n1[1:0] = {i1_1, i1_0}; n1_0 = i1_0; n1_1 = i1_1;
  //   n3 = i3; n5 = i5; write_data[1:0] = {write_1, write_0}
endmodule

module tty_harness (
  output p_i5,
  output p_i3,
  output p_i1_0,
  output [1:0] p_o0,
  output p_i1_1,
  output p_write_0,
  output p_write_1,
  output halt
);

  Clock #(.lowDuration(64)) clock_1 (.out(halt));
  Clock clock_2 (.out(p_i5));
  Clock #(.highDuration(2), .lowDuration(2)) clock_3 (.out(p_i3));
  Clock #(.highDuration(4), .lowDuration(4)) clock_4 (.out(p_i1_0));
  Clock #(.highDuration(8), .lowDuration(8)) clock_5 (.out(p_i1_1));
  Clock #(.highDuration(16), .lowDuration(16)) clock_6 (.out(p_write_0));
  Clock #(.highDuration(32), .lowDuration(32)) clock_7 (.out(p_write_1));
  main main_1 (.i5(p_i5), .i3(p_i3), .i1_0(p_i1_0), .i1_1(p_i1_1), .write_0(p_write_0), .write_1(p_write_1), .o0(p_o0));
endmodule
