// Logisim project comp-ram-a2-d2-separate.circ as structural Verilog: 2 circuits, main circuit tty_harness
module main (
  input  i1_0,
  input  i1_1,
  input  i2,
  input  i3,
  input  i4,
  input  i5,
  input  i6,
  input  i7_0,
  input  i7_1,
  output [1:0] o0
);

  RAM #(.addrWidth(2), .dataWidth(2), .bus("separate")) ram_1 (
    .addr({i1_1, i1_0}), .din({i7_1, i7_0}), .data(o0), .str(i6), .sel(i2), .clk(i5), .ld(i3), .clr(i4));

  // Other names for the same wires on the sheet: n0[1:0] = o0; n1[1:0] = {i1_1, i1_0}; n1_0 = i1_0; n1_1 = i1_1;
  //   n2 = i2; n3 = i3; n4 = i4; n5 = i5; n6 = i6; n7[1:0] = {i7_1, i7_0}; n7_0 = i7_0; n7_1 = i7_1
endmodule

module tty_harness (
  output p_i1_0,
  output p_i1_1,
  output p_i2,
  output p_i3,
  output p_i4,
  output [1:0] p_o0,
  output p_i5,
  output p_i6,
  output p_i7_0,
  output p_i7_1,
  output halt
);

  Clock #(.lowDuration(512)) clock_1 (.out(halt));
  Clock clock_2 (.out(p_i1_0));
  Clock #(.highDuration(2), .lowDuration(2)) clock_3 (.out(p_i1_1));
  Clock #(.highDuration(4), .lowDuration(4)) clock_4 (.out(p_i2));
  Clock #(.highDuration(8), .lowDuration(8)) clock_5 (.out(p_i3));
  Clock #(.highDuration(16), .lowDuration(16)) clock_6 (.out(p_i4));
  Clock #(.highDuration(32), .lowDuration(32)) clock_7 (.out(p_i5));
  Clock #(.highDuration(64), .lowDuration(64)) clock_8 (.out(p_i6));
  Clock #(.highDuration(128), .lowDuration(128)) clock_9 (.out(p_i7_0));
  Clock #(.highDuration(256), .lowDuration(256)) clock_10 (.out(p_i7_1));
  main main_1 (
    .i1_0(p_i1_0), .i1_1(p_i1_1), .i2(p_i2), .i3(p_i3), .i4(p_i4), .i5(p_i5), .i6(p_i6), .i7_0(p_i7_0),
    .i7_1(p_i7_1), .o0(p_o0));
endmodule
