// Logisim project comp-random-seed42.circ as structural Verilog: 2 circuits, main circuit tty_harness
module main (
  input  i1,
  input  i2,
  input  i3,
  output [11:0] o0
);

  Random #(.width(12), .seed(42)) random_1 (.clk(i1), .next(i2), .out(o0), .clr(i3));

  // Other names for the same wires on the sheet: n0[11:0] = o0; n1 = i1; n2 = i2; n3 = i3
endmodule

module tty_harness (
  output p_i1,
  output p_i2,
  output [11:0] p_o0,
  output p_i3,
  output halt
);

  Clock #(.lowDuration(8)) clock_1 (.out(halt));
  Clock clock_2 (.out(p_i1));
  Clock #(.highDuration(2), .lowDuration(2)) clock_3 (.out(p_i2));
  Clock #(.highDuration(4), .lowDuration(4)) clock_4 (.out(p_i3));
  main main_1 (.i1(p_i1), .i2(p_i2), .i3(p_i3), .o0(p_o0));
endmodule
