// Logisim project comp-rom-a4-d8-runs.circ as structural Verilog: 2 circuits, main circuit tty_harness
module main (
  input  i1_0,
  input  i1_1,
  input  i1_2,
  input  i1_3,
  input  i2,
  output [7:0] o0
);

  ROM #(.addrWidth(4)) rom_1 (.addr({i1_3, i1_2, i1_1, i1_0}), .data(o0), .sel(i2));

  // Other names for the same wires on the sheet: n0[7:0] = o0; n1[3:0] = {i1_3, i1_2, i1_1, i1_0}; n1_0 = i1_0;
  //   n1_1 = i1_1; n1_2 = i1_2; n1_3 = i1_3; n2 = i2

  // Notes on the sheet:
  //   contents of rom_1 (hex, n*v repeats v):
  //   5*9 ab 4*0 ff
endmodule

module tty_harness (
  output p_i1_0,
  output p_i1_1,
  output p_i1_2,
  output [7:0] p_o0,
  output p_i1_3,
  output p_i2,
  output halt
);

  Clock #(.lowDuration(32)) clock_1 (.out(halt));
  Clock clock_2 (.out(p_i1_0));
  Clock #(.highDuration(2), .lowDuration(2)) clock_3 (.out(p_i1_1));
  Clock #(.highDuration(4), .lowDuration(4)) clock_4 (.out(p_i1_2));
  Clock #(.highDuration(8), .lowDuration(8)) clock_5 (.out(p_i1_3));
  Clock #(.highDuration(16), .lowDuration(16)) clock_6 (.out(p_i2));
  main main_1 (.i1_0(p_i1_0), .i1_1(p_i1_1), .i1_2(p_i1_2), .i1_3(p_i1_3), .i2(p_i2), .o0(p_o0));
endmodule
