// Logisim project comp-shiftreg-w1-l3.circ as structural Verilog: 2 circuits, main circuit tty_harness
module main (
  input  i0,
  input  i1,
  input  i2,
  input  i3,
  input  i5,
  input  i6,
  input  i8,
  input  i10,
  output o4,
  output o7,
  output o9,
  output o11
);

  Shift_Register #(.length(3)) shift_register_1 (
    .shift(i1), .in(i0), .clk(i2), .out(o4), .load(i5), .clr(i3), .d0(i6), .q0(o7), .d1(i8), .q1(o9),
    .d2(i10), .q2(o11));

  // Other names for the same wires on the sheet: n0 = i0; n1 = i1; n2 = i2; n3 = i3; n4 = o4; n5 = i5; n6 = i6;
  //   n7 = o7; n8 = i8; n9 = o9; n10 = i10; n11 = o11
endmodule

module tty_harness (
  output p_i0,
  output p_i1,
  output p_i2,
  output p_o4,
  output p_i3,
  output p_o7,
  output p_i5,
  output p_o9,
  output p_i6,
  output p_o11,
  output p_i8,
  output p_i10,
  output halt
);

  Clock #(.lowDuration(256)) clock_1 (.out(halt));
  Clock clock_2 (.out(p_i0));
  Clock #(.highDuration(2), .lowDuration(2)) clock_3 (.out(p_i1));
  Clock #(.highDuration(4), .lowDuration(4)) clock_4 (.out(p_i2));
  Clock #(.highDuration(8), .lowDuration(8)) clock_5 (.out(p_i3));
  Clock #(.highDuration(16), .lowDuration(16)) clock_6 (.out(p_i5));
  Clock #(.highDuration(32), .lowDuration(32)) clock_7 (.out(p_i6));
  Clock #(.highDuration(64), .lowDuration(64)) clock_8 (.out(p_i8));
  Clock #(.highDuration(128), .lowDuration(128)) clock_9 (.out(p_i10));
  main main_1 (
    .i0(p_i0), .i1(p_i1), .i2(p_i2), .i3(p_i3), .i5(p_i5), .i6(p_i6), .i8(p_i8), .i10(p_i10), .o4(p_o4),
    .o7(p_o7), .o9(p_o9), .o11(p_o11));
endmodule
