// Logisim project feedback-1001.circ as structural Verilog: 2 circuits, main circuit tty_harness
module main (
  input  in0,
  input  in1,
  output out0,
  output out1
);

  wire n0, n1, n2, n3;

  not not_1 (n0, in1);
  not not_2 (out1, n1);
  xor odd_parity_1 (n1, in1, n0, in1, n0);
  xnor xnor_1 (out0, in0, n0, in0, ~in0, in0);  // XNOR_Gate
  and and_1 (n2, in1, in0, in1);
  not not_3 (n3, n1);

  // Other names for the same wires on the sheet: n4 = out1; n5 = out0

  // Notes on the sheet:
  //   odd_parity_1 drives only 0 and floats otherwise
endmodule

module tty_harness (
  output p_in0,
  output p_out0,
  output p_in1,
  output p_out1,
  output halt
);

  Clock #(.lowDuration(4)) clock_1 (.out(halt));
  Clock clock_2 (.out(p_in0));
  Clock #(.highDuration(2), .lowDuration(2)) clock_3 (.out(p_in1));
  main main_1 (.in0(p_in0), .in1(p_in1), .out0(p_out0), .out1(p_out1));
endmodule
