// Logisim project feedback-1002.circ as structural Verilog: 2 circuits, main circuit tty_harness
module main (
  input  in0,
  input  in1,
  input  in2,
  output out0,
  output out1,
  output out2
);

  wire n0, n1, n2, n3, n4, n5;

  nor nor_1 (n0, ~in1, out1, ~in1);  // NOR_Gate
  not not_1 (n4, in0);
  nor nor_2 (out0, n3, ~in0, n2, in1);  // NOR_Gate
  assign n1 = n0 ? in0 : 1'bz;  // Controlled_Buffer controlled_buffer_1
  not not_2 (n5, n3);
  ExactlyOne xor_1 (.out(n2), .in0(in2), .in1(n1), .in2(n0));
  or or_1 (out2, ~n1, ~n2, ~in0, n2, n4);  // OR_Gate
  ExactlyOne xor_2 (.out(n3), .in0(n0), .in1(n2), .in2(n0));
  ExactlyOne xor_3 (.out(out1), .in0(in2), .in1(n4), .in2(n2), .in3(out1), .in4(n0));
  Pull_Resistor pull_resistor_1 (.node(n3));

  // Other names for the same wires on the sheet: n6 = out2; n7 = out1; n8 = out0

  // Notes on the sheet:
  //   xor_1 drives only 0 and floats otherwise
endmodule

module tty_harness (
  output p_in0,
  output p_out0,
  output p_in1,
  output p_out1,
  output p_in2,
  output p_out2,
  output halt
);

  Clock #(.lowDuration(8)) clock_1 (.out(halt));
  Clock clock_2 (.out(p_in0));
  Clock #(.highDuration(2), .lowDuration(2)) clock_3 (.out(p_in1));
  Clock #(.highDuration(4), .lowDuration(4)) clock_4 (.out(p_in2));
  main main_1 (.in0(p_in0), .in1(p_in1), .in2(p_in2), .out0(p_out0), .out1(p_out1), .out2(p_out2));
endmodule
