// Logisim project feedback-1005.circ as structural Verilog: 2 circuits, main circuit tty_harness
module main (
  input  in0,
  input  in1,
  input  in2,
  output out0,
  output out1
);

  wire n0, n1, n2, n3, n4, n5, n6, n7;

  ExactlyOne xor_1 (.out(n0), .in0(in2), .in1(n2), .in2(in1), .in3(in1));
  and and_1 (n4, out1, n1);
  or or_1 (out1, in2, n7, ~n2);  // OR_Gate
  or or_2 (n1, n0, in2);
  not not_1 (n5, n7);
  nand nand_1 (out0, ~n7, ~n3);  // NAND_Gate
  and and_2 (n2, in0, in1, in2, ~n1, in1);  // AND_Gate
  xnor xnor_1 (n6, ~n2, n7);  // XNOR_Gate
  xnor xnor_2 (n3, ~n1, n0);  // XNOR_Gate
  xnor even_parity_1 (n7, in2, n2, ~n1);  // Even_Parity

  // Other names for the same wires on the sheet: n8 = out1; n9 = out0

  // Notes on the sheet:
  //   xor_1 drives only 1 and floats otherwise
  //   or_2 drives only 0 and floats otherwise
  //   nand_1 drives only 1 and floats otherwise
  //   and_2 drives only 0 and floats otherwise
  //   xnor_2 drives only 0 and floats otherwise
endmodule

module tty_harness (
  output p_in0,
  output p_out0,
  output p_in1,
  output p_out1,
  output p_in2,
  output halt
);

  Clock #(.lowDuration(8)) clock_1 (.out(halt));
  Clock clock_2 (.out(p_in0));
  Clock #(.highDuration(2), .lowDuration(2)) clock_3 (.out(p_in1));
  Clock #(.highDuration(4), .lowDuration(4)) clock_4 (.out(p_in2));
  main main_1 (.in0(p_in0), .in1(p_in1), .in2(p_in2), .out0(p_out0), .out1(p_out1));
endmodule
