// Logisim project feedback-1006.circ as structural Verilog: 2 circuits, main circuit tty_harness
module main (
  input  in0,
  input  in1,
  input  in2,
  output out0
);

  wire n0, n1, n2, n3, n4;

  xnor even_parity_1 (n0, in2, in0, in0, in1, ~in1);  // Even_Parity
  nor nor_1 (n4, n0, n2, ~n1, n0);  // NOR_Gate
  or or_1 (n1, n0, ~n1, ~n0, n0);  // OR_Gate
  nand nand_1 (out0, in0, n3, ~n1, n4, n3);  // NAND_Gate
  xor xor_1 (n2, in2, n0, ~out0);  // XOR_Gate
  and and_1 (n3, ~n0, in0, ~in1, ~in1);  // AND_Gate

  // Other names for the same wires on the sheet: n5 = out0

  // Notes on the sheet:
  //   even_parity_1 drives only 0 and floats otherwise
  //   or_1 drives only 1 and floats otherwise
  //   nand_1 drives only 1 and floats otherwise
  //   and_1 drives only 0 and floats otherwise
endmodule

module tty_harness (
  output p_in0,
  output p_in1,
  output p_out0,
  output p_in2,
  output halt
);

  Clock #(.lowDuration(8)) clock_1 (.out(halt));
  Clock clock_2 (.out(p_in0));
  Clock #(.highDuration(2), .lowDuration(2)) clock_3 (.out(p_in1));
  Clock #(.highDuration(4), .lowDuration(4)) clock_4 (.out(p_in2));
  main main_1 (.in0(p_in0), .in1(p_in1), .in2(p_in2), .out0(p_out0));
endmodule
