// Logisim project feedback-1007.circ as structural Verilog: 2 circuits, main circuit tty_harness
module main (
  input  in0,
  input  in1,
  input  in2,
  input  in3,
  output out0,
  output out1
);

  wire n0, n1, n2, n3;

  not not_1 (n0, in0);
  and and_1 (out1, ~in3, n1, ~in3);  // AND_Gate
  not not_2 (n1, out1);
  nand nand_1 (out0, in0, n1, n3);
  not not_3 (n2, n0);
  xor odd_parity_1 (n3, in0, ~n1, out1, in1, n2);  // Odd_Parity

  // Other names for the same wires on the sheet: n4 = out1; n5 = out0
endmodule

module tty_harness (
  output p_in0,
  output p_in1,
  output p_out0,
  output p_in2,
  output p_out1,
  output p_in3,
  output halt
);

  Clock #(.lowDuration(16)) clock_1 (.out(halt));
  Clock clock_2 (.out(p_in0));
  Clock #(.highDuration(2), .lowDuration(2)) clock_3 (.out(p_in1));
  Clock #(.highDuration(4), .lowDuration(4)) clock_4 (.out(p_in2));
  Clock #(.highDuration(8), .lowDuration(8)) clock_5 (.out(p_in3));
  main main_1 (.in0(p_in0), .in1(p_in1), .in2(p_in2), .in3(p_in3), .out0(p_out0), .out1(p_out1));
endmodule
