// Logisim project feedback-1008.circ as structural Verilog: 2 circuits, main circuit tty_harness
module main (
  input  in0,
  input  in1,
  input  in2,
  input  in3,
  output out0
);

  wire n0, n1, n2, n3, n4, n5, n6, n7, n8, n9;

  xor odd_parity_1 (n0, in0, n8, in2);
  xor xor_1 (n4, ~n0, out0, n0);  // XOR_Gate
  and and_1 (n8, ~n0, n1, in2, n5, n1);  // AND_Gate
  xor xor_2 (n1, in1, n0, in3, ~n3);  // XOR_Gate
  not not_1 (n5, n0);
  not not_2 (n9, n1);
  nand nand_1 (n2, in2, in2, n9, in3);
  xor xor_3 (n6, n3, ~n2, n2, in3, n3);  // XOR_Gate
  and and_2 (out0, ~in3, n9, ~n5);  // AND_Gate
  buf buffer_1 (n3, in1);
  xor odd_parity_2 (n7, n3, in1, n6, ~n6);  // Odd_Parity

  // Other names for the same wires on the sheet: n10 = out0

  // Notes on the sheet:
  //   odd_parity_1 drives only 0 and floats otherwise
  //   xor_1 drives only 0 and floats otherwise
  //   xor_3 drives only 0 and floats otherwise
  //   odd_parity_2 drives only 1 and floats otherwise
endmodule

module tty_harness (
  output p_in0,
  output p_in1,
  output p_out0,
  output p_in2,
  output p_in3,
  output halt
);

  Clock #(.lowDuration(16)) clock_1 (.out(halt));
  Clock clock_2 (.out(p_in0));
  Clock #(.highDuration(2), .lowDuration(2)) clock_3 (.out(p_in1));
  Clock #(.highDuration(4), .lowDuration(4)) clock_4 (.out(p_in2));
  Clock #(.highDuration(8), .lowDuration(8)) clock_5 (.out(p_in3));
  main main_1 (.in0(p_in0), .in1(p_in1), .in2(p_in2), .in3(p_in3), .out0(p_out0));
endmodule
