// Logisim project feedback-1009.circ as structural Verilog: 2 circuits, main circuit tty_harness
module main (
  input  in0,
  input  in1,
  input  in2,
  input  in3,
  output out0,
  output out1,
  output out2
);

  wire n0, n1, n2, n3, n4, n5, n6;

  nor nor_1 (n0, in2, ~in0, in2, in3);  // NOR_Gate
  buf buffer_1 (n4, n1);
  ExactlyOne xor_1 (.out(out1), .in0(n4), .in1(out2), .in2(n4), .in3(in0), .in4(in0));
  NotExactlyOne xnor_1 (.out(n1), .in0(in1), .in1(in1), .in2(n0), .in3(n4));
  xor xor_2 (n5, n3, ~out0);  // XOR_Gate
  nand nand_1 (out0, ~in3, in3, n4);  // NAND_Gate
  xor xor_3 (n2, in1, n0, in2, n0);
  xor odd_parity_1 (n6, n5, ~in2);  // Odd_Parity
  xor odd_parity_2 (n3, n0, n2);
  or or_1 (out2, ~in2, ~n6, in0, in2, ~n0);  // OR_Gate

  // Other names for the same wires on the sheet: n7 = out2; n8 = out1; n9 = out0

  // Notes on the sheet:
  //   nand_1 drives only 0 and floats otherwise
endmodule

module tty_harness (
  output p_in0,
  output p_out0,
  output p_in1,
  output p_out1,
  output p_in2,
  output p_out2,
  output p_in3,
  output halt
);

  Clock #(.lowDuration(16)) clock_1 (.out(halt));
  Clock clock_2 (.out(p_in0));
  Clock #(.highDuration(2), .lowDuration(2)) clock_3 (.out(p_in1));
  Clock #(.highDuration(4), .lowDuration(4)) clock_4 (.out(p_in2));
  Clock #(.highDuration(8), .lowDuration(8)) clock_5 (.out(p_in3));
  main main_1 (.in0(p_in0), .in1(p_in1), .in2(p_in2), .in3(p_in3), .out0(p_out0), .out1(p_out1), .out2(p_out2));
endmodule
