// Logisim project feedback-1010.circ as structural Verilog: 2 circuits, main circuit tty_harness
module main (
  input  in0,
  input  in1,
  input  in2,
  output out0
);

  wire n0, n1, n2, n3, n4, n5, n6, n7, n8, n9, n10;

  nand nand_1 (n0, in1, n7);
  xor odd_parity_1 (n4, n2, ~n3, in1, n2);  // Odd_Parity
  assign n8 = in0 ? ~n7 : 1'bz;  // Controlled_Inverter controlled_inverter_1
  xor odd_parity_2 (n1, ~n0, n0);  // Odd_Parity
  NotExactlyOne xnor_1 (.out(n5), .in0(n3), .in1(n3), .in2(n1));
  not not_1 (n9, n4);
  nand nand_2 (n2, ~n1, ~n0, ~n1);  // NAND_Gate
  nand nand_3 (n6, in0, ~n0, n2, n7);  // NAND_Gate
  buf buffer_1 (n10, n6);
  not not_2 (n3, in0);
  xnor even_parity_1 (n7, n4, in1, n0, in2, ~in0);  // Even_Parity
  and and_1 (out0, n8, n5);

  // Other names for the same wires on the sheet: n11 = out0

  // Notes on the sheet:
  //   nand_1 drives only 1 and floats otherwise
endmodule

module tty_harness (
  output p_in0,
  output p_in1,
  output p_out0,
  output p_in2,
  output halt
);

  Clock #(.lowDuration(8)) clock_1 (.out(halt));
  Clock clock_2 (.out(p_in0));
  Clock #(.highDuration(2), .lowDuration(2)) clock_3 (.out(p_in1));
  Clock #(.highDuration(4), .lowDuration(4)) clock_4 (.out(p_in2));
  main main_1 (.in0(p_in0), .in1(p_in1), .in2(p_in2), .out0(p_out0));
endmodule
