// Logisim project feedback-1011.circ as structural Verilog: 2 circuits, main circuit tty_harness
module main (
  input  in0,
  input  in1,
  input  in2,
  input  in3,
  output out0,
  output out1
);

  wire n0, n1, n2, n3, n4, n5, n6, n7;

  xor odd_parity_1 (n0, ~in1, ~in0, in1);  // Odd_Parity
  xor xor_1 (n4, in2, ~n2, n1, n1, in2);  // XOR_Gate
  assign out1 = n6 ? in3 : 1'bz;  // Controlled_Buffer controlled_buffer_1
  xnor even_parity_1 (n1, in3, ~in0, in2, ~in1);  // Even_Parity
  buf buffer_1 (n5, in1);
  nor nor_1 (out0, ~out0, n3, in2, ~in3, n7);  // NOR_Gate
  xor odd_parity_2 (n2, n0, n0, out0, n1);
  not not_1 (n6, n0);
  not not_2 (n3, n2);
  assign n7 = n3 ? in0 : 1'bz;  // Controlled_Buffer controlled_buffer_2
  Pull_Resistor #(.pull("X")) pull_resistor_1 (.node(n7));

  // Other names for the same wires on the sheet: n8 = out1; n9 = out0

  // Notes on the sheet:
  //   even_parity_1 drives only 1 and floats otherwise
endmodule

module tty_harness (
  output p_in0,
  output p_in1,
  output p_out0,
  output p_in2,
  output p_out1,
  output p_in3,
  output halt
);

  Clock #(.lowDuration(16)) clock_1 (.out(halt));
  Clock clock_2 (.out(p_in0));
  Clock #(.highDuration(2), .lowDuration(2)) clock_3 (.out(p_in1));
  Clock #(.highDuration(4), .lowDuration(4)) clock_4 (.out(p_in2));
  Clock #(.highDuration(8), .lowDuration(8)) clock_5 (.out(p_in3));
  main main_1 (.in0(p_in0), .in1(p_in1), .in2(p_in2), .in3(p_in3), .out0(p_out0), .out1(p_out1));
endmodule
