// Logisim project feedback-1012.circ as structural Verilog: 2 circuits, main circuit tty_harness
module main (
  input  in0,
  input  in1,
  output out0,
  output out1,
  output out2
);

  wire n0, n1, n2, n3, n4, n5;

  NotExactlyOne xnor_1 (.out(n0), .in0(out0), .in1(out2), .in2(in1), .in3(in0), .in4(in1));
  xor odd_parity_1 (n4, n5, in1, n2, in0);
  and and_1 (out0, n3, n5);
  not not_1 (n1, in0);
  xnor even_parity_1 (n5, in0, out1);
  and and_2 (n2, in1, n5, n0, n0, in1);
  nand nand_1 (out2, n5, n3, ~n1, ~n4);  // NAND_Gate
  and and_3 (n3, in1, n2, in1, n0, n1);
  not not_2 (out1, out2);

  // Other names for the same wires on the sheet: n6 = out2; n7 = out1; n8 = out0

  // Notes on the sheet:
  //   xnor_1 drives only 1 and floats otherwise
  //   and_1 drives only 1 and floats otherwise
endmodule

module tty_harness (
  output p_in0,
  output p_out0,
  output p_in1,
  output p_out1,
  output p_out2,
  output halt
);

  Clock #(.lowDuration(4)) clock_1 (.out(halt));
  Clock clock_2 (.out(p_in0));
  Clock #(.highDuration(2), .lowDuration(2)) clock_3 (.out(p_in1));
  main main_1 (.in0(p_in0), .in1(p_in1), .out0(p_out0), .out1(p_out1), .out2(p_out2));
endmodule
