// Logisim project feedback-1014.circ as structural Verilog: 2 circuits, main circuit tty_harness
module main (
  input  in0,
  input  in1,
  output out0,
  output out1,
  output out2
);

  wire n0, n1, n2, n3, n4, n5, n6, n7, n8;

  xnor even_parity_1 (n0, in1, in1, in1, ~n1);  // Even_Parity
  and and_1 (n4, n3, in0, ~in1, ~in1);  // AND_Gate
  buf buffer_1 (n8, n4);
  xor odd_parity_1 (n1, ~n0, in0, in1);  // Odd_Parity
  assign n5 = n3 ? n4 : 1'bz;  // Controlled_Buffer controlled_buffer_1
  and and_2 (out2, n4, n4, n2);
  nor nor_1 (n2, in0, n0, in1);
  not not_1 (n6, n3);
  xor odd_parity_2 (out1, in1, ~n6, n0);  // Odd_Parity
  nor nor_2 (n3, n0, in0, n0, in0, n0);
  nor nor_3 (n7, ~in1, n0, n6, n6, n4);  // NOR_Gate
  xnor even_parity_2 (out0, n4, n5);

  // Other names for the same wires on the sheet: n9 = out2; n10 = out1; n11 = out0

  // Notes on the sheet:
  //   odd_parity_2 drives only 1 and floats otherwise
  //   nor_3 drives only 1 and floats otherwise
endmodule

module tty_harness (
  output p_in0,
  output p_out0,
  output p_in1,
  output p_out1,
  output p_out2,
  output halt
);

  Clock #(.lowDuration(4)) clock_1 (.out(halt));
  Clock clock_2 (.out(p_in0));
  Clock #(.highDuration(2), .lowDuration(2)) clock_3 (.out(p_in1));
  main main_1 (.in0(p_in0), .in1(p_in1), .out0(p_out0), .out1(p_out1), .out2(p_out2));
endmodule
