// Logisim project feedback-1015.circ as structural Verilog: 2 circuits, main circuit tty_harness
module main (
  input  in0,
  input  in1,
  output out0,
  output out1
);

  wire n0, n1, n2, n3, n4, n5, n6, n7, n8, n9, n10;

  xor odd_parity_1 (n0, in0, in1, ~in1);  // Odd_Parity
  or or_1 (n4, n1, n2, in1);
  xnor even_parity_1 (n8, n4, n1);
  nor nor_1 (out0, n4, n9);
  and and_1 (n1, n0, in0, in0, n0);
  or or_2 (n5, n4, n3, ~in1, n4, n1);  // OR_Gate
  not not_1 (n9, n7);
  nand nand_1 (n2, in1, in0, in1);
  not not_2 (n6, in1);
  xnor even_parity_2 (n10, n9, n6, ~n6, n1);  // Even_Parity
  nand nand_2 (n3, in1, n1, in1, ~in0);  // NAND_Gate
  buf buffer_1 (n7, n7);
  or or_3 (out1, ~n4, ~n10);  // OR_Gate

  // Other names for the same wires on the sheet: n11 = out1; n12 = out0
endmodule

module tty_harness (
  output p_in0,
  output p_out0,
  output p_in1,
  output p_out1,
  output halt
);

  Clock #(.lowDuration(4)) clock_1 (.out(halt));
  Clock clock_2 (.out(p_in0));
  Clock #(.highDuration(2), .lowDuration(2)) clock_3 (.out(p_in1));
  main main_1 (.in0(p_in0), .in1(p_in1), .out0(p_out0), .out1(p_out1));
endmodule
