// Logisim project feedback-1016.circ as structural Verilog: 2 circuits, main circuit tty_harness
module main (
  input  in0,
  input  in1,
  input  in2,
  input  in3,
  output out0,
  output out1,
  output out2
);

  wire n0, n1, n2, n3, n4, n5, n6, n7, n8, n9;

  nand nand_1 (n0, in0, in0, ~in2);  // NAND_Gate
  nand nand_2 (n4, in3, in2, ~n2, in2, out1);  // NAND_Gate
  not not_1 (n8, n2);
  and and_1 (out0, ~n9, n3);  // AND_Gate
  xnor even_parity_1 (n1, in0, in2, in2, ~in3);  // Even_Parity
  NotExactlyOne xnor_1 (.out(n5), .in0(n3), .in1(in3), .in2(n1), .in3(n2), .in4(n0));
  NotExactlyOne xnor_2 (.out(n9), .in0(n5), .in1(n4), .in2(n8), .in3(n7), .in4(in2));
  xor odd_parity_1 (n2, in3, n3, in2, ~in3);  // Odd_Parity
  and and_2 (n6, n5, n2, in2, in0, n2);
  nand nand_3 (out2, ~in0, n8);  // NAND_Gate
  xor odd_parity_2 (n3, ~n2, n0, ~n2, ~n0);  // Odd_Parity
  buf buffer_1 (n7, n7);
  xor odd_parity_3 (out1, n4, in2, in3, n9);

  // Other names for the same wires on the sheet: n10 = out2; n11 = out1; n12 = out0

  // Notes on the sheet:
  //   xnor_1 drives only 1 and floats otherwise
  //   and_2 drives only 1 and floats otherwise
  //   nand_3 drives only 1 and floats otherwise
endmodule

module tty_harness (
  output p_in0,
  output p_out0,
  output p_in1,
  output p_out1,
  output p_in2,
  output p_out2,
  output p_in3,
  output halt
);

  Clock #(.lowDuration(16)) clock_1 (.out(halt));
  Clock clock_2 (.out(p_in0));
  Clock #(.highDuration(2), .lowDuration(2)) clock_3 (.out(p_in1));
  Clock #(.highDuration(4), .lowDuration(4)) clock_4 (.out(p_in2));
  Clock #(.highDuration(8), .lowDuration(8)) clock_5 (.out(p_in3));
  main main_1 (.in0(p_in0), .in1(p_in1), .in2(p_in2), .in3(p_in3), .out0(p_out0), .out1(p_out1), .out2(p_out2));
endmodule
