// Logisim project feedback-1017.circ as structural Verilog: 2 circuits, main circuit tty_harness
module main (
  input  in0,
  input  in1,
  output out0
);

  wire n0, n1, n2, n3;

  not not_1 (n0, in1);
  xnor even_parity_1 (out0, in0, in1, n0);
  xnor even_parity_2 (n1, n0, in1, in0);
  nor nor_1 (n2, in1, in1, in0, ~n1);  // NOR_Gate
  and and_1 (n3, ~n0, n2);  // AND_Gate

  // Other names for the same wires on the sheet: n4 = out0

  // Notes on the sheet:
  //   even_parity_2 drives only 1 and floats otherwise
  //   nor_1 drives only 0 and floats otherwise
  //   and_1 drives only 1 and floats otherwise
endmodule

module tty_harness (
  output p_in0,
  output p_out0,
  output p_in1,
  output halt
);

  Clock #(.lowDuration(4)) clock_1 (.out(halt));
  Clock clock_2 (.out(p_in0));
  Clock #(.highDuration(2), .lowDuration(2)) clock_3 (.out(p_in1));
  main main_1 (.in0(p_in0), .in1(p_in1), .out0(p_out0));
endmodule
