// Logisim project feedback-1018.circ as structural Verilog: 2 circuits, main circuit tty_harness
module main (
  input  in0,
  input  in1,
  input  in2,
  input  in3,
  output out0,
  output out1
);

  wire n0, n1, n2, n3, n4, n5, n6, n7, n8, n9;

  ExactlyOne xor_1 (.out(n0), .in0(in3), .in1(in3), .in2(in3), .in3(in3), .in4(in1));
  nor nor_1 (n4, n3, in0, n3);
  buf buffer_1 (n8, in1);
  xor xor_2 (n1, in3, in0, n2, in1);
  nand nand_1 (n5, n3, n4, n2, ~n3, n2);  // NAND_Gate
  nand nand_2 (n9, ~in0, ~n8, n7, ~in2, ~in3);  // NAND_Gate
  or or_1 (n2, out0, in3, n6, ~in0, ~in2);  // OR_Gate
  xor xor_3 (n6, ~n2, in0, in0, ~n2, n3);  // XOR_Gate
  and and_1 (out1, ~n3, in3, n8, in1, n7);  // AND_Gate
  or or_2 (n3, n3, ~n0, in3, ~n0);  // OR_Gate
  xnor xnor_1 (n7, n0, ~out0);  // XNOR_Gate
  nand nand_3 (out0, n6, out1, n0);

  // Other names for the same wires on the sheet: n10 = out1; n11 = out0

  // Notes on the sheet:
  //   nand_2 drives only 1 and floats otherwise
  //   or_1 drives only 1 and floats otherwise
  //   and_1 drives only 1 and floats otherwise
endmodule

module tty_harness (
  output p_in0,
  output p_in1,
  output p_out0,
  output p_in2,
  output p_out1,
  output p_in3,
  output halt
);

  Clock #(.lowDuration(16)) clock_1 (.out(halt));
  Clock clock_2 (.out(p_in0));
  Clock #(.highDuration(2), .lowDuration(2)) clock_3 (.out(p_in1));
  Clock #(.highDuration(4), .lowDuration(4)) clock_4 (.out(p_in2));
  Clock #(.highDuration(8), .lowDuration(8)) clock_5 (.out(p_in3));
  main main_1 (.in0(p_in0), .in1(p_in1), .in2(p_in2), .in3(p_in3), .out0(p_out0), .out1(p_out1));
endmodule
