// Logisim project feedback-1019.circ as structural Verilog: 2 circuits, main circuit tty_harness
module main (
  input  in0,
  input  in1,
  output out0,
  output out1,
  output out2
);

  wire n0, n1, n2, n3, n4, n5, n6, n7, n8, n9;

  nand nand_1 (n0, in0, n1);
  assign n4 = n0 ? n3 : 1'bz;  // Controlled_Buffer controlled_buffer_1
  nand nand_2 (n8, in0, n0, n1, n3);
  not not_1 (out0, n6);
  not not_2 (n1, n0);
  not not_3 (n5, in0);
  nand nand_3 (n9, n2, in0, ~n8);  // NAND_Gate
  and and_1 (n2, in1, n0, in0);
  xnor xnor_1 (n6, n1, n4);
  nand nand_4 (out2, n4, ~n3);  // NAND_Gate
  and and_2 (n3, ~n6, n0, ~in0, n1);  // AND_Gate
  xor odd_parity_1 (n7, n0, n2);
  not not_4 (out1, n1);

  // Other names for the same wires on the sheet: n10 = out2; n11 = out1; n12 = out0

  // Notes on the sheet:
  //   nand_1 drives only 1 and floats otherwise
endmodule

module tty_harness (
  output p_in0,
  output p_out0,
  output p_in1,
  output p_out1,
  output p_out2,
  output halt
);

  Clock #(.lowDuration(4)) clock_1 (.out(halt));
  Clock clock_2 (.out(p_in0));
  Clock #(.highDuration(2), .lowDuration(2)) clock_3 (.out(p_in1));
  main main_1 (.in0(p_in0), .in1(p_in1), .out0(p_out0), .out1(p_out1), .out2(p_out2));
endmodule
