// Logisim project feedback-1020.circ as structural Verilog: 2 circuits, main circuit tty_harness
module main (
  input  in0,
  input  in1,
  output out0,
  output out1
);

  wire n0, n1, n2, n3, n4, n5, n6, n7, n8, n9, n10;

  and and_1 (n0, in1, in1);
  nor nor_1 (n4, n3, in1, n0, ~in1, in1);  // NOR_Gate
  nand nand_1 (n8, n8, in0, n1, in0, ~n5);  // NAND_Gate
  ExactlyOne xor_1 (.out(out0), .in0(n1), .in1(n8), .in2(n7));
  nand nand_2 (n1, ~n0, ~n5, ~n0, n0);  // NAND_Gate
  buf buffer_1 (n5, n1);
  xor xor_2 (n9, out0, ~n6, n6);  // XOR_Gate
  ExactlyOne xor_3 (.out(n2), .in0(n0), .in1(n1), .in2(n1), .in3(n1));
  nor nor_2 (n6, n3, out0, in1, ~n4, ~n10);  // NOR_Gate
  nand nand_3 (n10, in0, in1);
  or or_1 (n3, n0, in0, n1, ~in0, in1);  // OR_Gate
  assign n7 = n0 ? n2 : 1'bz;  // Controlled_Buffer controlled_buffer_1
  nor nor_3 (out1, ~n6, n5);  // NOR_Gate
  Pull_Resistor pull_resistor_1 (.node(out0));

  // Other names for the same wires on the sheet: n11 = out1; n12 = out0

  // Notes on the sheet:
  //   and_1 drives only 1 and floats otherwise
  //   xor_2 drives only 1 and floats otherwise
  //   nor_2 drives only 0 and floats otherwise
endmodule

module tty_harness (
  output p_in0,
  output p_out0,
  output p_in1,
  output p_out1,
  output halt
);

  Clock #(.lowDuration(4)) clock_1 (.out(halt));
  Clock clock_2 (.out(p_in0));
  Clock #(.highDuration(2), .lowDuration(2)) clock_3 (.out(p_in1));
  main main_1 (.in0(p_in0), .in1(p_in1), .out0(p_out0), .out1(p_out1));
endmodule
