// Logisim project fixture-full-adder.circ as structural Verilog: 3 circuits, main circuit tty_harness
module main (
  input  A,
  input  B,
  input  Cin,
  output Sum,
  output Cout
);

  wire half_1_c, half_1_s, half_2_c;

  half half_1 (.A(A), .B(B), .S(half_1_s), .C(half_1_c));
  half half_2 (.A(half_1_s), .B(Cin), .S(Sum), .C(half_2_c));
  or or_1 (Cout, half_2_c, half_1_c);
endmodule

module half (
  input  A,
  input  B,
  output S,
  output C
);

  xor xor_1 (S, A, B);
  and and_1 (C, A, B);
endmodule

module tty_harness (
  output p_A,
  output p_Sum,
  output p_B,
  output p_Cout,
  output p_Cin,
  output halt
);

  Clock #(.lowDuration(8)) clock_1 (.out(halt));
  Clock clock_2 (.out(p_A));
  Clock #(.highDuration(2), .lowDuration(2)) clock_3 (.out(p_B));
  Clock #(.highDuration(4), .lowDuration(4)) clock_4 (.out(p_Cin));
  main main_1 (.A(p_A), .B(p_B), .Cin(p_Cin), .Sum(p_Sum), .Cout(p_Cout));
endmodule
