// Logisim project fixture-half-adder.circ as structural Verilog: 2 circuits, main circuit tty_harness
module main (
  input  A,
  input  B,
  output S,
  output C
);

  xor xor_1 (S, A, B);
  and and_1 (C, A, B);
endmodule

module tty_harness (
  output p_A,
  output p_S,
  output p_B,
  output p_C,
  output halt
);

  Clock #(.lowDuration(4)) clock_1 (.out(halt));
  Clock clock_2 (.out(p_A));
  Clock #(.highDuration(2), .lowDuration(2)) clock_3 (.out(p_B));
  main main_1 (.A(p_A), .B(p_B), .S(p_S), .C(p_C));
endmodule
