// Logisim project random-001.circ as structural Verilog: 2 circuits, main circuit tty_harness
module main (
  input  in0,
  input  in1,
  input  in2,
  output out0
);

  wire n0, n1, n2;

  xnor even_parity_1 (n0, in0, in1, in0, in0, in1);
  not not_1 (n1, n0);
  or or_1 (n2, in1, n0);
  xor odd_parity_1 (out0, in1, n1);
  Pull_Resistor #(.pull(1)) pull_resistor_1 (.node(n1));

  // Other names for the same wires on the sheet: n3 = out0
endmodule

module tty_harness (
  output p_in0,
  output p_in1,
  output p_out0,
  output p_in2,
  output halt
);

  Clock #(.lowDuration(8)) clock_1 (.out(halt));
  Clock clock_2 (.out(p_in0));
  Clock #(.highDuration(2), .lowDuration(2)) clock_3 (.out(p_in1));
  Clock #(.highDuration(4), .lowDuration(4)) clock_4 (.out(p_in2));
  main main_1 (.in0(p_in0), .in1(p_in1), .in2(p_in2), .out0(p_out0));
endmodule
