// Logisim project random-003.circ as structural Verilog: 2 circuits, main circuit tty_harness
module main (
  input  in0,
  input  in1,
  input  in2,
  input  in3,
  output out0
);

  wire n0, n1, n2;

  and and_1 (n0, ~in2, in1, in3, ~in3, ~in1);  // AND_Gate
  nand nand_1 (n1, n0, ~in3, in2, in3);  // NAND_Gate
  buf buffer_1 (n2, in2);
  and and_2 (out0, n1, n0);

  // Other names for the same wires on the sheet: n3 = out0
endmodule

module tty_harness (
  output p_in0,
  output p_in1,
  output p_out0,
  output p_in2,
  output p_in3,
  output halt
);

  Clock #(.lowDuration(16)) clock_1 (.out(halt));
  Clock clock_2 (.out(p_in0));
  Clock #(.highDuration(2), .lowDuration(2)) clock_3 (.out(p_in1));
  Clock #(.highDuration(4), .lowDuration(4)) clock_4 (.out(p_in2));
  Clock #(.highDuration(8), .lowDuration(8)) clock_5 (.out(p_in3));
  main main_1 (.in0(p_in0), .in1(p_in1), .in2(p_in2), .in3(p_in3), .out0(p_out0));
endmodule
