// Logisim project random-004.circ as structural Verilog: 2 circuits, main circuit tty_harness
module main (
  input  in0,
  input  in1,
  input  in2,
  input  in3,
  output out0,
  output out1,
  output out2
);

  wire n0, n1, n2, n3;

  assign n0 = in2 ? in0 : 1'bz;  // Controlled_Buffer controlled_buffer_1
  xor odd_parity_1 (out2, in0, n0);
  not not_1 (n1, in3);
  xor xor_1 (out1, n1, ~n0);  // XOR_Gate
  xor odd_parity_2 (n2, in2, n0, n1);
  not not_2 (out0, out1);
  nor nor_1 (n3, in3, in0, in3);
  Pull_Resistor #(.pull("X")) pull_resistor_1 (.node(n3));

  // Other names for the same wires on the sheet: n4 = out2; n5 = out1; n6 = out0
endmodule

module tty_harness (
  output p_in0,
  output p_out0,
  output p_in1,
  output p_out1,
  output p_in2,
  output p_out2,
  output p_in3,
  output halt
);

  Clock #(.lowDuration(16)) clock_1 (.out(halt));
  Clock clock_2 (.out(p_in0));
  Clock #(.highDuration(2), .lowDuration(2)) clock_3 (.out(p_in1));
  Clock #(.highDuration(4), .lowDuration(4)) clock_4 (.out(p_in2));
  Clock #(.highDuration(8), .lowDuration(8)) clock_5 (.out(p_in3));
  main main_1 (.in0(p_in0), .in1(p_in1), .in2(p_in2), .in3(p_in3), .out0(p_out0), .out1(p_out1), .out2(p_out2));
endmodule
