// Logisim project random-005.circ as structural Verilog: 2 circuits, main circuit tty_harness
module main (
  input  in0,
  input  in1,
  input  in2,
  input  in3,
  output out0
);

  wire n0, n1, n2, n3, n4, n5, n6, n7, n8, n9;

  assign n0 = in2 ? ~in0 : 1'bz;  // Controlled_Inverter controlled_inverter_1
  or or_1 (n4, n0, in2, n2, ~n0, in0);  // OR_Gate
  not not_1 (n8, n5);
  nor nor_1 (n1, n0, in1, ~in3, in3, in1);  // NOR_Gate
  nand nand_1 (n5, ~n4, in0, in3);  // NAND_Gate
  nor nor_2 (n9, n5, in1);
  not not_2 (n2, in1);
  nand nand_2 (n6, n3, n5, in2, ~n1);  // NAND_Gate
  xnor even_parity_1 (out0, n0, ~n6, in0, n7);  // Even_Parity
  and and_1 (n3, ~in2, n2, in1);  // AND_Gate
  xor odd_parity_1 (n7, in1, ~in2, n4, in1);  // Odd_Parity
  Pull_Resistor #(.pull("X")) pull_resistor_1 (.node(n5));

  // Other names for the same wires on the sheet: n10 = out0

  // Notes on the sheet:
  //   nand_2 drives only 1 and floats otherwise
endmodule

module tty_harness (
  output p_in0,
  output p_in1,
  output p_out0,
  output p_in2,
  output p_in3,
  output halt
);

  Clock #(.lowDuration(16)) clock_1 (.out(halt));
  Clock clock_2 (.out(p_in0));
  Clock #(.highDuration(2), .lowDuration(2)) clock_3 (.out(p_in1));
  Clock #(.highDuration(4), .lowDuration(4)) clock_4 (.out(p_in2));
  Clock #(.highDuration(8), .lowDuration(8)) clock_5 (.out(p_in3));
  main main_1 (.in0(p_in0), .in1(p_in1), .in2(p_in2), .in3(p_in3), .out0(p_out0));
endmodule
