// Logisim project random-007.circ as structural Verilog: 2 circuits, main circuit tty_harness
module main (
  input  in0,
  input  in1,
  output out0,
  output out1,
  output out2
);

  wire n0;

  NotExactlyOne xnor_1 (.out(n0), .in0(in1), .in1(in1), .in2(in0), .in3(in0));
  ExactlyOne xor_1 (.out(out2), .in0(in0), .in1(in1), .in2(n0));
  not not_1 (out1, n0);
  xnor xnor_2 (out0, ~in0, ~out2, in1, n0, ~n0);  // XNOR_Gate

  // Other names for the same wires on the sheet: n1 = out2; n2 = out1; n3 = out0
endmodule

module tty_harness (
  output p_in0,
  output p_out0,
  output p_in1,
  output p_out1,
  output p_out2,
  output halt
);

  Clock #(.lowDuration(4)) clock_1 (.out(halt));
  Clock clock_2 (.out(p_in0));
  Clock #(.highDuration(2), .lowDuration(2)) clock_3 (.out(p_in1));
  main main_1 (.in0(p_in0), .in1(p_in1), .out0(p_out0), .out1(p_out1), .out2(p_out2));
endmodule
