// Logisim project random-008.circ as structural Verilog: 2 circuits, main circuit tty_harness
module main (
  input  in0,
  input  in1,
  output out0
);

  wire n0, n1, n2, n3, n4, n5, n6, n7, n8;

  xnor xnor_1 (n0, in1, ~in0, in0, ~in1);  // XNOR_Gate
  or or_1 (n4, n3, ~n3, in1, ~in0, ~n3);  // OR_Gate
  nand nand_1 (n8, n5, n5, ~in1, ~n3, n2);  // NAND_Gate
  and and_1 (n1, n0, in0);
  xor odd_parity_1 (n5, n3, n0, ~in1);  // Odd_Parity
  nand nand_2 (out0, ~n3, in1, ~in0);  // NAND_Gate
  nand nand_3 (n2, ~n1, n0, n0, n1);  // NAND_Gate
  xnor even_parity_1 (n6, n0, n5, ~n0, n2, n0);  // Even_Parity
  nand nand_4 (n3, in0, n0, n1);
  xor xor_1 (n7, n6, in0, in0);

  // Other names for the same wires on the sheet: n9 = out0

  // Notes on the sheet:
  //   odd_parity_1 drives only 0 and floats otherwise
endmodule

module tty_harness (
  output p_in0,
  output p_out0,
  output p_in1,
  output halt
);

  Clock #(.lowDuration(4)) clock_1 (.out(halt));
  Clock clock_2 (.out(p_in0));
  Clock #(.highDuration(2), .lowDuration(2)) clock_3 (.out(p_in1));
  main main_1 (.in0(p_in0), .in1(p_in1), .out0(p_out0));
endmodule
