// Logisim project random-009.circ as structural Verilog: 2 circuits, main circuit tty_harness
module main (
  input  in0,
  input  in1,
  output out0,
  output out1,
  output out2
);

  wire n0, n1, n2, n3, n4, n5, n6, n7, n8;

  buf buffer_1 (n0, in1);
  nand nand_1 (n4, ~n2, n1, n1, n1);  // NAND_Gate
  xor odd_parity_1 (n8, n3, n3, ~n1);  // Odd_Parity
  NotExactlyOne xnor_1 (.out(n1), .in0(n0), .in1(in0), .in2(n0));
  nor nor_1 (n5, n2, n4);
  nand nand_2 (out2, n7, in0, n0);
  nand nand_3 (n2, in1, in0, ~n1, in0);  // NAND_Gate
  and and_1 (n6, n4, in1, n3, n5);
  xnor xnor_2 (out1, ~in1, n0);  // XNOR_Gate
  nor nor_2 (n3, ~n0, ~in1);  // NOR_Gate
  buf buffer_2 (n7, n6);
  not not_1 (out0, n0);
  Pull_Resistor pull_resistor_1 (.node(out2));

  // Other names for the same wires on the sheet: n9 = out2; n10 = out1; n11 = out0
endmodule

module tty_harness (
  output p_in0,
  output p_out0,
  output p_in1,
  output p_out1,
  output p_out2,
  output halt
);

  Clock #(.lowDuration(4)) clock_1 (.out(halt));
  Clock clock_2 (.out(p_in0));
  Clock #(.highDuration(2), .lowDuration(2)) clock_3 (.out(p_in1));
  main main_1 (.in0(p_in0), .in1(p_in1), .out0(p_out0), .out1(p_out1), .out2(p_out2));
endmodule
