// Logisim project random-010.circ as structural Verilog: 2 circuits, main circuit tty_harness
module main (
  input  in0,
  input  in1,
  input  in2,
  output out0,
  output out1
);

  wire n0, n1, n2, n3, n4, n5, n6, n7, n8, n9, n10;

  xor odd_parity_1 (n0, ~in2, ~in0, in1);  // Odd_Parity
  not not_1 (n4, n2);
  buf buffer_1 (n8, n6);
  nand nand_1 (out0, n3, n7, n1, n8);
  nor nor_1 (n1, in1, ~in1, in1, in1, in2);  // NOR_Gate
  nor nor_2 (n5, in1, ~n1, n4, n1);  // NOR_Gate
  xor odd_parity_2 (n9, n0, n5, n7, ~n7, ~n7);  // Odd_Parity
  not not_2 (n2, in0);
  not not_3 (n6, n3);
  or or_1 (n10, n2, n0, n0);
  not not_4 (n3, in0);
  xor odd_parity_3 (n7, in0, ~n5, n1, ~n1);  // Odd_Parity
  nand nand_2 (out1, n9, n3, n0, n0, in0);

  // Other names for the same wires on the sheet: n11 = out1; n12 = out0

  // Notes on the sheet:
  //   nor_2 drives only 0 and floats otherwise
  //   odd_parity_2 drives only 0 and floats otherwise
endmodule

module tty_harness (
  output p_in0,
  output p_out0,
  output p_in1,
  output p_out1,
  output p_in2,
  output halt
);

  Clock #(.lowDuration(8)) clock_1 (.out(halt));
  Clock clock_2 (.out(p_in0));
  Clock #(.highDuration(2), .lowDuration(2)) clock_3 (.out(p_in1));
  Clock #(.highDuration(4), .lowDuration(4)) clock_4 (.out(p_in2));
  main main_1 (.in0(p_in0), .in1(p_in1), .in2(p_in2), .out0(p_out0), .out1(p_out1));
endmodule
