// Logisim project random-011.circ as structural Verilog: 2 circuits, main circuit tty_harness
module main (
  input  in0,
  input  in1,
  input  in2,
  output out0,
  output out1
);

  wire n0, n1, n2, n3, n4, n5, n6;

  ExactlyOne xor_1 (.out(n0), .in0(in2), .in1(in2), .in2(in0), .in3(in0), .in4(in0));
  nor nor_1 (n4, n0, ~n1, n3, ~in2);  // NOR_Gate
  buf buffer_1 (out0, in0);
  nor nor_2 (n1, n0, in1, in2, in1);
  nand nand_1 (n5, n1, in2);
  not not_1 (n2, n1);
  or or_1 (n6, ~n0, n5);  // OR_Gate
  or or_2 (n3, n1, in2, ~in0, in0);  // OR_Gate
  xnor xnor_1 (out1, n5, n0, ~n1);  // XNOR_Gate

  // Other names for the same wires on the sheet: n7 = out1; n8 = out0
endmodule

module tty_harness (
  output p_in0,
  output p_out0,
  output p_in1,
  output p_out1,
  output p_in2,
  output halt
);

  Clock #(.lowDuration(8)) clock_1 (.out(halt));
  Clock clock_2 (.out(p_in0));
  Clock #(.highDuration(2), .lowDuration(2)) clock_3 (.out(p_in1));
  Clock #(.highDuration(4), .lowDuration(4)) clock_4 (.out(p_in2));
  main main_1 (.in0(p_in0), .in1(p_in1), .in2(p_in2), .out0(p_out0), .out1(p_out1));
endmodule
