// Logisim project random-013.circ as structural Verilog: 2 circuits, main circuit tty_harness
module main (
  input  in0,
  input  in1,
  input  in2,
  output out0,
  output out1,
  output out2
);

  wire n0, n1, n2, n3;

  not not_1 (n0, in0);
  xnor even_parity_1 (out2, in0, n0, in0);
  not not_2 (n1, in1);
  assign out1 = in1 ? in0 : 1'bz;  // Controlled_Buffer controlled_buffer_1
  xor odd_parity_1 (n2, ~n0, in0, n0, in2);  // Odd_Parity
  xnor even_parity_2 (out0, ~in2, ~out1);  // Even_Parity
  nand nand_1 (n3, ~in0, in0);  // NAND_Gate

  // Other names for the same wires on the sheet: n4 = out2; n5 = out1; n6 = out0
endmodule

module tty_harness (
  output p_in0,
  output p_out0,
  output p_in1,
  output p_out1,
  output p_in2,
  output p_out2,
  output halt
);

  Clock #(.lowDuration(8)) clock_1 (.out(halt));
  Clock clock_2 (.out(p_in0));
  Clock #(.highDuration(2), .lowDuration(2)) clock_3 (.out(p_in1));
  Clock #(.highDuration(4), .lowDuration(4)) clock_4 (.out(p_in2));
  main main_1 (.in0(p_in0), .in1(p_in1), .in2(p_in2), .out0(p_out0), .out1(p_out1), .out2(p_out2));
endmodule
