// Logisim project random-014.circ as structural Verilog: 2 circuits, main circuit tty_harness
module main (
  input  in0,
  input  in1,
  input  in2,
  output out0,
  output out1
);

  wire n0, n1, n2, n3, n4, n5;

  nand nand_1 (n0, ~in2, in1);  // NAND_Gate
  nand nand_2 (n4, ~n1, ~in2);  // NAND_Gate
  not not_1 (n1, in0);
  not not_2 (n5, n1);
  buf buffer_1 (n2, in1);
  xor odd_parity_1 (out1, n4, ~in1, n0, in0);  // Odd_Parity
  xnor even_parity_1 (n3, n2, n0);
  and and_1 (out0, n5, n0, n2);

  // Other names for the same wires on the sheet: n6 = out1; n7 = out0

  // Notes on the sheet:
  //   and_1 drives only 0 and floats otherwise
endmodule

module tty_harness (
  output p_in0,
  output p_out0,
  output p_in1,
  output p_out1,
  output p_in2,
  output halt
);

  Clock #(.lowDuration(8)) clock_1 (.out(halt));
  Clock clock_2 (.out(p_in0));
  Clock #(.highDuration(2), .lowDuration(2)) clock_3 (.out(p_in1));
  Clock #(.highDuration(4), .lowDuration(4)) clock_4 (.out(p_in2));
  main main_1 (.in0(p_in0), .in1(p_in1), .in2(p_in2), .out0(p_out0), .out1(p_out1));
endmodule
