// Logisim project random-015.circ as structural Verilog: 2 circuits, main circuit tty_harness
module main (
  input  in0,
  input  in1,
  output out0
);

  wire n0, n1, n2, n3, n4, n5, n6;

  nor nor_1 (n0, in0, ~in0);  // NOR_Gate
  ExactlyOne xor_1 (.out(n4), .in0(n1), .in1(in1), .in2(n2), .in3(in1), .in4(n3));
  and and_1 (n1, ~in1, in0, in1, in0);  // AND_Gate
  xnor xnor_1 (n5, n3, n4, n1, in1);
  or or_1 (n2, n0, in0, in0, ~in0, n1);  // OR_Gate
  and and_2 (n6, in1, in0, ~in0, ~in0);  // AND_Gate
  ExactlyOne xor_2 (.out(n3), .in0(in1), .in1(n2), .in2(n1), .in3(in1));
  xnor even_parity_1 (out0, ~n0, n0, n2);  // Even_Parity

  // Other names for the same wires on the sheet: n7 = out0

  // Notes on the sheet:
  //   and_2 drives only 0 and floats otherwise
  //   even_parity_1 drives only 1 and floats otherwise
endmodule

module tty_harness (
  output p_in0,
  output p_out0,
  output p_in1,
  output halt
);

  Clock #(.lowDuration(4)) clock_1 (.out(halt));
  Clock clock_2 (.out(p_in0));
  Clock #(.highDuration(2), .lowDuration(2)) clock_3 (.out(p_in1));
  main main_1 (.in0(p_in0), .in1(p_in1), .out0(p_out0));
endmodule
