// Logisim project random-016.circ as structural Verilog: 2 circuits, main circuit tty_harness
module main (
  input  in0,
  input  in1,
  input  in2,
  output out0
);

  wire n0, n1, n2, n3;

  nor nor_1 (n0, in1, ~in0, in0);  // NOR_Gate
  xnor even_parity_1 (out0, in1, n0);
  ExactlyOne xor_1 (.out(n1), .in0(in1), .in1(in2), .in2(n0), .in3(n0), .in4(in0));
  not not_1 (n2, in0);
  xor xor_2 (n3, n1, n0, in1, in1);
  Pull_Resistor #(.pull(1)) pull_resistor_1 (.node(n1));

  // Other names for the same wires on the sheet: n4 = out0
endmodule

module tty_harness (
  output p_in0,
  output p_in1,
  output p_out0,
  output p_in2,
  output halt
);

  Clock #(.lowDuration(8)) clock_1 (.out(halt));
  Clock clock_2 (.out(p_in0));
  Clock #(.highDuration(2), .lowDuration(2)) clock_3 (.out(p_in1));
  Clock #(.highDuration(4), .lowDuration(4)) clock_4 (.out(p_in2));
  main main_1 (.in0(p_in0), .in1(p_in1), .in2(p_in2), .out0(p_out0));
endmodule
