// Logisim project random-018.circ as structural Verilog: 2 circuits, main circuit tty_harness
module main (
  input  in0,
  input  in1,
  input  in2,
  output out0,
  output out1
);

  wire n0, n1, n2, n3, n4, n5, n6, n7;

  or or_1 (n0, ~in0, ~in1, in1, in0, in2);  // OR_Gate
  not not_1 (n4, n1);
  xnor xnor_1 (out1, n1, n6, in2, ~n1, ~n5);  // XNOR_Gate
  xnor even_parity_1 (n1, ~in2, in0, ~in0);  // Even_Parity
  or or_2 (n5, n2, ~in2);  // OR_Gate
  not not_2 (out0, n5);
  nand nand_1 (n2, ~n0, n1, in1);  // NAND_Gate
  assign n6 = n3 ? ~in2 : 1'bz;  // Controlled_Inverter controlled_inverter_1
  xor xor_1 (n3, n2, n2);
  xnor xnor_2 (n7, n0, in0, in0);

  // Other names for the same wires on the sheet: n8 = out1; n9 = out0
endmodule

module tty_harness (
  output p_in0,
  output p_out0,
  output p_in1,
  output p_out1,
  output p_in2,
  output halt
);

  Clock #(.lowDuration(8)) clock_1 (.out(halt));
  Clock clock_2 (.out(p_in0));
  Clock #(.highDuration(2), .lowDuration(2)) clock_3 (.out(p_in1));
  Clock #(.highDuration(4), .lowDuration(4)) clock_4 (.out(p_in2));
  main main_1 (.in0(p_in0), .in1(p_in1), .in2(p_in2), .out0(p_out0), .out1(p_out1));
endmodule
