// Logisim project random-019.circ as structural Verilog: 2 circuits, main circuit tty_harness
module main (
  input  in0,
  input  in1,
  output out0,
  output out1
);

  wire n0, n1, n2, n3, n4;

  xor odd_parity_1 (n0, in1, in0, in1, ~in0, in0);  // Odd_Parity
  not not_1 (n4, n1);
  NotExactlyOne xnor_1 (.out(n1), .in0(n0), .in1(n0), .in2(in1), .in3(in0), .in4(in0));
  xnor even_parity_1 (out1, ~n3, in1);  // Even_Parity
  xor odd_parity_2 (n2, in1, in0);
  and and_1 (out0, n2, ~n3);  // AND_Gate
  xor odd_parity_3 (n3, n0, in1);

  // Other names for the same wires on the sheet: n5 = out1; n6 = out0

  // Notes on the sheet:
  //   xnor_1 drives only 0 and floats otherwise
endmodule

module tty_harness (
  output p_in0,
  output p_out0,
  output p_in1,
  output p_out1,
  output halt
);

  Clock #(.lowDuration(4)) clock_1 (.out(halt));
  Clock clock_2 (.out(p_in0));
  Clock #(.highDuration(2), .lowDuration(2)) clock_3 (.out(p_in1));
  main main_1 (.in0(p_in0), .in1(p_in1), .out0(p_out0), .out1(p_out1));
endmodule
