// Logisim project random-021.circ as structural Verilog: 2 circuits, main circuit tty_harness
module main (
  input  in0,
  input  in1,
  input  in2,
  output out0,
  output out1
);

  wire n0, n1, n2, n3, n4, n5;

  nor nor_1 (n0, in0, in1, in1);
  nor nor_2 (n4, in1, n1, ~n2, ~in1, ~n3);  // NOR_Gate
  and and_1 (n1, in1, ~in0, in2, ~n0, n0);  // AND_Gate
  assign n5 = in2 ? ~n4 : 1'bz;  // Controlled_Inverter controlled_inverter_1
  xor xor_1 (n2, in1, n1);
  and and_2 (out1, in2, in2);
  xor odd_parity_1 (n3, in2, in0, ~in0);  // Odd_Parity
  xor odd_parity_2 (out0, n2, ~out1);  // Odd_Parity

  // Other names for the same wires on the sheet: n6 = out1; n7 = out0

  // Notes on the sheet:
  //   odd_parity_2 drives only 1 and floats otherwise
endmodule

module tty_harness (
  output p_in0,
  output p_out0,
  output p_in1,
  output p_out1,
  output p_in2,
  output halt
);

  Clock #(.lowDuration(8)) clock_1 (.out(halt));
  Clock clock_2 (.out(p_in0));
  Clock #(.highDuration(2), .lowDuration(2)) clock_3 (.out(p_in1));
  Clock #(.highDuration(4), .lowDuration(4)) clock_4 (.out(p_in2));
  main main_1 (.in0(p_in0), .in1(p_in1), .in2(p_in2), .out0(p_out0), .out1(p_out1));
endmodule
