// Logisim project random-022.circ as structural Verilog: 2 circuits, main circuit tty_harness
module main (
  input  in0,
  input  in1,
  input  in2,
  output out0
);

  wire n0, n1, n2, n3, n4;

  assign n0 = in2 ? in1 : 1'bz;  // Controlled_Buffer controlled_buffer_1
  or or_1 (n4, ~in0, in2, in2);  // OR_Gate
  NotExactlyOne xnor_1 (.out(n1), .in0(in2), .in1(n0), .in2(in2), .in3(n0));
  buf buffer_1 (out0, in0);
  not not_1 (n2, in2);
  not not_2 (n3, n0);

  // Other names for the same wires on the sheet: n5 = out0

  // Notes on the sheet:
  //   or_1 drives only 0 and floats otherwise
  //   xnor_1 drives only 0 and floats otherwise
endmodule

module tty_harness (
  output p_in0,
  output p_in1,
  output p_out0,
  output p_in2,
  output halt
);

  Clock #(.lowDuration(8)) clock_1 (.out(halt));
  Clock clock_2 (.out(p_in0));
  Clock #(.highDuration(2), .lowDuration(2)) clock_3 (.out(p_in1));
  Clock #(.highDuration(4), .lowDuration(4)) clock_4 (.out(p_in2));
  main main_1 (.in0(p_in0), .in1(p_in1), .in2(p_in2), .out0(p_out0));
endmodule
