// Logisim project random-024.circ as structural Verilog: 2 circuits, main circuit tty_harness
module main (
  input  in0,
  input  in1,
  output out0
);

  wire n0, n1, n2, n3, n4, n5, n6, n7, n8, n9, n10, n11;

  and and_1 (n0, in0, in0, in0, in1);
  xnor xnor_1 (n4, n2, n2, in0);
  nand nand_1 (n8, in1, n0, n4);
  xor xor_1 (out0, n10, n6, n8, n4);
  xnor even_parity_1 (n1, in0, in0, n0, n0, n0);
  NotExactlyOne xnor_2 (.out(n5), .in0(n0), .in1(n3), .in2(in0), .in3(n4), .in4(in1));
  assign n9 = n6 ? n2 : 1'bz;  // Controlled_Buffer controlled_buffer_1
  assign n2 = n1 ? n0 : 1'bz;  // Controlled_Buffer controlled_buffer_2
  nor nor_1 (n6, n1, n0);
  assign n10 = in0 ? ~n3 : 1'bz;  // Controlled_Inverter controlled_inverter_1
  nor nor_2 (n3, in1, n2);
  and and_2 (n7, ~n0, n3, n0, ~n4);  // AND_Gate
  buf buffer_1 (n11, n3);

  // Other names for the same wires on the sheet: n12 = out0

  // Notes on the sheet:
  //   xnor_1 drives only 1 and floats otherwise
  //   nand_1 drives only 1 and floats otherwise
  //   xnor_2 drives only 1 and floats otherwise
endmodule

module tty_harness (
  output p_in0,
  output p_out0,
  output p_in1,
  output halt
);

  Clock #(.lowDuration(4)) clock_1 (.out(halt));
  Clock clock_2 (.out(p_in0));
  Clock #(.highDuration(2), .lowDuration(2)) clock_3 (.out(p_in1));
  main main_1 (.in0(p_in0), .in1(p_in1), .out0(p_out0));
endmodule
