// Logisim project random-025.circ as structural Verilog: 2 circuits, main circuit tty_harness
module main (
  input  in0,
  input  in1,
  input  in2,
  output out0
);

  wire n0, n1, n2, n3, n4, n5, n6, n7, n8, n9, n10;

  NotExactlyOne xnor_1 (.out(n0), .in0(in0), .in1(in1), .in2(in0));
  xor odd_parity_1 (n4, ~in0, ~in1, n1, ~n1);  // Odd_Parity
  xnor xnor_2 (n8, n2, n0, n5);
  nand nand_1 (n1, n0, n0);
  and and_1 (n5, ~in1, n2, ~in1);  // AND_Gate
  buf buffer_1 (n9, n0);
  and and_2 (n2, ~n0, ~in0);  // AND_Gate
  nand nand_2 (n6, ~n0, n1, n2, ~in0, in0);  // NAND_Gate
  nand nand_3 (n10, ~n3, ~n6, in2, n0, in1);  // NAND_Gate
  nor nor_1 (n3, n1, n2, ~in1, n2, n0);  // NOR_Gate
  not not_1 (n7, n3);
  nand nand_4 (out0, n10, n5, n6);

  // Other names for the same wires on the sheet: n11 = out0
endmodule

module tty_harness (
  output p_in0,
  output p_in1,
  output p_out0,
  output p_in2,
  output halt
);

  Clock #(.lowDuration(8)) clock_1 (.out(halt));
  Clock clock_2 (.out(p_in0));
  Clock #(.highDuration(2), .lowDuration(2)) clock_3 (.out(p_in1));
  Clock #(.highDuration(4), .lowDuration(4)) clock_4 (.out(p_in2));
  main main_1 (.in0(p_in0), .in1(p_in1), .in2(p_in2), .out0(p_out0));
endmodule
