// Logisim project random-026.circ as structural Verilog: 2 circuits, main circuit tty_harness
module main (
  input  in0,
  input  in1,
  input  in2,
  output out0
);

  wire n0, n1, n2, n3, n4, n5, n6, n7, n8, n9;

  and and_1 (n0, in2, in2, in2, in0, ~in1);  // AND_Gate
  xor xor_1 (n4, n1, ~in1);  // XOR_Gate
  nand nand_1 (n8, ~in2, n1, n3, n1);  // NAND_Gate
  xnor xnor_1 (n1, in1, in2);
  xnor even_parity_1 (n5, n2, n2, n3);
  buf buffer_1 (n9, n2);
  NotExactlyOne xnor_2 (.out(n2), .in0(in2), .in1(in2), .in2(n0), .in3(n1), .in4(in0));
  xnor xnor_3 (n6, n5, ~n0, n3);  // XNOR_Gate
  or or_1 (out0, in2, n5, n2, ~in0, n4);  // OR_Gate
  xor odd_parity_1 (n3, ~n0, ~in0, n1, in0);  // Odd_Parity
  xnor even_parity_2 (n7, n5, n5, n3, in2, ~n3);  // Even_Parity

  // Other names for the same wires on the sheet: n10 = out0

  // Notes on the sheet:
  //   nand_1 drives only 1 and floats otherwise
  //   xnor_2 drives only 0 and floats otherwise
endmodule

module tty_harness (
  output p_in0,
  output p_in1,
  output p_out0,
  output p_in2,
  output halt
);

  Clock #(.lowDuration(8)) clock_1 (.out(halt));
  Clock clock_2 (.out(p_in0));
  Clock #(.highDuration(2), .lowDuration(2)) clock_3 (.out(p_in1));
  Clock #(.highDuration(4), .lowDuration(4)) clock_4 (.out(p_in2));
  main main_1 (.in0(p_in0), .in1(p_in1), .in2(p_in2), .out0(p_out0));
endmodule
