// Logisim project random-028.circ as structural Verilog: 2 circuits, main circuit tty_harness
module main (
  input  in0,
  input  in1,
  input  in2,
  output out0,
  output out1,
  output out2
);

  wire n0, n1, n2, n3, n4, n5, n6, n7;

  NotExactlyOne xnor_1 (.out(n0), .in0(in2), .in1(in0), .in2(in0));
  xnor xnor_2 (n4, in1, ~n0, in2, n2);  // XNOR_Gate
  nand nand_1 (out2, in2, n0, in2);
  xnor even_parity_1 (n1, ~in1, in1);  // Even_Parity
  nand nand_2 (n5, n4, ~n0, in0, ~n1);  // NAND_Gate
  nor nor_1 (out1, n0, n4, in0, n6);
  or or_1 (n2, in0, ~n1, n1, n1, n0);  // OR_Gate
  nand nand_3 (n6, n2, n2, ~in1);  // NAND_Gate
  xor xor_1 (out0, n0, ~n5);  // XOR_Gate
  buf buffer_1 (n3, in2);
  xnor even_parity_2 (n7, ~n4, ~n2);  // Even_Parity

  // Other names for the same wires on the sheet: n8 = out2; n9 = out1; n10 = out0

  // Notes on the sheet:
  //   xnor_1 drives only 1 and floats otherwise
endmodule

module tty_harness (
  output p_in0,
  output p_out0,
  output p_in1,
  output p_out1,
  output p_in2,
  output p_out2,
  output halt
);

  Clock #(.lowDuration(8)) clock_1 (.out(halt));
  Clock clock_2 (.out(p_in0));
  Clock #(.highDuration(2), .lowDuration(2)) clock_3 (.out(p_in1));
  Clock #(.highDuration(4), .lowDuration(4)) clock_4 (.out(p_in2));
  main main_1 (.in0(p_in0), .in1(p_in1), .in2(p_in2), .out0(p_out0), .out1(p_out1), .out2(p_out2));
endmodule
