// Logisim project random-032.circ as structural Verilog: 2 circuits, main circuit tty_harness
module main (
  input  in0,
  input  in1,
  input  in2,
  output out0,
  output out1
);

  wire n0, n1, n2, n3, n4, n5, n6, n7, n8;

  xor odd_parity_1 (n0, in0, in2, in1, ~in0);  // Odd_Parity
  xnor xnor_1 (n4, in1, n1, n1, n3);
  xnor even_parity_1 (n8, in2, ~n6);  // Even_Parity
  nand nand_1 (n1, in0, ~in1, in1, n0);  // NAND_Gate
  or or_1 (n5, n3, ~n1, in2);  // OR_Gate
  NotExactlyOne xnor_2 (.out(out1), .in0(in2), .in1(n3), .in2(n6), .in3(in1));
  xor odd_parity_2 (n2, n1, n0);
  buf buffer_1 (n6, n1);
  and and_1 (out0, ~n8, n6);  // AND_Gate
  not not_1 (n3, in1);
  assign n7 = n2 ? ~n4 : 1'bz;  // Controlled_Inverter controlled_inverter_1

  // Other names for the same wires on the sheet: n9 = out1; n10 = out0

  // Notes on the sheet:
  //   odd_parity_1 drives only 1 and floats otherwise
endmodule

module tty_harness (
  output p_in0,
  output p_out0,
  output p_in1,
  output p_out1,
  output p_in2,
  output halt
);

  Clock #(.lowDuration(8)) clock_1 (.out(halt));
  Clock clock_2 (.out(p_in0));
  Clock #(.highDuration(2), .lowDuration(2)) clock_3 (.out(p_in1));
  Clock #(.highDuration(4), .lowDuration(4)) clock_4 (.out(p_in2));
  main main_1 (.in0(p_in0), .in1(p_in1), .in2(p_in2), .out0(p_out0), .out1(p_out1));
endmodule
