// Logisim project random-033.circ as structural Verilog: 2 circuits, main circuit tty_harness
module main (
  input  in0,
  input  in1,
  input  in2,
  output out0,
  output out1
);

  wire n0, n1, n2, n3, n4, n5, n6, n7, n8;

  and and_1 (n0, in0, in2, in0);
  and and_2 (n4, n2, n2, n3);
  xor odd_parity_1 (n8, ~n7, ~n7);  // Odd_Parity
  xor odd_parity_2 (n1, in2, in2, ~in2, n0);  // Odd_Parity
  xor odd_parity_3 (n5, in0, n3, n3, ~n2, ~n2);  // Odd_Parity
  buf buffer_1 (out1, in1);
  nor nor_1 (n2, in2, in0, in2, in1);
  xnor even_parity_1 (n6, n0, ~n1, n4, in0, n0);  // Even_Parity
  xor odd_parity_4 (out0, out1, n1, n5);
  xor odd_parity_5 (n3, n2, in2);
  and and_3 (n7, n5, in2, n6, n3);

  // Other names for the same wires on the sheet: n9 = out1; n10 = out0

  // Notes on the sheet:
  //   odd_parity_2 drives only 0 and floats otherwise
  //   odd_parity_3 drives only 1 and floats otherwise
endmodule

module tty_harness (
  output p_in0,
  output p_out0,
  output p_in1,
  output p_out1,
  output p_in2,
  output halt
);

  Clock #(.lowDuration(8)) clock_1 (.out(halt));
  Clock clock_2 (.out(p_in0));
  Clock #(.highDuration(2), .lowDuration(2)) clock_3 (.out(p_in1));
  Clock #(.highDuration(4), .lowDuration(4)) clock_4 (.out(p_in2));
  main main_1 (.in0(p_in0), .in1(p_in1), .in2(p_in2), .out0(p_out0), .out1(p_out1));
endmodule
