// Logisim project random-034.circ as structural Verilog: 2 circuits, main circuit tty_harness
module main (
  input  in0,
  input  in1,
  input  in2,
  output out0,
  output out1,
  output out2
);

  wire n0, n1, n2, n3, n4, n5, n6, n7, n8;

  not not_1 (n0, in0);
  xor odd_parity_1 (n4, n1, in1, n2);
  not not_2 (n8, in2);
  nor nor_1 (n1, in2, n0, ~in1, ~in0, ~in0);  // NOR_Gate
  nand nand_1 (n5, ~in0, n3);  // NAND_Gate
  nor nor_2 (out2, n0, n5, n3, n6, n6);
  assign n2 = in0 ? n1 : 1'bz;  // Controlled_Buffer controlled_buffer_1
  and and_1 (n6, ~n5, n5);  // AND_Gate
  not not_3 (out1, n4);
  ExactlyOne xor_1 (.out(n3), .in0(n2), .in1(n0), .in2(in2));
  ExactlyOne xor_2 (.out(n7), .in0(n2), .in1(n0), .in2(n0), .in3(n0));
  not not_4 (out0, n7);

  // Other names for the same wires on the sheet: n9 = out2; n10 = out1; n11 = out0
endmodule

module tty_harness (
  output p_in0,
  output p_out0,
  output p_in1,
  output p_out1,
  output p_in2,
  output p_out2,
  output halt
);

  Clock #(.lowDuration(8)) clock_1 (.out(halt));
  Clock clock_2 (.out(p_in0));
  Clock #(.highDuration(2), .lowDuration(2)) clock_3 (.out(p_in1));
  Clock #(.highDuration(4), .lowDuration(4)) clock_4 (.out(p_in2));
  main main_1 (.in0(p_in0), .in1(p_in1), .in2(p_in2), .out0(p_out0), .out1(p_out1), .out2(p_out2));
endmodule
