// Logisim project random-035.circ as structural Verilog: 2 circuits, main circuit tty_harness
module main (
  input  in0,
  input  in1,
  output out0,
  output out1,
  output out2
);

  wire n0, n1, n2, n3, n4, n5;

  xnor even_parity_1 (n0, in1, in1, ~in1);  // Even_Parity
  or or_1 (n4, in0, ~n3, in1, ~in1);  // OR_Gate
  not not_1 (out0, in0);
  not not_2 (n1, in0);
  assign n5 = in1 ? ~n2 : 1'bz;  // Controlled_Inverter controlled_inverter_1
  or or_2 (n2, in0, n1, in0, ~in0, in0);  // OR_Gate
  buf buffer_1 (out2, in0);
  and and_1 (n3, in0, in1);
  xnor even_parity_2 (out1, in1, n3);

  // Other names for the same wires on the sheet: n6 = out2; n7 = out1; n8 = out0

  // Notes on the sheet:
  //   or_2 drives only 0 and floats otherwise
endmodule

module tty_harness (
  output p_in0,
  output p_out0,
  output p_in1,
  output p_out1,
  output p_out2,
  output halt
);

  Clock #(.lowDuration(4)) clock_1 (.out(halt));
  Clock clock_2 (.out(p_in0));
  Clock #(.highDuration(2), .lowDuration(2)) clock_3 (.out(p_in1));
  main main_1 (.in0(p_in0), .in1(p_in1), .out0(p_out0), .out1(p_out1), .out2(p_out2));
endmodule
