// Logisim project random-036.circ as structural Verilog: 2 circuits, main circuit tty_harness
module main (
  input  in0,
  input  in1,
  input  in2,
  input  in3,
  output out0,
  output out1,
  output out2
);

  wire n0, n1, n2, n3, n4, n5, n6, n7, n8, n9;

  or or_1 (n0, in0, in3, ~in0, in3, in3);  // OR_Gate
  xor odd_parity_1 (n4, in2, n0);
  xor odd_parity_2 (n8, in2, n2, n4, n4, in3);
  xor odd_parity_3 (out0, ~n0, in0, n4);  // Odd_Parity
  nand nand_1 (n1, ~in2, ~in0, in0, ~in3, ~in1);  // NAND_Gate
  xnor even_parity_1 (n5, n1, n0, n3);
  xor xor_1 (n9, n7, in2, n2, in0, n7);
  assign n2 = n1 ? in1 : 1'bz;  // Controlled_Buffer controlled_buffer_1
  xor odd_parity_4 (n6, ~in0, ~n2);  // Odd_Parity
  NotExactlyOne xnor_1 (.out(out2), .in0(n8), .in1(n1), .in2(in1), .in3(n6), .in4(n7));
  assign n3 = in1 ? n2 : 1'bz;  // Controlled_Buffer controlled_buffer_2
  xnor even_parity_2 (n7, n3, ~n0, n0, n0, in0);  // Even_Parity
  not not_1 (out1, n9);

  // Other names for the same wires on the sheet: n10 = out2; n11 = out1; n12 = out0

  // Notes on the sheet:
  //   odd_parity_3 drives only 0 and floats otherwise
  //   nand_1 drives only 0 and floats otherwise
endmodule

module tty_harness (
  output p_in0,
  output p_out0,
  output p_in1,
  output p_out1,
  output p_in2,
  output p_out2,
  output p_in3,
  output halt
);

  Clock #(.lowDuration(16)) clock_1 (.out(halt));
  Clock clock_2 (.out(p_in0));
  Clock #(.highDuration(2), .lowDuration(2)) clock_3 (.out(p_in1));
  Clock #(.highDuration(4), .lowDuration(4)) clock_4 (.out(p_in2));
  Clock #(.highDuration(8), .lowDuration(8)) clock_5 (.out(p_in3));
  main main_1 (.in0(p_in0), .in1(p_in1), .in2(p_in2), .in3(p_in3), .out0(p_out0), .out1(p_out1), .out2(p_out2));
endmodule
