// Logisim project random-038.circ as structural Verilog: 2 circuits, main circuit tty_harness
module main (
  input  in0,
  input  in1,
  input  in2,
  input  in3,
  output out0,
  output out1,
  output out2
);

  wire n0, n1, n2, n3, n4, n5, n6, n7, n8;

  not not_1 (n0, in3);
  ExactlyOne xor_1 (.out(n4), .in0(n0), .in1(in3), .in2(in3), .in3(n1));
  xor odd_parity_1 (n8, ~n2, in0, ~in0);  // Odd_Parity
  nor nor_1 (n1, in3, ~in2);  // NOR_Gate
  xnor even_parity_1 (n5, in2, in1, n3);
  buf buffer_1 (out2, n2);
  xnor even_parity_2 (n2, in2, in1);
  not not_2 (n6, in1);
  and and_1 (out1, ~n4, in3);  // AND_Gate
  xor xor_2 (n3, n2, n2, n1);
  xor xor_3 (n7, n5, n1, in0, n6);
  assign out0 = n8 ? ~n2 : 1'bz;  // Controlled_Inverter controlled_inverter_1
  Pull_Resistor #(.pull(1)) pull_resistor_1 (.node(n1));

  // Other names for the same wires on the sheet: n9 = out2; n10 = out1; n11 = out0

  // Notes on the sheet:
  //   and_1 drives only 0 and floats otherwise
  //   xor_3 drives only 0 and floats otherwise
endmodule

module tty_harness (
  output p_in0,
  output p_out0,
  output p_in1,
  output p_out1,
  output p_in2,
  output p_out2,
  output p_in3,
  output halt
);

  Clock #(.lowDuration(16)) clock_1 (.out(halt));
  Clock clock_2 (.out(p_in0));
  Clock #(.highDuration(2), .lowDuration(2)) clock_3 (.out(p_in1));
  Clock #(.highDuration(4), .lowDuration(4)) clock_4 (.out(p_in2));
  Clock #(.highDuration(8), .lowDuration(8)) clock_5 (.out(p_in3));
  main main_1 (.in0(p_in0), .in1(p_in1), .in2(p_in2), .in3(p_in3), .out0(p_out0), .out1(p_out1), .out2(p_out2));
endmodule
