// Logisim project random-039.circ as structural Verilog: 2 circuits, main circuit tty_harness
module main (
  input  in0,
  input  in1,
  output out0,
  output out1
);

  wire n0, n1, n2, n3, n4, n5, n6, n7, n8;

  and and_1 (n0, in1, in0, in0, in1, in1);
  xnor even_parity_1 (n4, in0, in0, n0);
  not not_1 (n8, n2);
  not not_2 (n1, n0);
  nor nor_1 (n5, n2, n1, in0, n2, n2);
  nand nand_1 (out1, n6, n0, n2);
  xnor even_parity_2 (n2, in1, ~in0, in1);  // Even_Parity
  nor nor_2 (n6, n3, n1, in1, n4, ~in0);  // NOR_Gate
  nand nand_2 (out0, ~n6, ~n5, ~n4, in1, ~n5);  // NAND_Gate
  not not_3 (n3, n0);
  assign n7 = n1 ? in0 : 1'bz;  // Controlled_Buffer controlled_buffer_1

  // Other names for the same wires on the sheet: n9 = out1; n10 = out0

  // Notes on the sheet:
  //   and_1 drives only 0 and floats otherwise
  //   even_parity_1 drives only 0 and floats otherwise
  //   nand_2 drives only 0 and floats otherwise
endmodule

module tty_harness (
  output p_in0,
  output p_out0,
  output p_in1,
  output p_out1,
  output halt
);

  Clock #(.lowDuration(4)) clock_1 (.out(halt));
  Clock clock_2 (.out(p_in0));
  Clock #(.highDuration(2), .lowDuration(2)) clock_3 (.out(p_in1));
  main main_1 (.in0(p_in0), .in1(p_in1), .out0(p_out0), .out1(p_out1));
endmodule
