// Logisim project random-040.circ as structural Verilog: 2 circuits, main circuit tty_harness
module main (
  input  in0,
  input  in1,
  input  in2,
  output out0
);

  wire n0, n1, n2, n3, n4, n5, n6, n7, n8, n9, n10;

  not not_1 (n0, in1);
  xor odd_parity_1 (n4, ~n0, in0, n0);  // Odd_Parity
  and and_1 (n8, n5, n1, in2, in1, n1);
  xnor xnor_1 (n1, ~in0, ~n0);  // XNOR_Gate
  assign n5 = in0 ? in0 : 1'bz;  // Controlled_Buffer controlled_buffer_1
  nor nor_1 (n9, ~in2, n2, n7, in0, in1);  // NOR_Gate
  nand nand_1 (n2, n0, in0, n1, in2, ~n0);  // NAND_Gate
  and and_2 (n6, n1, n2, n5);
  nor nor_2 (n10, in2, n9);
  xnor even_parity_1 (n3, in1, n2);
  xnor xnor_2 (n7, ~n1, ~n1, in2, in0, in0);  // XNOR_Gate
  and and_3 (out0, n6, n8, n1, ~in1);  // AND_Gate

  // Other names for the same wires on the sheet: n11 = out0

  // Notes on the sheet:
  //   odd_parity_1 drives only 0 and floats otherwise
  //   xnor_1 drives only 0 and floats otherwise
endmodule

module tty_harness (
  output p_in0,
  output p_in1,
  output p_out0,
  output p_in2,
  output halt
);

  Clock #(.lowDuration(8)) clock_1 (.out(halt));
  Clock clock_2 (.out(p_in0));
  Clock #(.highDuration(2), .lowDuration(2)) clock_3 (.out(p_in1));
  Clock #(.highDuration(4), .lowDuration(4)) clock_4 (.out(p_in2));
  main main_1 (.in0(p_in0), .in1(p_in1), .in2(p_in2), .out0(p_out0));
endmodule
