// Logisim project random-041.circ as structural Verilog: 2 circuits, main circuit tty_harness
module main (
  input  in0,
  input  in1,
  input  in2,
  input  in3,
  output out0
);

  wire n0, n1, n2, n3, n4, n5, n6, n7;

  xor xor_1 (n0, ~in3, in1, in0, in1, in2);  // XOR_Gate
  nand nand_1 (n4, ~n0, ~in1, ~in3, n3, ~n2);  // NAND_Gate
  xor xor_2 (out0, n3, n2);
  nand nand_2 (n1, in1, ~in0, n0);  // NAND_Gate
  xor odd_parity_1 (n5, n1, n4);
  buf buffer_1 (n2, in0);
  ExactlyOne xor_3 (.out(n6), .in0(in2), .in1(n5), .in2(in3));
  nor nor_1 (n3, in1, in1, n1);
  or or_1 (n7, n5, in0, n6);
  Pull_Resistor #(.pull("X")) pull_resistor_1 (.node(n2));

  // Other names for the same wires on the sheet: n8 = out0
endmodule

module tty_harness (
  output p_in0,
  output p_in1,
  output p_out0,
  output p_in2,
  output p_in3,
  output halt
);

  Clock #(.lowDuration(16)) clock_1 (.out(halt));
  Clock clock_2 (.out(p_in0));
  Clock #(.highDuration(2), .lowDuration(2)) clock_3 (.out(p_in1));
  Clock #(.highDuration(4), .lowDuration(4)) clock_4 (.out(p_in2));
  Clock #(.highDuration(8), .lowDuration(8)) clock_5 (.out(p_in3));
  main main_1 (.in0(p_in0), .in1(p_in1), .in2(p_in2), .in3(p_in3), .out0(p_out0));
endmodule
