// Logisim project random-042.circ as structural Verilog: 2 circuits, main circuit tty_harness
module main (
  input  in0,
  input  in1,
  input  in2,
  output out0
);

  wire n0, n1, n2, n3, n4, n5, n6;

  xnor xnor_1 (n0, in0, in2);
  nand nand_1 (n4, in1, ~in2, n2);  // NAND_Gate
  nand nand_2 (n1, in1, ~n0);  // NAND_Gate
  xor xor_1 (n5, n4, in0);
  not not_1 (n2, in0);
  nor nor_1 (n6, n3, n5, in2, n3, ~in1);  // NOR_Gate
  and and_1 (n3, ~n2, ~in2);  // AND_Gate
  xor odd_parity_1 (out0, n2, n0);

  // Other names for the same wires on the sheet: n7 = out0

  // Notes on the sheet:
  //   nand_1 drives only 1 and floats otherwise
  //   xor_1 drives only 1 and floats otherwise
  //   nor_1 drives only 0 and floats otherwise
endmodule

module tty_harness (
  output p_in0,
  output p_in1,
  output p_out0,
  output p_in2,
  output halt
);

  Clock #(.lowDuration(8)) clock_1 (.out(halt));
  Clock clock_2 (.out(p_in0));
  Clock #(.highDuration(2), .lowDuration(2)) clock_3 (.out(p_in1));
  Clock #(.highDuration(4), .lowDuration(4)) clock_4 (.out(p_in2));
  main main_1 (.in0(p_in0), .in1(p_in1), .in2(p_in2), .out0(p_out0));
endmodule
