// Logisim project random-043.circ as structural Verilog: 2 circuits, main circuit tty_harness
module main (
  input  in0,
  input  in1,
  input  in2,
  input  in3,
  output out0,
  output out1
);

  wire n0, n1, n2, n3;

  and and_1 (n0, in1, ~in3);  // AND_Gate
  assign out1 = n3 ? ~in0 : 1'bz;  // Controlled_Inverter controlled_inverter_1
  and and_2 (n1, in1, in0, n0);
  and and_3 (out0, ~out1, n1, in1, in0, n3);  // AND_Gate
  xnor xnor_1 (n2, in1, in0, n0);
  xor xor_1 (n3, in0, in2, in3, n1, n1);

  // Other names for the same wires on the sheet: n4 = out1; n5 = out0

  // Notes on the sheet:
  //   and_1 drives only 0 and floats otherwise
endmodule

module tty_harness (
  output p_in0,
  output p_in1,
  output p_out0,
  output p_in2,
  output p_out1,
  output p_in3,
  output halt
);

  Clock #(.lowDuration(16)) clock_1 (.out(halt));
  Clock clock_2 (.out(p_in0));
  Clock #(.highDuration(2), .lowDuration(2)) clock_3 (.out(p_in1));
  Clock #(.highDuration(4), .lowDuration(4)) clock_4 (.out(p_in2));
  Clock #(.highDuration(8), .lowDuration(8)) clock_5 (.out(p_in3));
  main main_1 (.in0(p_in0), .in1(p_in1), .in2(p_in2), .in3(p_in3), .out0(p_out0), .out1(p_out1));
endmodule
