// Logisim project random-044.circ as structural Verilog: 2 circuits, main circuit tty_harness
module main (
  input  in0,
  input  in1,
  input  in2,
  input  in3,
  output out0,
  output out1
);

  wire n0, n1, n2;

  not not_1 (n0, in2);
  not not_2 (out0, in3);
  xor xor_1 (n1, ~n0, in0, in2);  // XOR_Gate
  ExactlyOne xor_2 (.out(n2), .in0(n1), .in1(in2), .in2(in3), .in3(in1));
  assign out1 = in2 ? in2 : 1'bz;  // Controlled_Buffer controlled_buffer_1

  // Other names for the same wires on the sheet: n3 = out1; n4 = out0
endmodule

module tty_harness (
  output p_in0,
  output p_in1,
  output p_out0,
  output p_in2,
  output p_out1,
  output p_in3,
  output halt
);

  Clock #(.lowDuration(16)) clock_1 (.out(halt));
  Clock clock_2 (.out(p_in0));
  Clock #(.highDuration(2), .lowDuration(2)) clock_3 (.out(p_in1));
  Clock #(.highDuration(4), .lowDuration(4)) clock_4 (.out(p_in2));
  Clock #(.highDuration(8), .lowDuration(8)) clock_5 (.out(p_in3));
  main main_1 (.in0(p_in0), .in1(p_in1), .in2(p_in2), .in3(p_in3), .out0(p_out0), .out1(p_out1));
endmodule
