// Logisim project random-045.circ as structural Verilog: 2 circuits, main circuit tty_harness
module main (
  input  in0,
  input  in1,
  output out0
);

  wire n0, n1, n2, n3, n4, n5, n6, n7, n8, n9, n10, n11;

  nand nand_1 (n0, in1, in0, in0);
  and and_1 (n4, n1, in1);
  xor odd_parity_1 (n8, n1, n0, n7);
  nand nand_2 (out0, ~n10, n5, n0, n2, ~n3);  // NAND_Gate
  xnor even_parity_1 (n1, n0, in1, in0, n0);
  assign n5 = n1 ? ~n3 : 1'bz;  // Controlled_Inverter controlled_inverter_1
  nor nor_1 (n9, n3, n0);
  not not_1 (n2, in0);
  and and_2 (n6, n2, n2, ~in0, n3, in1);  // AND_Gate
  nor nor_2 (n10, ~n1, ~n3, n7, n0, in0);  // NOR_Gate
  buf buffer_1 (n3, n2);
  not not_2 (n7, n2);
  nor nor_3 (n11, n9, n7);

  // Other names for the same wires on the sheet: n12 = out0

  // Notes on the sheet:
  //   nand_1 drives only 1 and floats otherwise
  //   and_1 drives only 1 and floats otherwise
  //   and_2 drives only 0 and floats otherwise
  //   nor_3 drives only 0 and floats otherwise
endmodule

module tty_harness (
  output p_in0,
  output p_out0,
  output p_in1,
  output halt
);

  Clock #(.lowDuration(4)) clock_1 (.out(halt));
  Clock clock_2 (.out(p_in0));
  Clock #(.highDuration(2), .lowDuration(2)) clock_3 (.out(p_in1));
  main main_1 (.in0(p_in0), .in1(p_in1), .out0(p_out0));
endmodule
