// Logisim project random-046.circ as structural Verilog: 2 circuits, main circuit tty_harness
module main (
  input  in0,
  input  in1,
  output out0,
  output out1
);

  wire n0, n1, n2, n3, n4, n5, n6, n7, n8, n9, n10;

  xor odd_parity_1 (n0, ~in1, in0);  // Odd_Parity
  or or_1 (n4, n0, n3, in0, n1);
  not not_1 (n8, n2);
  xor odd_parity_2 (out0, n0, n2);
  assign n1 = in0 ? ~n0 : 1'bz;  // Controlled_Inverter controlled_inverter_1
  xor xor_1 (n5, ~n1, n0, n4, ~n0, ~n1);  // XOR_Gate
  and and_1 (n9, n0, in1, n4, n4, n5);
  xnor even_parity_1 (n2, in1, in1, n0);
  nand nand_1 (n6, n1, n4, n3, n1, n5);
  xnor xnor_1 (n10, ~n2, n6, n3, in1);  // XNOR_Gate
  or or_2 (n3, ~n0, in1, n2);  // OR_Gate
  xnor even_parity_2 (n7, ~n5, ~n6);  // Even_Parity
  nor nor_1 (out1, in0, n1, ~n6, n3, n8);  // NOR_Gate

  // Other names for the same wires on the sheet: n11 = out1; n12 = out0

  // Notes on the sheet:
  //   xnor_1 drives only 0 and floats otherwise
  //   even_parity_2 drives only 0 and floats otherwise
endmodule

module tty_harness (
  output p_in0,
  output p_out0,
  output p_in1,
  output p_out1,
  output halt
);

  Clock #(.lowDuration(4)) clock_1 (.out(halt));
  Clock clock_2 (.out(p_in0));
  Clock #(.highDuration(2), .lowDuration(2)) clock_3 (.out(p_in1));
  main main_1 (.in0(p_in0), .in1(p_in1), .out0(p_out0), .out1(p_out1));
endmodule
