// Logisim project random-047.circ as structural Verilog: 2 circuits, main circuit tty_harness
module main (
  input  in0,
  input  in1,
  input  in2,
  output out0
);

  wire n0, n1, n2;

  xor xor_1 (n0, ~in1, in0, ~in1, ~in1);  // XOR_Gate
  nand nand_1 (n1, ~in2, in2, in0, n0);  // NAND_Gate
  or or_1 (n2, in1, in1);
  NotExactlyOne xnor_1 (.out(out0), .in0(in1), .in1(n2), .in2(in0), .in3(n0));

  // Other names for the same wires on the sheet: n3 = out0

  // Notes on the sheet:
  //   or_1 drives only 0 and floats otherwise
endmodule

module tty_harness (
  output p_in0,
  output p_in1,
  output p_out0,
  output p_in2,
  output halt
);

  Clock #(.lowDuration(8)) clock_1 (.out(halt));
  Clock clock_2 (.out(p_in0));
  Clock #(.highDuration(2), .lowDuration(2)) clock_3 (.out(p_in1));
  Clock #(.highDuration(4), .lowDuration(4)) clock_4 (.out(p_in2));
  main main_1 (.in0(p_in0), .in1(p_in1), .in2(p_in2), .out0(p_out0));
endmodule
