// Logisim project random-048.circ as structural Verilog: 2 circuits, main circuit tty_harness
module main (
  input  in0,
  input  in1,
  input  in2,
  input  in3,
  output out0,
  output out1,
  output out2
);

  wire n0, n1, n2, n3, n4, n5;

  and and_1 (n0, in0, in2, in2);
  buf buffer_1 (n4, in0);
  nand nand_1 (out0, out2, in2, n2);
  and and_2 (n1, ~n0, in0, ~in3, ~in0, in1);  // AND_Gate
  and and_3 (n5, n0, n1);
  NotExactlyOne xnor_1 (.out(n2), .in0(in3), .in1(in0), .in2(in2), .in3(in3));
  NotExactlyOne xnor_2 (.out(out2), .in0(n2), .in1(n2), .in2(n5));
  xor xor_1 (n3, in3, ~in0, in1);  // XOR_Gate
  or or_1 (out1, n3, ~in3, ~n5, ~n0, n3);  // OR_Gate
  Pull_Resistor #(.pull(1)) pull_resistor_1 (.node(n5));

  // Other names for the same wires on the sheet: n6 = out2; n7 = out1; n8 = out0

  // Notes on the sheet:
  //   and_1 drives only 0 and floats otherwise
  //   and_3 drives only 0 and floats otherwise
  //   xnor_2 drives only 0 and floats otherwise
endmodule

module tty_harness (
  output p_in0,
  output p_out0,
  output p_in1,
  output p_out1,
  output p_in2,
  output p_out2,
  output p_in3,
  output halt
);

  Clock #(.lowDuration(16)) clock_1 (.out(halt));
  Clock clock_2 (.out(p_in0));
  Clock #(.highDuration(2), .lowDuration(2)) clock_3 (.out(p_in1));
  Clock #(.highDuration(4), .lowDuration(4)) clock_4 (.out(p_in2));
  Clock #(.highDuration(8), .lowDuration(8)) clock_5 (.out(p_in3));
  main main_1 (.in0(p_in0), .in1(p_in1), .in2(p_in2), .in3(p_in3), .out0(p_out0), .out1(p_out1), .out2(p_out2));
endmodule
