// Logisim project random-049.circ as structural Verilog: 2 circuits, main circuit tty_harness
module main (
  input  in0,
  input  in1,
  input  in2,
  output out0,
  output out1,
  output out2
);

  wire n0, n1, n2, n3, n4, n5, n6;

  and and_1 (n0, in1, ~in1, ~in0, in1);  // AND_Gate
  or or_1 (n4, ~in2, n2, in0, in2, in1);  // OR_Gate
  or or_2 (out1, n2, n6, n0, n0, n0);
  nor nor_1 (n1, in1, in2, n0);
  buf buffer_1 (n5, n0);
  nand nand_1 (out0, ~n1, n6, n5);  // NAND_Gate
  nand nand_2 (n2, n0, in1, ~in1);  // NAND_Gate
  assign n6 = n4 ? ~n1 : 1'bz;  // Controlled_Inverter controlled_inverter_1
  and and_2 (n3, ~n1, ~n1, n2, in2, ~n2);  // AND_Gate
  xnor xnor_1 (out2, ~n5, n3, ~n6, n6);  // XNOR_Gate

  // Other names for the same wires on the sheet: n7 = out2; n8 = out1; n9 = out0
endmodule

module tty_harness (
  output p_in0,
  output p_out0,
  output p_in1,
  output p_out1,
  output p_in2,
  output p_out2,
  output halt
);

  Clock #(.lowDuration(8)) clock_1 (.out(halt));
  Clock clock_2 (.out(p_in0));
  Clock #(.highDuration(2), .lowDuration(2)) clock_3 (.out(p_in1));
  Clock #(.highDuration(4), .lowDuration(4)) clock_4 (.out(p_in2));
  main main_1 (.in0(p_in0), .in1(p_in1), .in2(p_in2), .out0(p_out0), .out1(p_out1), .out2(p_out2));
endmodule
