// Logisim project random-050.circ as structural Verilog: 2 circuits, main circuit tty_harness
module main (
  input  in0,
  input  in1,
  input  in2,
  output out0
);

  wire n0, n1, n2, n3;

  and and_1 (n0, in0, ~in0);  // AND_Gate
  or or_1 (out0, n1, n3, ~in1);  // OR_Gate
  assign n1 = n0 ? ~in0 : 1'bz;  // Controlled_Inverter controlled_inverter_1
  and and_2 (n2, in2, n0, in0, in2);
  nand nand_1 (n3, n1, n2, ~n1, in0, n0);  // NAND_Gate
  Pull_Resistor pull_resistor_1 (.node(n2));

  // Other names for the same wires on the sheet: n4 = out0

  // Notes on the sheet:
  //   and_1 drives only 0 and floats otherwise
  //   or_1 drives only 1 and floats otherwise
  //   nand_1 drives only 0 and floats otherwise
endmodule

module tty_harness (
  output p_in0,
  output p_in1,
  output p_out0,
  output p_in2,
  output halt
);

  Clock #(.lowDuration(8)) clock_1 (.out(halt));
  Clock clock_2 (.out(p_in0));
  Clock #(.highDuration(2), .lowDuration(2)) clock_3 (.out(p_in1));
  Clock #(.highDuration(4), .lowDuration(4)) clock_4 (.out(p_in2));
  main main_1 (.in0(p_in0), .in1(p_in1), .in2(p_in2), .out0(p_out0));
endmodule
