// Logisim project random-052.circ as structural Verilog: 2 circuits, main circuit tty_harness
module main (
  input  in0,
  input  in1,
  output out0,
  output out1,
  output out2
);

  wire n0;

  xor odd_parity_1 (n0, in1, in0, in0, in1);
  not not_1 (out2, in0);
  xnor even_parity_1 (out1, n0, in1, n0, in1);
  xnor even_parity_2 (out0, in0, in1);
  Pull_Resistor #(.pull(1)) pull_resistor_1 (.node(out2));

  // Other names for the same wires on the sheet: n1 = out2; n2 = out1; n3 = out0

  // Notes on the sheet:
  //   odd_parity_1 drives only 0 and floats otherwise
  //   even_parity_1 drives only 1 and floats otherwise
endmodule

module tty_harness (
  output p_in0,
  output p_out0,
  output p_in1,
  output p_out1,
  output p_out2,
  output halt
);

  Clock #(.lowDuration(4)) clock_1 (.out(halt));
  Clock clock_2 (.out(p_in0));
  Clock #(.highDuration(2), .lowDuration(2)) clock_3 (.out(p_in1));
  main main_1 (.in0(p_in0), .in1(p_in1), .out0(p_out0), .out1(p_out1), .out2(p_out2));
endmodule
