// Logisim project random-053.circ as structural Verilog: 2 circuits, main circuit tty_harness
module main (
  input  in0,
  input  in1,
  output out0,
  output out1
);

  wire n0, n1, n2, n3, n4, n5, n6, n7, n8, n9;

  not not_1 (n0, in0);
  xnor even_parity_1 (n4, n1, in0, n3, n0, ~n3);  // Even_Parity
  assign n8 = n2 ? n5 : 1'bz;  // Controlled_Buffer controlled_buffer_1
  and and_1 (n1, in1, in0, n0, in0, in1);
  assign n5 = n2 ? n1 : 1'bz;  // Controlled_Buffer controlled_buffer_2
  nand nand_1 (n9, ~in1, n5, n3, n6);  // NAND_Gate
  xnor even_parity_2 (n2, in0, in0, ~n1, ~in1, n1);  // Even_Parity
  buf buffer_1 (n6, n0);
  not not_2 (out1, in1);
  and and_2 (n3, ~n2, ~n0, n2, n1, ~in0);  // AND_Gate
  assign n7 = n4 ? in0 : 1'bz;  // Controlled_Buffer controlled_buffer_3
  nor nor_1 (out0, ~in0, in1, out1);  // NOR_Gate

  // Other names for the same wires on the sheet: n10 = out1; n11 = out0
endmodule

module tty_harness (
  output p_in0,
  output p_out0,
  output p_in1,
  output p_out1,
  output halt
);

  Clock #(.lowDuration(4)) clock_1 (.out(halt));
  Clock clock_2 (.out(p_in0));
  Clock #(.highDuration(2), .lowDuration(2)) clock_3 (.out(p_in1));
  main main_1 (.in0(p_in0), .in1(p_in1), .out0(p_out0), .out1(p_out1));
endmodule
