// Logisim project random-054.circ as structural Verilog: 2 circuits, main circuit tty_harness
module main (
  input  in0,
  input  in1,
  output out0,
  output out1,
  output out2
);

  wire n0, n1, n2, n3, n4, n5, n6;

  nor nor_1 (n0, in0, in1, in1);
  not not_1 (n4, n2);
  nor nor_2 (out1, out2, n3, n2);
  or or_1 (n1, in0, n0, in0, in0, in1);
  xnor xnor_1 (n5, ~n2, n2);  // XNOR_Gate
  not not_2 (out0, in0);
  xor odd_parity_1 (n2, ~n1, in0, in0);  // Odd_Parity
  not not_3 (n6, n2);
  xnor even_parity_1 (n3, ~in0, ~n1, ~in1);  // Even_Parity
  and and_1 (out2, n0, ~n0, in1, ~n5, n4);  // AND_Gate

  // Other names for the same wires on the sheet: n7 = out2; n8 = out1; n9 = out0

  // Notes on the sheet:
  //   nor_2 drives only 1 and floats otherwise
endmodule

module tty_harness (
  output p_in0,
  output p_out0,
  output p_in1,
  output p_out1,
  output p_out2,
  output halt
);

  Clock #(.lowDuration(4)) clock_1 (.out(halt));
  Clock clock_2 (.out(p_in0));
  Clock #(.highDuration(2), .lowDuration(2)) clock_3 (.out(p_in1));
  main main_1 (.in0(p_in0), .in1(p_in1), .out0(p_out0), .out1(p_out1), .out2(p_out2));
endmodule
