// Logisim project random-055.circ as structural Verilog: 2 circuits, main circuit tty_harness
module main (
  input  in0,
  input  in1,
  input  in2,
  output out0,
  output out1,
  output out2
);

  wire n0, n1, n2, n3, n4, n5, n6, n7, n8;

  xnor xnor_1 (n0, in1, ~in1);  // XNOR_Gate
  nand nand_1 (n4, n3, ~n0, in2, in0, in0);  // NAND_Gate
  NotExactlyOne xnor_2 (.out(n8), .in0(n5), .in1(n4), .in2(in0), .in3(in0));
  and and_1 (n1, ~n0, ~in0, ~n0, in1);  // AND_Gate
  NotExactlyOne xnor_3 (.out(n5), .in0(in1), .in1(n3), .in2(n2));
  nand nand_2 (out2, ~n4, ~n7, ~in0, ~in1, ~n8);  // NAND_Gate
  or or_1 (n2, in0, in1);
  and and_2 (n6, in2, ~n0, ~n0);  // AND_Gate
  nor nor_1 (out1, n0, n5);
  xnor xnor_4 (n3, n0, n2);
  xnor even_parity_1 (n7, ~in0, n0);  // Even_Parity
  buf buffer_1 (out0, n5);

  // Other names for the same wires on the sheet: n9 = out2; n10 = out1; n11 = out0

  // Notes on the sheet:
  //   or_1 drives only 1 and floats otherwise
endmodule

module tty_harness (
  output p_in0,
  output p_out0,
  output p_in1,
  output p_out1,
  output p_in2,
  output p_out2,
  output halt
);

  Clock #(.lowDuration(8)) clock_1 (.out(halt));
  Clock clock_2 (.out(p_in0));
  Clock #(.highDuration(2), .lowDuration(2)) clock_3 (.out(p_in1));
  Clock #(.highDuration(4), .lowDuration(4)) clock_4 (.out(p_in2));
  main main_1 (.in0(p_in0), .in1(p_in1), .in2(p_in2), .out0(p_out0), .out1(p_out1), .out2(p_out2));
endmodule
