// Logisim project random-056.circ as structural Verilog: 2 circuits, main circuit tty_harness
module main (
  input  in0,
  input  in1,
  output out0,
  output out1
);

  wire n0, n1, n2, n3, n4, n5;

  nand nand_1 (n0, in0, in0, in1);
  not not_1 (n4, in0);
  assign n1 = n0 ? in0 : 1'bz;  // Controlled_Buffer controlled_buffer_1
  xnor even_parity_1 (n5, ~n4, in1);  // Even_Parity
  or or_1 (n2, in1, in1);
  xor odd_parity_1 (out1, n0, in0, n3);
  xnor xnor_1 (n3, n2, n1);
  xnor even_parity_2 (out0, in0, n1, in1, out1);

  // Other names for the same wires on the sheet: n6 = out1; n7 = out0

  // Notes on the sheet:
  //   odd_parity_1 drives only 1 and floats otherwise
  //   xnor_1 drives only 1 and floats otherwise
endmodule

module tty_harness (
  output p_in0,
  output p_out0,
  output p_in1,
  output p_out1,
  output halt
);

  Clock #(.lowDuration(4)) clock_1 (.out(halt));
  Clock clock_2 (.out(p_in0));
  Clock #(.highDuration(2), .lowDuration(2)) clock_3 (.out(p_in1));
  main main_1 (.in0(p_in0), .in1(p_in1), .out0(p_out0), .out1(p_out1));
endmodule
