// Logisim project random-058.circ as structural Verilog: 2 circuits, main circuit tty_harness
module main (
  input  in0,
  input  in1,
  input  in2,
  output out0
);

  wire n0, n1, n2, n3, n4, n5, n6, n7, n8;

  and and_1 (n0, in0, in0, in1, in0, in0);
  nor nor_1 (n4, in1, n3, n0);
  xor xor_1 (n8, in2, in1, in1, n4, n6);
  or or_1 (n1, in1, n0, ~in1, ~in2);  // OR_Gate
  xnor even_parity_1 (n5, n0, ~n2, in2, n2, in2);  // Even_Parity
  nand nand_1 (out0, n4, ~n2);  // NAND_Gate
  xnor even_parity_2 (n2, in0, ~in1, ~in1, n0, n0);  // Even_Parity
  buf buffer_1 (n6, n5);
  xor odd_parity_1 (n3, in1, in1, in2, ~n2, in2);  // Odd_Parity
  nor nor_2 (n7, ~n3, n6, n4);  // NOR_Gate

  // Other names for the same wires on the sheet: n9 = out0
endmodule

module tty_harness (
  output p_in0,
  output p_in1,
  output p_out0,
  output p_in2,
  output halt
);

  Clock #(.lowDuration(8)) clock_1 (.out(halt));
  Clock clock_2 (.out(p_in0));
  Clock #(.highDuration(2), .lowDuration(2)) clock_3 (.out(p_in1));
  Clock #(.highDuration(4), .lowDuration(4)) clock_4 (.out(p_in2));
  main main_1 (.in0(p_in0), .in1(p_in1), .in2(p_in2), .out0(p_out0));
endmodule
