// Logisim project random-060.circ as structural Verilog: 2 circuits, main circuit tty_harness
module main (
  input  in0,
  input  in1,
  output out0
);

  wire n0, n1, n2, n3;

  xor xor_1 (n0, in0, in0, ~in1, in1);  // XOR_Gate
  xnor even_parity_1 (out0, n1, ~n0, ~n0, in0, in0);  // Even_Parity
  xnor xnor_1 (n1, n0, in0, in1);
  assign n2 = in1 ? ~n1 : 1'bz;  // Controlled_Inverter controlled_inverter_1
  buf buffer_1 (n3, n2);

  // Other names for the same wires on the sheet: n4 = out0
endmodule

module tty_harness (
  output p_in0,
  output p_out0,
  output p_in1,
  output halt
);

  Clock #(.lowDuration(4)) clock_1 (.out(halt));
  Clock clock_2 (.out(p_in0));
  Clock #(.highDuration(2), .lowDuration(2)) clock_3 (.out(p_in1));
  main main_1 (.in0(p_in0), .in1(p_in1), .out0(p_out0));
endmodule
