// Logisim project base.circ as structural Verilog: 1 circuit, main circuit bloque
module bloque (
  input  in0,
  input  in1,
  output out0,
  output out1,
  output out2
);

  wire n0;

  NotExactlyOne xnor_1 (.out(n0), .in0(in1), .in1(in1), .in2(in0), .in3(in0));
  ExactlyOne xor_1 (.out(out2), .in0(in0), .in1(in1), .in2(n0));
  not not_1 (out1, n0);
  xnor xnor_2 (out0, ~in0, ~out2, in1, n0, ~n0);  // XNOR_Gate

  // Other names for the same wires on the sheet: n1 = out2; n2 = out1; n3 = out0
endmodule
