// Logisim project compuertas.circ as structural Verilog: 1 circuit, main circuit doble
module doble (
  input  x_in0,
  input  x_in1,
  output y_out0,
  output y_out1,
  output y_out2
);

  wire m_out0, m_out1, m_out2;

  bloque bloque_1 (.in0(x_in0), .in1(x_in1), .out0(m_out0), .out1(m_out1), .out2(m_out2));
  bloque bloque_2 (.in0(m_out0), .in1(m_out1), .out0(y_out0), .out1(y_out1), .out2(y_out2));
endmodule
