// Logisim project principal.circ as structural Verilog: 2 circuits, main circuit tty_harness
module main (
  input  in_in0,
  input  in_in1,
  output d_y_out0,
  output d_y_out1,
  output d_y_out2,
  output b_out0,
  output b_out1,
  output b_out2
);

  doble doble_1 (.x_in0(in_in0), .x_in1(in_in1), .y_out0(d_y_out0), .y_out1(d_y_out1), .y_out2(d_y_out2));
  bloque bloque_1 (.in0(in_in0), .in1(in_in1), .out0(b_out0), .out1(b_out1), .out2(b_out2));
endmodule

module tty_harness (
  output p_d_y_out0,
  output p_d_y_out1,
  output p_in_in0,
  output p_d_y_out2,
  output p_in_in1,
  output p_b_out0,
  output p_b_out1,
  output p_b_out2,
  output halt
);

  Clock #(.lowDuration(4)) clock_1 (.out(halt));
  Clock clock_2 (.out(p_in_in0));
  Clock #(.highDuration(2), .lowDuration(2)) clock_3 (.out(p_in_in1));
  main main_1 (
    .in_in0(p_in_in0), .in_in1(p_in_in1), .d_y_out0(p_d_y_out0), .d_y_out1(p_d_y_out1),
    .d_y_out2(p_d_y_out2), .b_out0(p_b_out0), .b_out1(p_b_out1), .b_out2(p_b_out2));
endmodule
